// Logisim project CPU.circ as structural Verilog: 23 circuits, main circuit ◇重定向流水线
module \单周期MIPS_with_Interupt  (
);

  wire and_1_out, and_2_out, and_3_out, and_4_out, and_8_out, and_9_out, and_10_out, and_12_out, and_13_out,
       and_14_out, and_15_out, and_16_out, and_17_out, and_18_out, Beq, BGTZ, Bne, CLK, comparator_1_gt,
       comparator_2_gt, comparator_3_eq, d_ff_1_q, d_ff_2_q, d_ff_3_q, d_ff_4_q, d_ff_5_q, d_ff_6_q,
       demultiplexer_1_out0, demultiplexer_1_out1, demultiplexer_1_out2, Equ, eret, Go, IE, IR1, IR2, IR3,
       JAL, JMP, JR, nohalt, not_1_out, not_2_out, or_4_out, or_5_out, or_6_out, or_7_out, or_8_out,
       or_11_out, or_12_out, priority_encoder_1_gs, RST, SH, SignedExt, SRLV, syscall, W1, W2, W3, \中断请求 ,
       \同步清零1 , \同步清零2 , \同步清零3 , \硬布线控制器_1_alu_src , \硬布线控制器_1_memtoreg , \硬布线控制器_1_memwrite ,
       \硬布线控制器_1_regdst , \硬布线控制器_1_regwrite ;
  wire [1:0] IR, \中断编号 ;
  wire [2:0] or_9_out;
  wire [3:0] multiplexer_12_out, multiplexer_13_out, \硬布线控制器_1_alu_op ;
  wire [4:0] multiplexer_4_out, multiplexer_5_out, multiplexer_6_out, multiplexer_7_out, multiplexer_10_out;
  wire [15:0] \总周期数 , \无条件分支数 , \条件分支成功数 ;
  wire [31:0] adder_2_out, EPC, IntVec, LedData, mips_alu_1_result, mips_ram_1_p9, multiplexer_2_out,
       multiplexer_8_out, multiplexer_9_out, multiplexer_14_out, multiplexer_15_out, multiplexer_16_out,
       PC_q, PCin, PCinCom, PCout, R1, R2, rom_1_data, shifter_1_out, shifter_2_out, shifter_3_out;

  Button \u_总复位  (.out(RST));
  Button _1 (.out(IR1));
  Button _2 (.out(IR2));
  Button _3 (.out(IR3));
  Button \u_继续运行  (.out(Go));
  LED led_1 (.in(W1));
  LED led_2 (.in(W2));
  LED led_3 (.in(W3));
  Register #(.width(32)) PC (.D(PCin), .en(nohalt), .Q(PC_q), .clk(CLK), .clr(RST));
  or or_1 (W1, d_ff_4_q, d_ff_2_q);
  or or_2 (W2, d_ff_5_q, d_ff_3_q);
  D_Flip_Flop d_ff_1 (.clk(IR3), .D(1'b1), .Q(d_ff_1_q), .reset(d_ff_6_q));  // open: Qn, preset, en
  or or_3 (W3, d_ff_6_q, d_ff_1_q);
  Hex_Digit_Display hex_digit_display_1 (.value(LedData[31:28]));  // open: dp
  Adder #(.width(32)) adder_1 (.a(PC_q), .b(32'h4), .out(PCout));  // open: cin, cout
  D_Flip_Flop d_ff_2 (.clk(IR1), .D(1'b1), .Q(d_ff_2_q), .reset(d_ff_4_q));  // open: Qn, preset, en
  or or_4 (or_4_out, d_ff_2_q, d_ff_4_q);
  D_Flip_Flop d_ff_3 (.clk(IR2), .D(1'b1), .Q(d_ff_3_q), .reset(d_ff_5_q));  // open: Qn, preset, en
  or or_5 (or_5_out, d_ff_3_q, d_ff_5_q);
  or or_6 (or_6_out, d_ff_1_q, d_ff_6_q);
  Multiplexer #(.select(2), .width(32), .enable("false")) multiplexer_1 (
    .in0(32'h10), .in1(32'hc0), .in2(32'h170), .in3(32'h220), .out(IntVec), .sel(\中断编号 ));
  Multiplexer #(.width(32), .enable("false")) multiplexer_2 (
    .in0(PCinCom), .in1(IntVec), .out(multiplexer_2_out), .sel(\中断请求 ));
  Multiplexer #(.width(32), .enable("false")) multiplexer_3 (
    .in0(multiplexer_2_out), .in1(EPC), .out(PCin), .sel(eret));
  Hex_Digit_Display hex_digit_display_2 (.value(LedData[23:20]));  // open: dp
  Hex_Digit_Display hex_digit_display_3 (.value(LedData[27:24]));  // open: dp
  ROM #(.addrWidth(10), .dataWidth(32)) rom_1 (.addr(PC_q[11:2]), .data(rom_1_data), .sel(1'b1));
  and and_1 (and_1_out, or_4_out, ~\同步清零1 );  // AND_Gate
  and and_2 (and_2_out, or_5_out, ~\同步清零2 );  // AND_Gate
  and and_3 (and_3_out, or_6_out, ~\同步清零3 );  // AND_Gate
  Hex_Digit_Display hex_digit_display_4 (.value(LedData[19:16]));  // open: dp
  Hex_Digit_Display hex_digit_display_5 (.value(LedData[15:12]));  // open: dp
  D_Flip_Flop d_ff_4 (.clk(CLK), .D(and_1_out), .Q(d_ff_4_q));  // open: Qn, preset, en, reset
  D_Flip_Flop d_ff_5 (.clk(CLK), .D(and_2_out), .Q(d_ff_5_q));  // open: Qn, preset, en, reset
  D_Flip_Flop d_ff_6 (.clk(CLK), .D(and_3_out), .Q(d_ff_6_q));  // open: Qn, preset, en, reset
  or or_7 (or_7_out, \中断请求 , eret);
  Hex_Digit_Display hex_digit_display_6 (.value(LedData[11:8]));  // open: dp
  Hex_Digit_Display hex_digit_display_7 (.value(LedData[7:4]));  // open: dp
  Clock clock_1 (.out(CLK));
  \硬布线控制器  \u_硬布线控制器_1  (
    .Func(rom_1_data[5:0]), .OP(rom_1_data[31:26]), .ALU_OP(\硬布线控制器_1_alu_op ),
    .MemToReg(\硬布线控制器_1_memtoreg ), .MemWrite(\硬布线控制器_1_memwrite ), .ALU_SRC(\硬布线控制器_1_alu_src ),
    .RegWrite(\硬布线控制器_1_regwrite ), .SysCALL(syscall), .SignedExt(SignedExt), .RegDst(\硬布线控制器_1_regdst ),
    .JR(JR), .JMP(JMP), .Beq(Beq), .JAL(JAL), .Bne(Bne), .SH(SH), .BGTZ(BGTZ), .SRLV(SRLV), .ERET(eret));  // open: RS, MFC0, MTC0
  Multiplexer #(.width(5), .enable("false")) multiplexer_4 (
    .in0(rom_1_data[25:21]), .in1(5'b00010), .out(multiplexer_4_out), .sel(syscall));
  Multiplexer #(.width(5), .enable("false")) multiplexer_5 (
    .in0(rom_1_data[20:16]), .in1(5'b00100), .out(multiplexer_5_out), .sel(syscall));
  Multiplexer #(.width(5), .enable("false")) multiplexer_6 (
    .in0(rom_1_data[20:16]), .in1(rom_1_data[15:11]), .out(multiplexer_6_out), .sel(\硬布线控制器_1_regdst ));
  Shifter #(.width(32), .shift("ar")) shifter_1 (
    .in({rom_1_data[15:0], {16{1'b0}}}), .\dist (5'b10000), .out(shifter_1_out));
  Demultiplexer #(.select(2), .enable("false")) demultiplexer_1 (
    .out0(demultiplexer_1_out0), .out1(demultiplexer_1_out1), .out2(demultiplexer_1_out2), .in(1'b1), .sel(IR));  // open: out3
  D_Flip_Flop d_ff_7 (.clk(CLK), .D(IE), .Qn(IE), .en(or_7_out), .reset(RST));  // open: Q, preset
  Hex_Digit_Display hex_digit_display_8 (.value(LedData[3:0]));  // open: dp
  and and_4 (and_4_out, \硬布线控制器_1_regwrite , nohalt, ~\中断请求 );  // AND_Gate
  Multiplexer #(.width(5), .enable("false")) multiplexer_7 (
    .in0(multiplexer_6_out), .in1({5{1'b1}}), .out(multiplexer_7_out), .sel(JAL));
  Multiplexer #(.width(32), .enable("false")) multiplexer_8 (
    .in0({{16{1'b0}}, rom_1_data[15:0]}), .in1(shifter_1_out), .out(multiplexer_8_out), .sel(SignedExt));
  Priority_Encoder #(.select(2)) priority_encoder_1 (
    .in0(d_ff_4_q), .in1(d_ff_5_q), .in2(d_ff_6_q), .in3(1'b0), .out(\中断编号 ), .gs(priority_encoder_1_gs),
    .en_in(1'b1));  // open: en_out
  Comparator #(.width(32), .mode("unsigned")) comparator_1 (
    .a(PCout), .b(32'hf), .gt(comparator_1_gt));  // open: eq, lt
  or or_8 (or_8_out, \中断请求 , eret);
  and and_5 (\同步清零1 , eret, demultiplexer_1_out0);
  and and_6 (\同步清零2 , demultiplexer_1_out1, eret);
  and and_7 (\同步清零3 , demultiplexer_1_out2, eret);
  MIPS_Regifile mips_regifile_1 (
    .Din(multiplexer_16_out), .Clk(CLK), .R1(R1), .R2(R2), .WE(and_4_out), .W_num(multiplexer_7_out),
    .R1_num(multiplexer_4_out), .R2_num(multiplexer_5_out));
  Shifter #(.width(32)) shifter_2 (.in(shifter_1_out), .\dist (5'b00010), .out(shifter_2_out));
  and and_8 (and_8_out, Beq, Equ);
  not not_1 (not_1_out, Equ);
  and and_9 (and_9_out, not_1_out, Bne);
  and and_10 (and_10_out, BGTZ, comparator_2_gt);
  Comparator #(.width(32)) comparator_2 (.a(R1), .b({32{1'b0}}), .gt(comparator_2_gt));  // open: eq, lt
  and and_11 (\中断请求 , priority_encoder_1_gs, IE, comparator_1_gt);
  Register #(.width(2), .trigger("falling")) u_IR (.D(\中断编号 ), .Q(IR), .clk(or_8_out));  // open: en, clr
  Register #(.width(32)) u_EPC (.D(PCout), .en(\中断请求 ), .Q(EPC), .clk(CLK), .clr(RST));
  // Probe on \总周期数 
  // Probe on \无条件分支数 
  // Probe on \条件分支成功数 
  Multiplexer #(.width(32), .enable("false")) multiplexer_9 (
    .in0(R2), .in1(multiplexer_8_out), .out(multiplexer_9_out), .sel(\硬布线控制器_1_alu_src ));
  Multiplexer #(.width(5), .enable("false")) multiplexer_10 (
    .in0(rom_1_data[10:6]), .in1(R1[4:0]), .out(multiplexer_10_out), .sel(SRLV));
  Adder #(.width(32)) adder_2 (.a(PCout), .b(shifter_2_out), .out(adder_2_out));  // open: cin, cout
  or or_9 (or_9_out[0], JMP, JAL);
  or or_10 (or_9_out[2], and_8_out, and_9_out, and_10_out);
  and and_12 (and_12_out, nohalt, ~\中断请求 );  // AND_Gate
  MIPS_ALU mips_alu_1 (
    .X(R1), .Y(multiplexer_9_out), .AluOP(\硬布线控制器_1_alu_op ), .Equal(Equ), .Result(mips_alu_1_result),
    .shamt(multiplexer_10_out));  // open: Result_2
  Multiplexer #(.select(3), .width(32), .enable("false")) multiplexer_11 (
    .in0(PCout), .in1({PCout[31:28], rom_1_data[25:0], 2'b00}), .in2(R1), .in3({32{1'b0}}),
    .in4(adder_2_out), .in5({32{1'b0}}), .in6({32{1'b0}}), .in7({32{1'b0}}), .out(PCinCom),
    .sel({or_9_out[2], JR, or_9_out[0]}));
  or or_11 (or_11_out, or_9_out[0], JR);
  Comparator #(.width(32)) comparator_3 (.a(R1), .b(32'h22), .eq(comparator_3_eq));  // open: gt, lt
  Multiplexer #(.width(4), .enable("false")) multiplexer_12 (
    .in0(4'b1111), .in1(multiplexer_13_out), .out(multiplexer_12_out), .sel(SH));
  Multiplexer #(.width(4), .enable("false")) multiplexer_13 (
    .in0(4'b0011), .in1(4'b1100), .out(multiplexer_13_out), .sel(mips_alu_1_result[1]));
  and and_13 (and_13_out, and_12_out, or_11_out);
  and and_14 (and_14_out, and_12_out, or_9_out[2]);
  not not_2 (not_2_out, comparator_3_eq);
  and and_15 (and_15_out, not_2_out, syscall);
  LED led_4 (.in(\中断请求 ));
  // Probe on \中断编号 
  // Probe on IR
  and and_16 (and_16_out, \硬布线控制器_1_memwrite , nohalt, ~\中断请求 );  // AND_Gate
  Multiplexer #(.width(32), .enable("false")) multiplexer_14 (
    .in0(R2), .in1(shifter_3_out), .out(multiplexer_14_out), .sel(and_17_out));
  and and_17 (and_17_out, SH, mips_alu_1_result[1]);
  Shifter #(.width(32)) shifter_3 (.in(R2), .\dist (5'b10000), .out(shifter_3_out));
  Counter #(.width(16), .max('hffff)) counter_1 (
    .count(and_12_out), .Q(\总周期数 ), .clk(CLK), .clr(RST));  // open: load, D, carry
  Counter #(.width(16), .max('hffff)) counter_2 (
    .count(and_13_out), .Q(\无条件分支数 ), .clk(CLK), .clr(RST));  // open: load, D, carry
  Counter #(.width(16), .max('hffff)) counter_3 (
    .count(and_14_out), .Q(\条件分支成功数 ), .clk(CLK), .clr(RST));  // open: load, D, carry
  and and_18 (and_18_out, comparator_3_eq, syscall);
  or or_12 (or_12_out, Go, RST);
  Multiplexer #(.width(32), .enable("false")) multiplexer_15 (
    .in0(mips_alu_1_result), .in1(mips_ram_1_p9), .out(multiplexer_15_out), .sel(\硬布线控制器_1_memtoreg ));
  // MIPS_RAM mips_ram_1: pin names not known; wires that end beside it: \硬布线控制器_1_alu_op , mips_alu_1_result[21:2], multiplexer_14_out, and_16_out, multiplexer_12_out, CLK, \硬布线控制器_1_memtoreg , RST, mips_ram_1_p9
  Register #(.width(32)) register_1 (.D(R2), .en(and_18_out), .Q(LedData), .clk(and_18_out), .clr(RST));
  D_Flip_Flop d_ff_8 (
    .clk(CLK), .D(and_15_out), .Qn(nohalt), .preset(1'b0), .en(nohalt), .reset(or_12_out));  // open: Q
  Multiplexer #(.width(32), .enable("false")) multiplexer_16 (
    .in0(multiplexer_15_out), .in1(PCout), .out(multiplexer_16_out), .sel(JAL));

  // Notes on the sheet:
  //   中断源
  //   中断等待指示
  //   Single CPU with single interupt
  //   指令存储器
  //   PC+4
  //   contents of rom_1 (hex, n*v repeats v):
  //   20110001 8000c05 20110001 20120002 20130003 8000c09 20110001 20120002 20130003 8000c0d 20110001
  //   20120002 20130003 8000c11 20110001 20120002 20130003 c000cf8 20100001 20110001 118fc0 112020
  //   20020022 c 118882 12200001 8000c15 112020 20020022 c 20110001 118880 112020 20020022 c 12200001
  //   8000c1f 20110001 118fc0 112020 20020022 c 1188c3 112020 20020022 c 118903 112020 20020022 c 118903
  //   112020 20020022 c 118903 112020 20020022 c 118903 112020 20020022 c 118903 112020 20020022 c 118903
  //   112020 20020022 c 118903 112020 20020022 c 20100001 109fc0 139fc3 8021 2012000c 24160003 26100001
  //   3210000f 20080008 20090001 139900 2709825 132020 20020022 c 1094022 1500fff9 22100001 2018000f
  //   2188024 108700 20080008 20090001 139902 2709825 132021 20020022 c 1094022 1500fff9 108702 2c9b022
  //   12c00001 8000c50 4020 1084027 84400 3508ffff 82021 20020022 c 2010ffff 20110000 ae300000 22100001
  //   22310004 ae300000 22100001 22310004 ae300000 22100001 22310004 ae300000 22100001 22310004 ae300000
  //   22100001 22310004 ae300000 22100001 22310004 ae300000 22100001 22310004 ae300000 22100001 22310004
  //   ae300000 22100001 22310004 ae300000 22100001 22310004 ae300000 22100001 22310004 ae300000 22100001
  //   22310004 ae300000 22100001 22310004 ae300000 22100001 22310004 ae300000 22100001 22310004 ae300000
  //   22100001 22310004 22100001 8020 2011003c 8e130000 8e340000 274402a 11000002 ae330000 ae140000
  //   2231fffc 1611fff8 102020 20020022 c 22100004 2011003c 1611fff2 20020032 c 20080001 20090003 20110876
  //   118d00 112020 20020022 c 200b0008 1118806 1318806 112020 20020022 c 216bffff 1560fff9 2002000a c
  //   2008ffff 20117777 112020 20020022 c 200b0010 2288826 112020 20020022 c 216bffff 1560fffa 2002000a c
  //   20090000 200b0020 20110001 20120001 a5310000 112020 20020022 c 2328820 21290002 216bffff 1560fff8
  //   200b0010 20090000 8d310000 112020 20020022 c 21290004 216bffff 1560fff9 2002000a c 2011000f 112020
  //   20020022 c 2231ffff 1e20fffb 2002000a c 2002000a c 20100000 22100001 102020 20020022 c 22100002
  //   102020 20020022 c 22100003 102020 20020022 c 22100004 102020 20020022 c 22100005 102020 20020022 c
  //   22100006 102020 20020022 c 22100007 102020 20020022 c 22100008 102020 20020022 20020022 c 3e00008
  //   指令字
  //   数码管输出
  //   JMP
  //   JR
  //   OP
  //   Func
  //   rs
  //   rt
  //   rd
  //   shamt
  //   Imme
  //   Beq
  //   Bne
  //   MemToReg
  //   MemWrite
  //   AluOP
  //   AluSrcB
  //   RegWrite
  //   JAL
  //   RegDst
  //   Syscall
endmodule

module \单周期MIPS_with_MultiInterupt  (
);

  wire and_1_out, and_2_out, and_3_out, and_4_out, and_5_out, and_6_out, and_7_out, and_9_out, and_10_out,
       and_11_out, and_12_out, and_13_out, and_14_out, and_15_out, and_16_out, and_17_out, and_18_out,
       and_19_out, Beq, BGTZ, Bne, CLK, comparator_1_eq, comparator_2_eq, comparator_3_gt, comparator_4_gt,
       comparator_5_eq, comparator_6_gt, comparator_7_eq, comparator_8_eq, d_ff_1_q, d_ff_2_q, d_ff_3_q,
       d_ff_4_q, d_ff_5_q, d_ff_6_q, demultiplexer_1_out1, demultiplexer_1_out2, demultiplexer_1_out3, Equ,
       eret, Go, IE, IR1, IR2, IR3, JAL, JMP, JR, MFC0, MTC0, nohalt, not_1_out, not_2_out, or_4_out,
       or_5_out, or_6_out, or_7_out, or_8_out, or_9_out, or_12_out, or_13_out, or_14_out,
       priority_encoder_1_gs, regDst, RST, SH, SignedExt, SRLV, syscall, W1, W2, W3, \中断请求 , \同步清零1 ,
       \同步清零2 , \同步清零3 , \硬布线控制器_1_alu_src , \硬布线控制器_1_memtoreg , \硬布线控制器_1_memwrite , \硬布线控制器_1_regwrite ;
  wire [1:0] IR, multiplexer_17_out, \中断编号 ;
  wire [2:0] or_10_out;
  wire [3:0] multiplexer_14_out, multiplexer_15_out, \硬布线控制器_1_alu_op ;
  wire [4:0] multiplexer_4_out, multiplexer_5_out, multiplexer_6_out, multiplexer_7_out, multiplexer_11_out,
       rd;
  wire [15:0] \总周期数 , \无条件分支数 , \条件分支成功数 ;
  wire [31:0] adder_1_out, adder_2_out, copro, EPC, IntVec, LedData, mips_alu_1_result, mips_ram_1_p9,
       multiplexer_1_out, multiplexer_8_out, multiplexer_10_out, multiplexer_12_out, multiplexer_16_out,
       multiplexer_18_out, multiplexer_19_out, multiplexer_20_out, PCin, PCinCom, PCout, R1, R2, rom_1_data,
       shifter_1_out, shifter_2_out, shifter_3_out;

  Button \u_总复位  (.out(RST));
  Button _1 (.out(IR1));
  Button _2 (.out(IR2));
  Button _3 (.out(IR3));
  Button \u_继续运行  (.out(Go));
  LED led_1 (.in(W1));
  LED led_2 (.in(W2));
  LED led_3 (.in(W3));
  Register #(.width(32)) PC (.D(PCin), .en(nohalt), .Q(PCout), .clk(CLK), .clr(RST));
  // Probe on PCout
  or or_1 (W1, d_ff_4_q, d_ff_2_q);
  or or_2 (W2, d_ff_5_q, d_ff_3_q);
  D_Flip_Flop d_ff_1 (.clk(IR3), .D(1'b1), .Q(d_ff_1_q), .reset(d_ff_6_q));  // open: Qn, preset, en
  or or_3 (W3, d_ff_6_q, d_ff_1_q);
  Hex_Digit_Display hex_digit_display_1 (.value(LedData[31:28]));  // open: dp
  Adder #(.width(32)) adder_1 (.a(PCout), .b(32'h4), .out(adder_1_out));  // open: cin, cout
  D_Flip_Flop d_ff_2 (.clk(IR1), .D(1'b1), .Q(d_ff_2_q), .reset(d_ff_4_q));  // open: Qn, preset, en
  or or_4 (or_4_out, d_ff_2_q, d_ff_4_q);
  D_Flip_Flop d_ff_3 (.clk(IR2), .D(1'b1), .Q(d_ff_3_q), .reset(d_ff_5_q));  // open: Qn, preset, en
  or or_5 (or_5_out, d_ff_3_q, d_ff_5_q);
  or or_6 (or_6_out, d_ff_1_q, d_ff_6_q);
  Multiplexer #(.width(32), .enable("false")) multiplexer_1 (
    .in0(PCinCom), .in1(IntVec), .out(multiplexer_1_out), .sel(\中断请求 ));
  Multiplexer #(.width(32), .enable("false")) multiplexer_2 (
    .in0(multiplexer_1_out), .in1(EPC), .out(PCin), .sel(eret));
  Comparator #(.width(5), .mode("unsigned")) comparator_1 (.a(rd), .b(5'b01100), .eq(comparator_1_eq));  // open: gt, lt
  Hex_Digit_Display hex_digit_display_2 (.value(LedData[23:20]));  // open: dp
  Hex_Digit_Display hex_digit_display_3 (.value(LedData[27:24]));  // open: dp
  ROM #(.addrWidth(10), .dataWidth(32)) rom_1 (
    .addr(PCout[11:2]), .data({rom_1_data[31:16], rd, rom_1_data[10:0]}), .sel(1'b1));
  and and_1 (and_1_out, or_4_out, ~\同步清零1 );  // AND_Gate
  and and_2 (and_2_out, or_5_out, ~\同步清零2 );  // AND_Gate
  and and_3 (and_3_out, or_6_out, ~\同步清零3 );  // AND_Gate
  Multiplexer #(.select(2), .width(32), .enable("false")) multiplexer_3 (
    .in0(32'h3310), .in1(32'h10), .in2(32'h3110), .in3(32'h3210), .out(IntVec), .sel(\中断编号 ));
  Hex_Digit_Display hex_digit_display_4 (.value(LedData[15:12]));  // open: dp
  Hex_Digit_Display hex_digit_display_5 (.value(LedData[19:16]));  // open: dp
  D_Flip_Flop d_ff_4 (.clk(CLK), .D(and_1_out), .Q(d_ff_4_q));  // open: Qn, preset, en, reset
  D_Flip_Flop d_ff_5 (.clk(CLK), .D(and_2_out), .Q(d_ff_5_q));  // open: Qn, preset, en, reset
  D_Flip_Flop d_ff_6 (.clk(CLK), .D(and_3_out), .Q(d_ff_6_q));  // open: Qn, preset, en, reset
  or or_7 (or_7_out, \中断请求 , eret, and_4_out);
  and and_4 (and_4_out, MTC0, comparator_1_eq);
  Hex_Digit_Display hex_digit_display_6 (.value(LedData[7:4]));  // open: dp
  Hex_Digit_Display hex_digit_display_7 (.value(LedData[11:8]));  // open: dp
  Clock clock_1 (.out(CLK));
  \硬布线控制器  \u_硬布线控制器_1  (
    .Func(rom_1_data[5:0]), .OP(rom_1_data[31:26]), .ALU_OP(\硬布线控制器_1_alu_op ),
    .MemToReg(\硬布线控制器_1_memtoreg ), .MemWrite(\硬布线控制器_1_memwrite ), .ALU_SRC(\硬布线控制器_1_alu_src ),
    .RegWrite(\硬布线控制器_1_regwrite ), .SysCALL(syscall), .SignedExt(SignedExt), .RegDst(regDst), .JR(JR),
    .JMP(JMP), .Beq(Beq), .JAL(JAL), .Bne(Bne), .SH(SH), .BGTZ(BGTZ), .SRLV(SRLV), .ERET(eret),
    .RS(rom_1_data[25:21]), .MFC0(MFC0), .MTC0(MTC0));
  Multiplexer #(.width(5), .enable("false")) multiplexer_4 (
    .in0(rom_1_data[25:21]), .in1(5'b00010), .out(multiplexer_4_out), .sel(syscall));
  Multiplexer #(.width(5), .enable("false")) multiplexer_5 (
    .in0(rom_1_data[20:16]), .in1(5'b00100), .out(multiplexer_5_out), .sel(syscall));
  Multiplexer #(.width(5), .enable("false")) multiplexer_6 (
    .in0(rom_1_data[20:16]), .in1(rd), .out(multiplexer_6_out), .sel(regDst));
  Shifter #(.width(32), .shift("ar")) shifter_1 (
    .in({rd, rom_1_data[10:0], {16{1'b0}}}), .\dist (5'b10000), .out(shifter_1_out));
  Comparator #(.width(5), .mode("unsigned")) comparator_2 (.a(rd), .b(5'b01110), .eq(comparator_2_eq));  // open: gt, lt
  D_Flip_Flop d_ff_7 (.clk(CLK), .D(IE), .Qn(IE), .en(or_7_out), .reset(RST));  // open: Q, preset
  Hex_Digit_Display hex_digit_display_8 (.value(LedData[3:0]));  // open: dp
  Multiplexer #(.width(5), .enable("false")) multiplexer_7 (
    .in0(multiplexer_6_out), .in1({5{1'b1}}), .out(multiplexer_7_out), .sel(JAL));
  Multiplexer #(.width(32), .enable("false")) multiplexer_8 (
    .in0({{16{1'b0}}, rd, rom_1_data[10:0]}), .in1(shifter_1_out), .out(multiplexer_8_out), .sel(SignedExt));
  Priority_Encoder #(.select(2)) priority_encoder_1 (
    .in0(1'b1), .in1(d_ff_4_q), .in2(d_ff_5_q), .in3(d_ff_6_q), .out(\中断编号 ), .gs(priority_encoder_1_gs),
    .en_in(1'b1));  // open: en_out
  Comparator #(.width(32), .mode("unsigned")) comparator_3 (
    .a(PCout), .b(32'hf), .gt(comparator_3_gt));  // open: eq, lt
  Comparator #(.width(2), .mode("unsigned")) comparator_4 (.a(\中断编号 ), .b(IR), .gt(comparator_4_gt));  // open: eq, lt
  Multiplexer #(.width(32), .enable("false")) multiplexer_9 (
    .in0({{30{1'b0}}, IR}), .in1(EPC), .out(copro), .sel(comparator_2_eq));
  Comparator #(.width(5), .mode("unsigned")) comparator_5 (.a(rd), .b(5'b01110), .eq(comparator_5_eq));  // open: gt, lt
  MIPS_Regifile mips_regifile_1 (
    .Din(multiplexer_20_out), .Clk(CLK), .R1(R1), .R2(R2), .WE(or_9_out), .W_num(multiplexer_7_out),
    .R1_num(multiplexer_4_out), .R2_num(multiplexer_5_out));
  Shifter #(.width(32)) shifter_2 (.in(shifter_1_out), .\dist (5'b00010), .out(shifter_2_out));
  and and_5 (and_5_out, Beq, Equ);
  not not_1 (not_1_out, Equ);
  and and_6 (and_6_out, not_1_out, Bne);
  and and_7 (and_7_out, BGTZ, comparator_6_gt);
  Comparator #(.width(32)) comparator_6 (.a(R1), .b({32{1'b0}}), .gt(comparator_6_gt));  // open: eq, lt
  and and_8 (\中断请求 , priority_encoder_1_gs, IE, comparator_3_gt, comparator_4_gt);
  or or_8 (or_8_out, \中断请求 , and_9_out);
  and and_9 (and_9_out, MTC0, comparator_5_eq);
  // Probe on \总周期数 
  // Probe on \无条件分支数 
  // Probe on \条件分支成功数 
  or or_9 (or_9_out, MFC0, and_10_out);
  and and_10 (and_10_out, ~\中断请求 , nohalt, \硬布线控制器_1_regwrite );  // AND_Gate
  Multiplexer #(.width(32), .enable("false")) multiplexer_10 (
    .in0(R2), .in1(multiplexer_8_out), .out(multiplexer_10_out), .sel(\硬布线控制器_1_alu_src ));
  Multiplexer #(.width(5), .enable("false")) multiplexer_11 (
    .in0(rom_1_data[10:6]), .in1(R1[4:0]), .out(multiplexer_11_out), .sel(SRLV));
  Adder #(.width(32)) adder_2 (.a(adder_1_out), .b(shifter_2_out), .out(adder_2_out));  // open: cin, cout
  or or_10 (or_10_out[0], JMP, JAL);
  or or_11 (or_10_out[2], and_5_out, and_6_out, and_7_out);
  and and_11 (and_11_out, nohalt, ~\中断请求 );  // AND_Gate
  Register #(.width(32)) u_EPC (.D(multiplexer_12_out), .en(or_8_out), .Q(EPC), .clk(CLK), .clr(RST));
  Multiplexer #(.width(32), .enable("false")) multiplexer_12 (
    .in0(PCout), .in1(R2), .out(multiplexer_12_out), .sel(and_9_out));
  MIPS_ALU mips_alu_1 (
    .X(R1), .Y(multiplexer_10_out), .AluOP(\硬布线控制器_1_alu_op ), .Equal(Equ), .Result(mips_alu_1_result),
    .shamt(multiplexer_11_out));  // open: Result_2
  Multiplexer #(.select(3), .width(32), .enable("false")) multiplexer_13 (
    .in0(adder_1_out), .in1({adder_1_out[31:28], rom_1_data[25:16], rd, rom_1_data[10:0], 2'b00}), .in2(R1),
    .in3({32{1'b0}}), .in4(adder_2_out), .in5({32{1'b0}}), .in6({32{1'b0}}), .in7({32{1'b0}}), .out(PCinCom),
    .sel({or_10_out[2], JR, or_10_out[0]}));
  or or_12 (or_12_out, or_10_out[0], JR);
  Comparator #(.width(5), .mode("unsigned")) comparator_7 (.a(rd), .b(5'b01000), .eq(comparator_7_eq));  // open: gt, lt
  // Probe on IR
  Multiplexer #(.width(4), .enable("false")) multiplexer_14 (
    .in0(4'b1111), .in1(multiplexer_15_out), .out(multiplexer_14_out), .sel(SH));
  Multiplexer #(.width(4), .enable("false")) multiplexer_15 (
    .in0(4'b0011), .in1(4'b1100), .out(multiplexer_15_out), .sel(mips_alu_1_result[1]));
  and and_12 (and_12_out, and_11_out, or_12_out);
  and and_13 (and_13_out, and_11_out, or_10_out[2]);
  Comparator #(.width(32)) comparator_8 (.a(R1), .b(32'h22), .eq(comparator_8_eq));  // open: gt, lt
  not not_2 (not_2_out, comparator_8_eq);
  Demultiplexer #(.select(2), .enable("false")) demultiplexer_1 (
    .out1(demultiplexer_1_out1), .out2(demultiplexer_1_out2), .out3(demultiplexer_1_out3), .in(1'b1), .sel(IR));  // open: out0
  and and_14 (and_14_out, \硬布线控制器_1_memwrite , nohalt, ~\中断请求 );  // AND_Gate
  Multiplexer #(.width(32), .enable("false")) multiplexer_16 (
    .in0(R2), .in1(shifter_3_out), .out(multiplexer_16_out), .sel(and_15_out));
  and and_15 (and_15_out, SH, mips_alu_1_result[1]);
  Shifter #(.width(32)) shifter_3 (.in(R2), .\dist (5'b10000), .out(shifter_3_out));
  Counter #(.width(16), .max('hffff)) counter_1 (
    .count(and_11_out), .Q(\总周期数 ), .clk(CLK), .clr(RST));  // open: load, D, carry
  Counter #(.width(16), .max('hffff)) counter_2 (
    .count(and_12_out), .Q(\无条件分支数 ), .clk(CLK), .clr(RST));  // open: load, D, carry
  Counter #(.width(16), .max('hffff)) counter_3 (
    .count(and_13_out), .Q(\条件分支成功数 ), .clk(CLK), .clr(RST));  // open: load, D, carry
  and and_16 (and_16_out, comparator_8_eq, syscall);
  and and_17 (and_17_out, not_2_out, syscall);
  or or_13 (or_13_out, Go, RST);
  Multiplexer #(.width(2), .enable("false")) multiplexer_17 (
    .in0(\中断编号 ), .in1(R2[1:0]), .out(multiplexer_17_out), .sel(and_18_out));
  and and_18 (and_18_out, MTC0, comparator_7_eq);
  and and_19 (and_19_out, MFC0, comparator_7_eq);
  Multiplexer #(.width(32), .enable("false")) multiplexer_18 (
    .in0(mips_alu_1_result), .in1(mips_ram_1_p9), .out(multiplexer_18_out), .sel(\硬布线控制器_1_memtoreg ));
  // MIPS_RAM mips_ram_1: pin names not known; wires that end beside it: \硬布线控制器_1_alu_op , mips_alu_1_result[21:2], multiplexer_16_out, and_14_out, multiplexer_14_out, CLK, \硬布线控制器_1_memtoreg , RST, mips_ram_1_p9
  D_Flip_Flop d_ff_8 (
    .clk(CLK), .D(and_17_out), .Qn(nohalt), .preset(1'b0), .en(nohalt), .reset(or_13_out));  // open: Q
  Register #(.width(2), .trigger("falling")) u_IR (
    .D(multiplexer_17_out), .Q(IR), .clk(or_14_out), .clr(RST));  // open: en
  or or_14 (or_14_out, and_18_out, and_19_out);
  and and_20 (\同步清零1 , and_18_out, demultiplexer_1_out1);
  and and_21 (\同步清零2 , demultiplexer_1_out2, and_18_out);
  and and_22 (\同步清零3 , demultiplexer_1_out3, and_18_out);
  Multiplexer #(.width(32), .enable("false")) multiplexer_19 (
    .in0(multiplexer_18_out), .in1(adder_1_out), .out(multiplexer_19_out), .sel(JAL));
  Register #(.width(32)) register_1 (.D(R2), .en(and_16_out), .Q(LedData), .clk(and_16_out), .clr(RST));
  Multiplexer #(.width(32), .enable("false")) multiplexer_20 (
    .in0(multiplexer_19_out), .in1(copro), .out(multiplexer_20_out), .sel(MFC0));

  // Notes on the sheet:
  //   中断源
  //   中断等待指示
  //   Single CPU with multiple interupt
  //   指令存储器
  //   PC+4
  //   contents of rom_1 (hex, n*v repeats v):
  //   201d2ffc 20093310 1200008 0 23bdfffc afa90000 40094000 23bdfffc 0 0 afa90000 40097000 23bdfffc 0 0
  //   afa90000 23bdfffc afb00000 23bdfffc afb30000 23bdfffc afb40000 23bdfffc afb50000 23bdfffc afb60000
  //   23bdfffc afa20000 40896000 20160001 20140006 20150001 168020 108100 2149825 132020 20020022 c
  //   1600fffa 295a022 1680fff7 40896000 8fa20000 27bd0004 8fb60000 27bd0004 8fb50000 27bd0004 8fb40000
  //   27bd0004 8fb30000 27bd0004 8fb00000 27bd0004 8fa90000 27bd0004 0 0 40897000 8fa90000 27bd0004 0 0
  //   40894000 8fa90000 27bd0004 42000018 0 23bdfffc afa90000 40094000 23bdfffc 0 0 afa90000 40097000
  //   23bdfffc 0 0 afa90000 23bdfffc afb00000 23bdfffc afb30000 23bdfffc afb40000 23bdfffc afb50000
  //   23bdfffc afb60000 23bdfffc afa20000 40896000 20160002 20140006 20150001 168020 108100 2149825 132020
  //   20020022 c 1600fffa 295a022 1680fff7 40896000 8fa20000 27bd0004 8fb60000 27bd0004 8fb50000 27bd0004
  //   8fb40000 27bd0004 8fb30000 27bd0004 8fb00000 27bd0004 8fa90000 27bd0004 0 0 40897000 8fa90000
  //   27bd0004 0 0 40894000 8fa90000 27bd0004 42000018 0 23bdfffc afa90000 40094000 23bdfffc 0 0 afa90000
  //   40097000 23bdfffc 0 0 afa90000 23bdfffc afb00000 23bdfffc afb30000 23bdfffc afb40000 23bdfffc
  //   afb50000 23bdfffc afb60000 23bdfffc afa20000 40896000 20160003 20140006 20150001 168020 108100
  //   2149825 132020 20020022 c 1600fffa 295a022 1680fff7 40896000 8fa20000 27bd0004 8fb60000 27bd0004
  //   8fb50000 27bd0004 8fb40000 27bd0004 8fb30000 27bd0004 8fb00000 27bd0004 8fa90000 27bd0004 0 0
  //   40897000 8fa90000 27bd0004 0 0 40894000 8fa90000 27bd0004 42000018 0 20110001 8000cc9 20110001
  //   20120002 20130003 8000ccd 20110001 20120002 20130003 8000cd1 20110001 20120002 20130003 8000cd5
  //   20110001 20120002 20130003 c000dbc 20100001 20110001 118fc0 112020 20020022 c 118882 12200001
  //   8000cd9 112020 20020022 c 20110001 118880 112020 20020022 c 12200001 8000ce3 20110001 118fc0 112020
  //   20020022 c 1188c3 112020 20020022 c 118903 112020 20020022 c 118903 112020 20020022 c 118903 112020
  //   20020022 c 118903 112020 20020022 c 118903 112020 20020022 c 118903 112020 20020022 c 118903 112020
  //   20020022 c 20100001 109fc0 139fc3 8021 2012000c 24160003 26100001 3210000f 20080008 20090001 139900
  //   2709825 132020 20020022 c 1094022 1500fff9 22100001 2018000f 2188024 108700 20080008 20090001 139902
  //   2709825 132021 20020022 c 1094022 1500fff9 108702 2c9b022 12c00001 8000d14 4020 1084027 84400
  //   3508ffff 82021 20020022 c 2010ffff 20110000 ae300000 22100001 22310004 ae300000 22100001 22310004
  //   ae300000 22100001 22310004 ae300000 22100001 22310004 ae300000 22100001 22310004 ae300000 22100001
  //   22310004 ae300000 22100001 22310004 ae300000 22100001 22310004 ae300000 22100001 22310004 ae300000
  //   22100001 22310004 ae300000 22100001 22310004 ae300000 22100001 22310004 ae300000 22100001 22310004
  //   ae300000 22100001 22310004 ae300000 22100001 22310004 ae300000 22100001 22310004 22100001 8020
  //   2011003c 8e130000 8e340000 274402a 11000002 ae330000 ae140000 2231fffc 1611fff8 102020 20020022 c
  //   22100004 2011003c 1611fff2 20020032 c 20080001 20090003 20110876 118d00 112020 20020022 c 200b0008
  //   1118806 1318806 112020 20020022 c 216bffff 1560fff9 20020032 c 2008ffff 20117777 112020 20020022 c
  //   200b0010 2288826 112020 20020022 c 216bffff 1560fffa 20020032 c 20090000 200b0020 20110001 20120001
  //   a5310000 112020 20020022 c 2328820 21290002 216bffff 1560fff8 200b0010 20090000 8d310000 112020
  //   20020022 c 21290004 216bffff 1560fff9 20020032 c 2011000f 112020 20020022 c 2231ffff 1e20fffb
  //   2002000a c 20020032 c 20100000 22100001 102020 20020022 c 22100002 102020 20020022 c 22100003 102020
  //   20020022 c 22100004 102020 20020022 c 22100005 102020 20020022 c 22100006 102020 20020022 c 22100007
  //   102020 20020022 c 22100008 102020 20020022 20020022 c 3e00008
  //   指令字
  //   数码管输出
  //   JR
  //   Func
  //   rs
  //   rt
  //   shamt
  //   Imme
  //   Beq
  //   Bne
  //   MemToReg
  //   MemWrite
  //   AluOP
  //   AluSrcB
  //   RegWrite
  //   JAL
endmodule

// 单周期硬布线控制器
module \硬布线控制器  (
  input  [5:0] OP,
  input  [5:0] Func,
  input  [4:0] RS,
  output [3:0] ALU_OP,
  output MemToReg,
  output MemWrite,
  output ALU_SRC,
  output RegWrite,
  output SysCALL,
  output SignedExt,
  output RegDst,
  output Beq,
  output Bne,
  output JR,
  output JMP,
  output JAL,
  output SH,
  output BGTZ,
  output SRLV,
  output ERET,
  output MFC0,
  output MTC0
);

  \运算控制器  \u_运算控制器_1  (
    .OP0(OP[0]), .OP1(OP[1]), .OP2(OP[2]), .OP3(OP[3]), .OP4(OP[4]), .OP5(OP[5]), .F0(Func[0]), .F1(Func[1]),
    .F2(Func[2]), .F3(Func[3]), .F4(Func[4]), .F5(Func[5]), .S0(ALU_OP[0]), .S1(ALU_OP[1]), .S2(ALU_OP[2]),
    .S3(ALU_OP[3]));
  \控制信号生成  \u_控制信号生成_1  (
    .OP0(OP[0]), .MemToReg(MemToReg), .OP1(OP[1]), .OP2(OP[2]), .OP3(OP[3]), .OP4(OP[4]),
    .MemWrite(MemWrite), .OP5(OP[5]), .F0(Func[0]), .F1(Func[1]), .F2(Func[2]), .F3(Func[3]), .F4(Func[4]),
    .F5(Func[5]), .ALU_SRC(ALU_SRC), .RegWrite(RegWrite), .SysCALL(SysCALL), .SignedExt(SignedExt),
    .RegDst(RegDst), .BEQ(Beq), .BNE(Bne), .JR(JR), .JMP(JMP), .JAL(JAL), .SH(SH), .BGTZ(BGTZ), .SRLV(SRLV),
    .ERET(ERET), .R0(RS[0]), .R1(RS[1]), .R2(RS[2]), .R3(RS[3]), .R4(RS[4]), .MFC0(MFC0), .MTC0(MTC0));

  // Other names for the same wires on the sheet: OP_CODE[5:0] = OP

  // Notes on the sheet:
  //   运算器控制器，根据指令生成运算器功能选择信号
  //   控制信号生成，产生数据通路需要的其他控制信号
endmodule

// 运算器控制器
module \运算控制器  (
  input  OP0,
  input  OP1,
  input  OP2,
  input  OP3,
  input  OP4,
  input  OP5,
  input  F0,
  input  F1,
  input  F2,
  input  F3,
  input  F4,
  input  F5,
  output S0,
  output S1,
  output S2,
  output S3
);

  wire and_1_out, and_2_out, and_3_out, and_4_out, and_5_out, and_6_out, and_7_out, and_8_out, and_9_out,
       and_10_out, and_11_out, and_12_out, and_13_out, and_14_out, and_15_out, and_16_out, and_17_out,
       and_18_out, and_19_out, and_20_out, and_21_out, and_22_out, and_23_out, and_24_out, and_25_out,
       and_26_out, and_27_out, and_28_out, and_29_out, and_30_out, and_31_out, and_32_out, and_33_out,
       and_34_out, and_35_out, and_36_out, and_37_out, and_38_out, and_39_out, not_1_out, not_2_out,
       not_3_out, not_4_out, not_5_out, not_6_out, not_7_out, not_8_out, not_9_out, not_10_out, not_11_out,
       not_12_out, not_13_out, not_14_out, not_15_out, not_16_out, not_17_out, not_18_out, not_19_out,
       not_20_out, not_21_out, not_22_out, not_23_out, not_24_out, not_25_out, not_26_out, not_27_out,
       not_28_out, not_29_out, not_30_out, not_31_out, not_32_out, not_33_out, not_34_out, not_35_out,
       not_36_out, not_37_out, not_38_out, not_39_out, not_40_out, not_41_out, not_42_out, not_43_out,
       not_44_out, not_45_out, not_46_out, not_47_out, not_48_out, not_49_out, not_50_out, not_51_out,
       not_52_out, not_53_out, not_54_out, not_55_out, not_56_out, not_57_out, not_58_out, not_59_out,
       not_60_out, not_61_out, not_62_out, not_63_out, not_64_out, not_65_out, not_66_out, not_67_out,
       not_68_out, not_69_out, not_70_out, not_71_out, not_72_out, not_73_out, not_74_out, not_75_out,
       not_76_out, not_77_out, not_78_out, not_79_out, not_80_out, not_81_out, not_82_out, not_83_out,
       not_84_out, not_85_out, not_86_out, not_87_out, not_88_out, not_89_out, not_90_out, not_91_out,
       not_92_out, not_93_out, not_94_out, not_95_out, not_96_out, not_97_out, not_98_out, not_99_out,
       not_100_out, not_101_out, not_102_out, not_103_out, not_104_out, not_105_out, not_106_out,
       not_107_out, not_108_out, not_109_out, not_110_out, not_111_out, not_112_out, not_113_out,
       not_114_out, not_115_out, not_116_out, not_117_out, not_118_out, not_119_out, not_120_out,
       not_121_out, not_122_out, not_123_out, not_124_out, not_125_out, not_126_out, not_127_out,
       not_128_out, not_129_out, not_130_out, not_131_out, not_132_out, not_133_out, not_134_out,
       not_135_out, not_136_out, not_137_out, not_138_out, not_139_out, not_140_out, not_141_out,
       not_142_out, not_143_out, not_144_out, not_145_out, not_146_out, not_147_out, not_148_out,
       not_149_out, not_150_out, not_151_out, not_152_out, not_153_out, not_154_out, not_155_out,
       not_156_out, not_157_out, not_158_out, not_159_out, not_160_out, not_161_out, not_162_out,
       not_163_out, not_164_out, not_165_out, not_166_out, not_167_out, not_168_out, not_169_out,
       not_170_out, not_171_out, not_172_out, not_173_out, not_174_out, not_175_out, not_176_out,
       not_177_out, not_178_out, not_179_out, not_180_out, not_181_out, not_182_out, not_183_out,
       not_184_out, not_185_out, not_186_out, not_187_out, not_188_out, not_189_out, not_190_out,
       not_191_out, not_192_out, not_193_out, not_194_out, not_195_out, not_196_out, not_197_out,
       not_198_out, not_199_out, not_200_out, not_201_out, not_202_out, not_203_out, not_204_out,
       not_205_out, not_206_out, not_207_out, not_208_out, not_209_out, not_210_out, not_211_out,
       not_212_out, not_213_out, not_214_out, not_215_out, not_216_out, not_217_out, not_218_out,
       not_219_out, not_220_out, not_221_out, not_222_out, not_223_out, not_224_out, not_225_out,
       not_226_out, not_227_out, not_228_out, not_229_out, not_230_out, not_231_out, not_232_out,
       not_233_out, not_234_out, not_235_out, not_236_out, not_237_out, not_238_out, not_239_out,
       not_240_out, not_241_out, not_242_out, not_243_out, not_244_out, not_245_out, not_246_out,
       not_247_out, not_248_out, not_249_out, not_250_out, not_251_out, not_252_out, not_253_out,
       not_254_out, not_255_out, not_256_out, not_257_out, not_258_out, not_259_out, not_260_out,
       not_261_out, not_262_out, not_263_out, not_264_out, not_265_out, not_266_out, not_267_out,
       not_268_out, not_269_out, not_270_out;

  not not_1 (not_1_out, OP5);
  not not_2 (not_2_out, OP4);
  not not_3 (not_3_out, OP3);
  not not_4 (not_4_out, OP2);
  not not_5 (not_5_out, OP1);
  not not_6 (not_6_out, OP0);
  not not_7 (not_7_out, F5);
  not not_8 (not_8_out, F4);
  not not_9 (not_9_out, F3);
  not not_10 (not_10_out, F2);
  not not_11 (not_11_out, OP5);
  not not_12 (not_12_out, OP4);
  not not_13 (not_13_out, OP3);
  not not_14 (not_14_out, OP2);
  not not_15 (not_15_out, OP1);
  not not_16 (not_16_out, OP0);
  not not_17 (not_17_out, F4);
  not not_18 (not_18_out, F3);
  not not_19 (not_19_out, F2);
  not not_20 (not_20_out, F1);
  not not_21 (not_21_out, F0);
  not not_22 (not_22_out, OP5);
  not not_23 (not_23_out, OP4);
  not not_24 (not_24_out, OP3);
  not not_25 (not_25_out, OP2);
  not not_26 (not_26_out, OP1);
  not not_27 (not_27_out, OP0);
  not not_28 (not_28_out, F4);
  not not_29 (not_29_out, F3);
  not not_30 (not_30_out, F2);
  not not_31 (not_31_out, F1);
  not not_32 (not_32_out, OP5);
  not not_33 (not_33_out, OP4);
  not not_34 (not_34_out, OP3);
  not not_35 (not_35_out, OP2);
  not not_36 (not_36_out, OP1);
  not not_37 (not_37_out, OP0);
  not not_38 (not_38_out, F4);
  not not_39 (not_39_out, F3);
  not not_40 (not_40_out, F1);
  not not_41 (not_41_out, F0);
  not not_42 (not_42_out, OP5);
  not not_43 (not_43_out, OP4);
  not not_44 (not_44_out, OP3);
  not not_45 (not_45_out, OP2);
  not not_46 (not_46_out, OP1);
  not not_47 (not_47_out, OP0);
  not not_48 (not_48_out, F4);
  not not_49 (not_49_out, F2);
  not not_50 (not_50_out, F0);
  not not_51 (not_51_out, OP5);
  not not_52 (not_52_out, OP4);
  not not_53 (not_53_out, OP2);
  not not_54 (not_54_out, OP1);
  not not_55 (not_55_out, OP0);
  not not_56 (not_56_out, OP5);
  not not_57 (not_57_out, OP4);
  not not_58 (not_58_out, OP1);
  not not_59 (not_59_out, OP0);
  not not_60 (not_60_out, OP5);
  not not_61 (not_61_out, OP4);
  not not_62 (not_62_out, OP2);
  not not_63 (not_63_out, OP1);
  not not_64 (not_64_out, OP5);
  not not_65 (not_65_out, OP4);
  not not_66 (not_66_out, OP2);
  not not_67 (not_67_out, OP0);
  not not_68 (not_68_out, OP4);
  not not_69 (not_69_out, OP3);
  not not_70 (not_70_out, OP2);
  not not_71 (not_71_out, OP4);
  not not_72 (not_72_out, OP2);
  not not_73 (not_73_out, OP5);
  not not_74 (not_74_out, OP4);
  not not_75 (not_75_out, OP3);
  not not_76 (not_76_out, OP2);
  not not_77 (not_77_out, OP1);
  not not_78 (not_78_out, OP0);
  not not_79 (not_79_out, F4);
  not not_80 (not_80_out, F3);
  not not_81 (not_81_out, F0);
  not not_82 (not_82_out, OP4);
  not not_83 (not_83_out, OP2);
  not not_84 (not_84_out, OP1);
  not not_85 (not_85_out, OP5);
  not not_86 (not_86_out, OP4);
  not not_87 (not_87_out, OP3);
  not not_88 (not_88_out, OP2);
  not not_89 (not_89_out, OP1);
  not not_90 (not_90_out, OP0);
  not not_91 (not_91_out, F5);
  not not_92 (not_92_out, F4);
  not not_93 (not_93_out, F3);
  not not_94 (not_94_out, F2);
  not not_95 (not_95_out, F0);
  not not_96 (not_96_out, OP5);
  not not_97 (not_97_out, OP4);
  not not_98 (not_98_out, OP3);
  not not_99 (not_99_out, OP2);
  not not_100 (not_100_out, OP1);
  not not_101 (not_101_out, OP0);
  not not_102 (not_102_out, F4);
  not not_103 (not_103_out, F3);
  not not_104 (not_104_out, F2);
  not not_105 (not_105_out, F0);
  not not_106 (not_106_out, OP5);
  not not_107 (not_107_out, OP4);
  not not_108 (not_108_out, OP3);
  not not_109 (not_109_out, OP2);
  not not_110 (not_110_out, OP1);
  not not_111 (not_111_out, OP0);
  not not_112 (not_112_out, F4);
  not not_113 (not_113_out, F3);
  not not_114 (not_114_out, F1);
  not not_115 (not_115_out, F0);
  not not_116 (not_116_out, OP5);
  not not_117 (not_117_out, OP4);
  not not_118 (not_118_out, OP3);
  not not_119 (not_119_out, OP2);
  not not_120 (not_120_out, OP1);
  not not_121 (not_121_out, OP0);
  not not_122 (not_122_out, F4);
  not not_123 (not_123_out, F3);
  not not_124 (not_124_out, OP5);
  not not_125 (not_125_out, OP4);
  not not_126 (not_126_out, OP3);
  not not_127 (not_127_out, OP2);
  not not_128 (not_128_out, OP1);
  not not_129 (not_129_out, OP0);
  not not_130 (not_130_out, F4);
  not not_131 (not_131_out, F2);
  not not_132 (not_132_out, F0);
  not not_133 (not_133_out, OP5);
  not not_134 (not_134_out, OP4);
  not not_135 (not_135_out, OP1);
  not not_136 (not_136_out, OP0);
  not not_137 (not_137_out, OP5);
  not not_138 (not_138_out, OP4);
  not not_139 (not_139_out, OP2);
  not not_140 (not_140_out, OP0);
  not not_141 (not_141_out, OP5);
  not not_142 (not_142_out, OP4);
  not not_143 (not_143_out, OP3);
  not not_144 (not_144_out, OP2);
  not not_145 (not_145_out, OP1);
  not not_146 (not_146_out, OP0);
  not not_147 (not_147_out, F5);
  not not_148 (not_148_out, F4);
  not not_149 (not_149_out, F3);
  not not_150 (not_150_out, F0);
  not not_151 (not_151_out, OP5);
  not not_152 (not_152_out, OP4);
  not not_153 (not_153_out, OP3);
  not not_154 (not_154_out, OP2);
  not not_155 (not_155_out, OP1);
  not not_156 (not_156_out, OP0);
  not not_157 (not_157_out, F4);
  not not_158 (not_158_out, F3);
  not not_159 (not_159_out, F2);
  not not_160 (not_160_out, F1);
  not not_161 (not_161_out, F0);
  not not_162 (not_162_out, OP5);
  not not_163 (not_163_out, OP4);
  not not_164 (not_164_out, OP3);
  not not_165 (not_165_out, OP2);
  not not_166 (not_166_out, OP1);
  not not_167 (not_167_out, OP0);
  not not_168 (not_168_out, F4);
  not not_169 (not_169_out, F3);
  not not_170 (not_170_out, F2);
  not not_171 (not_171_out, F1);
  not not_172 (not_172_out, OP5);
  not not_173 (not_173_out, OP4);
  not not_174 (not_174_out, OP3);
  not not_175 (not_175_out, OP2);
  not not_176 (not_176_out, OP1);
  not not_177 (not_177_out, OP0);
  not not_178 (not_178_out, F4);
  not not_179 (not_179_out, F3);
  not not_180 (not_180_out, F2);
  not not_181 (not_181_out, F0);
  not not_182 (not_182_out, OP5);
  not not_183 (not_183_out, OP4);
  not not_184 (not_184_out, OP3);
  not not_185 (not_185_out, OP2);
  not not_186 (not_186_out, OP1);
  not not_187 (not_187_out, OP0);
  not not_188 (not_188_out, F4);
  not not_189 (not_189_out, F3);
  not not_190 (not_190_out, F1);
  not not_191 (not_191_out, F0);
  not not_192 (not_192_out, OP5);
  not not_193 (not_193_out, OP4);
  not not_194 (not_194_out, OP3);
  not not_195 (not_195_out, OP2);
  not not_196 (not_196_out, OP1);
  not not_197 (not_197_out, OP0);
  not not_198 (not_198_out, F4);
  not not_199 (not_199_out, F2);
  not not_200 (not_200_out, OP5);
  not not_201 (not_201_out, OP4);
  not not_202 (not_202_out, OP2);
  not not_203 (not_203_out, OP1);
  not not_204 (not_204_out, OP0);
  not not_205 (not_205_out, OP5);
  not not_206 (not_206_out, OP4);
  not not_207 (not_207_out, OP1);
  not not_208 (not_208_out, OP0);
  not not_209 (not_209_out, OP5);
  not not_210 (not_210_out, OP4);
  not not_211 (not_211_out, OP2);
  not not_212 (not_212_out, OP1);
  not not_213 (not_213_out, OP4);
  not not_214 (not_214_out, OP3);
  not not_215 (not_215_out, OP2);
  not not_216 (not_216_out, OP4);
  not not_217 (not_217_out, OP2);
  not not_218 (not_218_out, OP4);
  not not_219 (not_219_out, OP2);
  not not_220 (not_220_out, OP1);
  not not_221 (not_221_out, OP5);
  not not_222 (not_222_out, OP4);
  not not_223 (not_223_out, OP3);
  not not_224 (not_224_out, OP2);
  not not_225 (not_225_out, OP1);
  not not_226 (not_226_out, OP0);
  not not_227 (not_227_out, F4);
  not not_228 (not_228_out, F3);
  not not_229 (not_229_out, F1);
  not not_230 (not_230_out, OP5);
  not not_231 (not_231_out, OP4);
  not not_232 (not_232_out, OP3);
  not not_233 (not_233_out, OP2);
  not not_234 (not_234_out, OP1);
  not not_235 (not_235_out, OP0);
  not not_236 (not_236_out, F4);
  not not_237 (not_237_out, F3);
  not not_238 (not_238_out, OP5);
  not not_239 (not_239_out, OP4);
  not not_240 (not_240_out, OP3);
  not not_241 (not_241_out, OP2);
  not not_242 (not_242_out, OP1);
  not not_243 (not_243_out, OP0);
  not not_244 (not_244_out, F4);
  not not_245 (not_245_out, F2);
  not not_246 (not_246_out, F0);
  not not_247 (not_247_out, OP5);
  not not_248 (not_248_out, OP4);
  not not_249 (not_249_out, OP3);
  not not_250 (not_250_out, OP2);
  not not_251 (not_251_out, OP1);
  not not_252 (not_252_out, OP0);
  not not_253 (not_253_out, F4);
  not not_254 (not_254_out, F2);
  not not_255 (not_255_out, OP5);
  not not_256 (not_256_out, OP4);
  not not_257 (not_257_out, OP2);
  not not_258 (not_258_out, OP0);
  not not_259 (not_259_out, OP5);
  not not_260 (not_260_out, OP4);
  not not_261 (not_261_out, OP1);
  not not_262 (not_262_out, OP5);
  not not_263 (not_263_out, OP4);
  not not_264 (not_264_out, OP3);
  not not_265 (not_265_out, OP2);
  not not_266 (not_266_out, OP1);
  not not_267 (not_267_out, OP0);
  not not_268 (not_268_out, F4);
  not not_269 (not_269_out, F3);
  not not_270 (not_270_out, F0);
  and and_1 (and_1_out, not_1_out, not_2_out, not_3_out, not_4_out, not_5_out, not_6_out, not_7_out, not_8_out, not_9_out, not_10_out, F1, F0);
  and and_2 (and_2_out, not_11_out, not_12_out, not_13_out, not_14_out, not_15_out, not_16_out, F5, not_17_out, not_18_out, not_19_out, not_20_out, not_21_out);
  and and_3 (and_3_out, not_22_out, not_23_out, not_24_out, not_25_out, not_26_out, not_27_out, F5, not_28_out, not_29_out, not_30_out, not_31_out, F0);
  and and_4 (and_4_out, not_32_out, not_33_out, not_34_out, not_35_out, not_36_out, not_37_out, F5, not_38_out, not_39_out, F2, not_40_out, not_41_out);
  and and_5 (and_5_out, not_42_out, not_43_out, not_44_out, not_45_out, not_46_out, not_47_out, F5, not_48_out, F3, not_49_out, F1, not_50_out);
  and and_6 (and_6_out, not_51_out, not_52_out, OP3, not_53_out, not_54_out, not_55_out);
  and and_7 (and_7_out, not_56_out, not_57_out, OP3, OP2, not_58_out, not_59_out);
  and and_8 (and_8_out, not_60_out, not_61_out, OP3, not_62_out, not_63_out, OP0);
  and and_9 (and_9_out, not_64_out, not_65_out, OP3, not_66_out, OP1, not_67_out);
  and and_10 (and_10_out, OP5, not_68_out, not_69_out, not_70_out, OP1, OP0);
  and and_11 (and_11_out, OP5, not_71_out, OP3, not_72_out, OP1, OP0);
  and and_12 (and_12_out, not_73_out, not_74_out, not_75_out, not_76_out, not_77_out, not_78_out, F5, not_79_out, not_80_out, F2, F1, not_81_out);
  and and_13 (and_13_out, OP5, not_82_out, OP3, not_83_out, not_84_out, OP0);
  and and_14 (and_14_out, not_85_out, not_86_out, not_87_out, not_88_out, not_89_out, not_90_out, not_91_out, not_92_out, not_93_out, not_94_out, F1, not_95_out);
  and and_15 (and_15_out, not_96_out, not_97_out, not_98_out, not_99_out, not_100_out, not_101_out, F5, not_102_out, not_103_out, not_104_out, F1, not_105_out);
  and and_16 (and_16_out, not_106_out, not_107_out, not_108_out, not_109_out, not_110_out, not_111_out, F5, not_112_out, not_113_out, F2, not_114_out, not_115_out);
  and and_17 (and_17_out, not_116_out, not_117_out, not_118_out, not_119_out, not_120_out, not_121_out, F5, not_122_out, not_123_out, F2, F1, F0);
  and and_18 (and_18_out, not_124_out, not_125_out, not_126_out, not_127_out, not_128_out, not_129_out, F5, not_130_out, F3, not_131_out, F1, not_132_out);
  and and_19 (and_19_out, not_133_out, not_134_out, OP3, OP2, not_135_out, not_136_out);
  and and_20 (and_20_out, not_137_out, not_138_out, OP3, not_139_out, OP1, not_140_out);
  and and_21 (and_21_out, not_141_out, not_142_out, not_143_out, not_144_out, not_145_out, not_146_out, not_147_out, not_148_out, not_149_out, F2, F1, not_150_out);
  and and_22 (and_22_out, not_151_out, not_152_out, not_153_out, not_154_out, not_155_out, not_156_out, F5, not_157_out, not_158_out, not_159_out, not_160_out, not_161_out);
  and and_23 (and_23_out, not_162_out, not_163_out, not_164_out, not_165_out, not_166_out, not_167_out, F5, not_168_out, not_169_out, not_170_out, not_171_out, F0);
  and and_24 (and_24_out, not_172_out, not_173_out, not_174_out, not_175_out, not_176_out, not_177_out, F5, not_178_out, not_179_out, not_180_out, F1, not_181_out);
  and and_25 (and_25_out, not_182_out, not_183_out, not_184_out, not_185_out, not_186_out, not_187_out, F5, not_188_out, not_189_out, F2, not_190_out, not_191_out);
  and and_26 (and_26_out, not_192_out, not_193_out, not_194_out, not_195_out, not_196_out, not_197_out, F5, not_198_out, F3, not_199_out, F1, F0);
  and and_27 (and_27_out, not_200_out, not_201_out, OP3, not_202_out, not_203_out, not_204_out);
  and and_28 (and_28_out, not_205_out, not_206_out, OP3, OP2, not_207_out, not_208_out);
  and and_29 (and_29_out, not_209_out, not_210_out, OP3, not_211_out, not_212_out, OP0);
  and and_30 (and_30_out, OP5, not_213_out, not_214_out, not_215_out, OP1, OP0);
  and and_31 (and_31_out, OP5, not_216_out, OP3, not_217_out, OP1, OP0);
  and and_32 (and_32_out, OP5, not_218_out, OP3, not_219_out, not_220_out, OP0);
  and and_33 (and_33_out, not_221_out, not_222_out, not_223_out, not_224_out, not_225_out, not_226_out, F5, not_227_out, not_228_out, F2, not_229_out, F0);
  and and_34 (and_34_out, not_230_out, not_231_out, not_232_out, not_233_out, not_234_out, not_235_out, F5, not_236_out, not_237_out, F2, F1, F0);
  and and_35 (and_35_out, not_238_out, not_239_out, not_240_out, not_241_out, not_242_out, not_243_out, F5, not_244_out, F3, not_245_out, F1, not_246_out);
  and and_36 (and_36_out, not_247_out, not_248_out, not_249_out, not_250_out, not_251_out, not_252_out, F5, not_253_out, F3, not_254_out, F1, F0);
  and and_37 (and_37_out, not_255_out, not_256_out, OP3, not_257_out, OP1, not_258_out);
  and and_38 (and_38_out, not_259_out, not_260_out, OP3, OP2, not_261_out, OP0);
  and and_39 (and_39_out, not_262_out, not_263_out, not_264_out, not_265_out, not_266_out, not_267_out, F5, not_268_out, not_269_out, F2, F1, not_270_out);
  or or_1 (S1, and_14_out, and_15_out, and_16_out, and_17_out, and_18_out, and_19_out, and_20_out, and_21_out);
  or or_2 (S2, and_22_out, and_23_out, and_24_out, and_25_out, and_26_out, and_27_out, and_28_out, and_29_out, and_30_out, and_31_out, and_32_out);
  or or_3 (S3, and_33_out, and_34_out, and_35_out, and_36_out, and_37_out, and_38_out, and_39_out);
  or or_4 (S0, and_1_out, and_2_out, and_3_out, and_4_out, and_5_out, and_6_out, and_7_out, and_8_out, and_9_out, and_10_out, and_11_out, and_12_out, and_13_out);
endmodule

// 控制信号生成
module \控制信号生成  (
  input  OP0,
  input  OP1,
  input  OP2,
  input  OP3,
  input  OP4,
  input  OP5,
  input  F0,
  input  F1,
  input  F2,
  input  F3,
  input  F4,
  input  F5,
  input  R0,
  input  R1,
  input  R2,
  input  R3,
  input  R4,
  output MemToReg,
  output MemWrite,
  output ALU_SRC,
  output RegWrite,
  output SysCALL,
  output SignedExt,
  output RegDst,
  output BEQ,
  output BNE,
  output JR,
  output JMP,
  output JAL,
  output SH,
  output BGTZ,
  output SRLV,
  output ERET,
  output MFC0,
  output MTC0
);

  wire and_2_out, and_3_out, and_4_out, and_5_out, and_6_out, and_7_out, and_8_out, and_9_out, and_10_out,
       and_11_out, and_12_out, and_13_out, and_14_out, and_15_out, and_16_out, and_17_out, and_18_out,
       and_19_out, and_20_out, and_21_out, and_22_out, and_23_out, and_24_out, and_25_out, and_26_out,
       and_27_out, and_28_out, and_29_out, and_30_out, and_31_out, and_33_out, and_34_out, and_35_out,
       and_36_out, and_37_out, and_38_out, and_39_out, and_40_out, and_41_out, and_42_out, and_43_out,
       and_44_out, and_45_out, and_46_out, and_47_out, and_48_out, and_49_out, and_50_out, and_51_out,
       and_52_out, and_53_out, and_54_out, not_1_out, not_2_out, not_3_out, not_4_out, not_5_out, not_6_out,
       not_7_out, not_8_out, not_9_out, not_10_out, not_11_out, not_12_out, not_13_out, not_14_out,
       not_15_out, not_16_out, not_17_out, not_18_out, not_19_out, not_20_out, not_21_out, not_22_out,
       not_23_out, not_24_out, not_25_out, not_26_out, not_27_out, not_28_out, not_29_out, not_30_out,
       not_31_out, not_32_out, not_33_out, not_34_out, not_35_out, not_36_out, not_37_out, not_38_out,
       not_39_out, not_40_out, not_41_out, not_42_out, not_43_out, not_44_out, not_45_out, not_46_out,
       not_47_out, not_48_out, not_49_out, not_50_out, not_51_out, not_52_out, not_53_out, not_54_out,
       not_55_out, not_56_out, not_57_out, not_58_out, not_59_out, not_60_out, not_61_out, not_62_out,
       not_63_out, not_64_out, not_65_out, not_66_out, not_67_out, not_68_out, not_69_out, not_70_out,
       not_71_out, not_72_out, not_73_out, not_74_out, not_75_out, not_76_out, not_77_out, not_78_out,
       not_79_out, not_80_out, not_81_out, not_82_out, not_83_out, not_84_out, not_85_out, not_86_out,
       not_87_out, not_88_out, not_89_out, not_90_out, not_91_out, not_92_out, not_93_out, not_94_out,
       not_95_out, not_96_out, not_97_out, not_98_out, not_99_out, not_100_out, not_101_out, not_102_out,
       not_103_out, not_104_out, not_105_out, not_106_out, not_107_out, not_108_out, not_109_out,
       not_110_out, not_111_out, not_112_out, not_113_out, not_114_out, not_115_out, not_116_out,
       not_117_out, not_118_out, not_119_out, not_120_out, not_121_out, not_122_out, not_123_out,
       not_124_out, not_125_out, not_126_out, not_127_out, not_128_out, not_129_out, not_130_out,
       not_131_out, not_132_out, not_133_out, not_134_out, not_135_out, not_136_out, not_137_out,
       not_138_out, not_139_out, not_140_out, not_141_out, not_142_out, not_143_out, not_144_out,
       not_145_out, not_146_out, not_147_out, not_148_out, not_149_out, not_150_out, not_151_out,
       not_152_out, not_153_out, not_154_out, not_155_out, not_156_out, not_157_out, not_158_out,
       not_159_out, not_160_out, not_161_out, not_162_out, not_163_out, not_164_out, not_165_out,
       not_166_out, not_167_out, not_168_out, not_169_out, not_170_out, not_171_out, not_172_out,
       not_173_out, not_174_out, not_175_out, not_176_out, not_177_out, not_178_out, not_179_out,
       not_180_out, not_181_out, not_182_out, not_183_out, not_184_out, not_185_out, not_186_out,
       not_187_out, not_188_out, not_189_out, not_190_out, not_191_out, not_192_out, not_193_out,
       not_194_out, not_195_out, not_196_out, not_197_out, not_198_out, not_199_out, not_200_out,
       not_201_out, not_202_out, not_203_out, not_204_out, not_205_out, not_206_out, not_207_out,
       not_208_out, not_209_out, not_210_out, not_211_out, not_212_out, not_213_out, not_214_out,
       not_215_out, not_216_out, not_217_out, not_218_out, not_219_out, not_220_out, not_221_out,
       not_222_out, not_223_out, not_224_out, not_225_out, not_226_out, not_227_out, not_228_out,
       not_229_out, not_230_out, not_231_out, not_232_out, not_233_out, not_234_out, not_235_out,
       not_236_out, not_237_out, not_238_out, not_239_out, not_240_out, not_241_out, not_242_out,
       not_243_out, not_244_out, not_245_out, not_246_out, not_247_out, not_248_out, not_249_out,
       not_250_out, not_251_out, not_252_out, not_253_out, not_254_out, not_255_out, not_256_out,
       not_257_out, not_258_out, not_259_out, not_260_out, not_261_out, not_262_out, not_263_out,
       not_264_out, not_265_out, not_266_out, not_267_out, not_268_out, not_269_out, not_270_out,
       not_271_out, not_272_out, not_273_out, not_274_out, not_275_out, not_276_out, not_277_out,
       not_278_out, not_279_out, not_280_out, not_281_out, not_282_out, not_283_out, not_284_out,
       not_285_out, not_286_out, not_287_out, not_288_out, not_289_out, not_290_out, not_291_out,
       not_292_out, not_293_out, not_294_out, not_295_out, not_296_out, not_297_out, not_298_out,
       not_299_out, not_300_out, not_301_out, not_302_out, not_303_out, not_304_out, not_305_out,
       not_306_out, not_307_out, not_308_out, not_309_out, not_310_out, not_311_out, not_312_out,
       not_313_out, not_314_out, not_315_out, not_316_out, not_317_out, not_318_out, not_319_out,
       not_320_out, not_321_out, not_322_out, not_323_out, not_324_out, not_325_out, not_326_out,
       not_327_out, not_328_out, not_329_out, not_330_out, not_331_out, not_332_out, not_333_out,
       not_334_out, not_335_out, not_336_out, not_337_out, not_338_out, not_339_out, not_340_out,
       not_341_out, not_342_out, not_343_out, not_344_out, not_345_out, not_346_out, not_347_out,
       not_348_out, not_349_out, not_350_out, not_351_out, not_352_out, not_353_out, not_354_out,
       not_355_out, not_356_out, not_357_out, not_358_out, not_359_out, not_360_out, not_361_out,
       not_362_out, not_363_out, not_364_out, not_365_out, not_366_out, not_367_out, not_368_out,
       not_369_out, not_370_out, not_371_out, not_372_out, not_373_out, not_374_out, not_375_out,
       not_376_out, not_377_out, not_378_out, not_379_out, not_380_out, not_381_out, not_382_out,
       not_383_out, not_384_out, not_385_out, not_386_out, not_387_out, not_388_out, not_389_out,
       not_390_out, not_391_out, not_392_out, not_393_out, not_394_out, not_395_out, not_396_out,
       not_397_out, not_398_out, not_399_out, not_400_out, not_401_out, not_402_out, not_403_out,
       not_404_out, not_405_out, not_406_out, not_407_out, not_408_out, not_409_out, not_410_out,
       not_411_out, not_412_out, not_413_out, not_414_out, not_415_out, not_416_out, not_417_out,
       not_418_out, not_419_out, not_420_out, not_421_out, not_422_out, not_423_out, not_424_out,
       not_425_out, not_426_out, not_427_out, not_428_out, not_429_out, not_430_out, not_431_out,
       not_432_out, not_433_out;

  not not_1 (not_1_out, OP4);
  not not_2 (not_2_out, OP3);
  not not_3 (not_3_out, OP2);
  not not_4 (not_4_out, OP4);
  not not_5 (not_5_out, OP2);
  not not_6 (not_6_out, OP4);
  not not_7 (not_7_out, OP2);
  not not_8 (not_8_out, OP1);
  not not_9 (not_9_out, OP5);
  not not_10 (not_10_out, OP4);
  not not_11 (not_11_out, OP2);
  not not_12 (not_12_out, OP1);
  not not_13 (not_13_out, OP0);
  not not_14 (not_14_out, OP5);
  not not_15 (not_15_out, OP4);
  not not_16 (not_16_out, OP1);
  not not_17 (not_17_out, OP0);
  not not_18 (not_18_out, OP5);
  not not_19 (not_19_out, OP4);
  not not_20 (not_20_out, OP2);
  not not_21 (not_21_out, OP1);
  not not_22 (not_22_out, OP5);
  not not_23 (not_23_out, OP4);
  not not_24 (not_24_out, OP2);
  not not_25 (not_25_out, OP0);
  not not_26 (not_26_out, OP5);
  not not_27 (not_27_out, OP4);
  not not_28 (not_28_out, OP1);
  not not_29 (not_29_out, OP4);
  not not_30 (not_30_out, OP3);
  not not_31 (not_31_out, OP2);
  not not_32 (not_32_out, OP4);
  not not_33 (not_33_out, OP2);
  not not_34 (not_34_out, OP4);
  not not_35 (not_35_out, OP2);
  not not_36 (not_36_out, OP1);
  not not_37 (not_37_out, OP5);
  not not_38 (not_38_out, OP4);
  not not_39 (not_39_out, OP3);
  not not_40 (not_40_out, OP2);
  not not_41 (not_41_out, OP1);
  not not_42 (not_42_out, OP0);
  not not_43 (not_43_out, F5);
  not not_44 (not_44_out, F4);
  not not_45 (not_45_out, F3);
  not not_46 (not_46_out, F2);
  not not_47 (not_47_out, F1);
  not not_48 (not_48_out, F0);
  not not_49 (not_49_out, OP5);
  not not_50 (not_50_out, OP4);
  not not_51 (not_51_out, OP3);
  not not_52 (not_52_out, OP2);
  not not_53 (not_53_out, OP1);
  not not_54 (not_54_out, OP0);
  not not_55 (not_55_out, F5);
  not not_56 (not_56_out, F4);
  not not_57 (not_57_out, F3);
  not not_58 (not_58_out, F2);
  not not_59 (not_59_out, OP5);
  not not_60 (not_60_out, OP4);
  not not_61 (not_61_out, OP3);
  not not_62 (not_62_out, OP2);
  not not_63 (not_63_out, OP1);
  not not_64 (not_64_out, OP0);
  not not_65 (not_65_out, F5);
  not not_66 (not_66_out, F4);
  not not_67 (not_67_out, F3);
  not not_68 (not_68_out, F2);
  not not_69 (not_69_out, F0);
  not not_70 (not_70_out, OP5);
  not not_71 (not_71_out, OP4);
  not not_72 (not_72_out, OP3);
  not not_73 (not_73_out, OP2);
  not not_74 (not_74_out, OP1);
  not not_75 (not_75_out, OP0);
  not not_76 (not_76_out, F4);
  not not_77 (not_77_out, F3);
  not not_78 (not_78_out, F2);
  not not_79 (not_79_out, F1);
  not not_80 (not_80_out, F0);
  not not_81 (not_81_out, OP5);
  not not_82 (not_82_out, OP4);
  not not_83 (not_83_out, OP3);
  not not_84 (not_84_out, OP2);
  not not_85 (not_85_out, OP1);
  not not_86 (not_86_out, OP0);
  not not_87 (not_87_out, F4);
  not not_88 (not_88_out, F3);
  not not_89 (not_89_out, F2);
  not not_90 (not_90_out, F1);
  not not_91 (not_91_out, OP5);
  not not_92 (not_92_out, OP4);
  not not_93 (not_93_out, OP3);
  not not_94 (not_94_out, OP2);
  not not_95 (not_95_out, OP1);
  not not_96 (not_96_out, OP0);
  not not_97 (not_97_out, F4);
  not not_98 (not_98_out, F3);
  not not_99 (not_99_out, F2);
  not not_100 (not_100_out, F0);
  not not_101 (not_101_out, OP5);
  not not_102 (not_102_out, OP4);
  not not_103 (not_103_out, OP3);
  not not_104 (not_104_out, OP2);
  not not_105 (not_105_out, OP1);
  not not_106 (not_106_out, OP0);
  not not_107 (not_107_out, F4);
  not not_108 (not_108_out, F3);
  not not_109 (not_109_out, F1);
  not not_110 (not_110_out, F0);
  not not_111 (not_111_out, OP5);
  not not_112 (not_112_out, OP4);
  not not_113 (not_113_out, OP3);
  not not_114 (not_114_out, OP2);
  not not_115 (not_115_out, OP1);
  not not_116 (not_116_out, OP0);
  not not_117 (not_117_out, F4);
  not not_118 (not_118_out, F3);
  not not_119 (not_119_out, F1);
  not not_120 (not_120_out, OP5);
  not not_121 (not_121_out, OP4);
  not not_122 (not_122_out, OP3);
  not not_123 (not_123_out, OP2);
  not not_124 (not_124_out, OP1);
  not not_125 (not_125_out, OP0);
  not not_126 (not_126_out, F4);
  not not_127 (not_127_out, F3);
  not not_128 (not_128_out, OP5);
  not not_129 (not_129_out, OP4);
  not not_130 (not_130_out, OP3);
  not not_131 (not_131_out, OP2);
  not not_132 (not_132_out, OP1);
  not not_133 (not_133_out, OP0);
  not not_134 (not_134_out, F4);
  not not_135 (not_135_out, F2);
  not not_136 (not_136_out, F0);
  not not_137 (not_137_out, OP5);
  not not_138 (not_138_out, OP4);
  not not_139 (not_139_out, OP3);
  not not_140 (not_140_out, OP2);
  not not_141 (not_141_out, OP1);
  not not_142 (not_142_out, OP0);
  not not_143 (not_143_out, F4);
  not not_144 (not_144_out, F2);
  not not_145 (not_145_out, OP5);
  not not_146 (not_146_out, OP4);
  not not_147 (not_147_out, OP3);
  not not_148 (not_148_out, OP2);
  not not_149 (not_149_out, OP5);
  not not_150 (not_150_out, OP4);
  not not_151 (not_151_out, OP2);
  not not_152 (not_152_out, OP1);
  not not_153 (not_153_out, OP0);
  not not_154 (not_154_out, OP5);
  not not_155 (not_155_out, OP4);
  not not_156 (not_156_out, OP1);
  not not_157 (not_157_out, OP0);
  not not_158 (not_158_out, OP5);
  not not_159 (not_159_out, OP4);
  not not_160 (not_160_out, OP2);
  not not_161 (not_161_out, OP1);
  not not_162 (not_162_out, OP5);
  not not_163 (not_163_out, OP4);
  not not_164 (not_164_out, OP2);
  not not_165 (not_165_out, OP0);
  not not_166 (not_166_out, OP5);
  not not_167 (not_167_out, OP4);
  not not_168 (not_168_out, OP1);
  not not_169 (not_169_out, OP4);
  not not_170 (not_170_out, OP3);
  not not_171 (not_171_out, OP2);
  not not_172 (not_172_out, OP5);
  not not_173 (not_173_out, OP4);
  not not_174 (not_174_out, OP3);
  not not_175 (not_175_out, OP2);
  not not_176 (not_176_out, OP1);
  not not_177 (not_177_out, OP0);
  not not_178 (not_178_out, F5);
  not not_179 (not_179_out, F4);
  not not_180 (not_180_out, F3);
  not not_181 (not_181_out, F0);
  not not_182 (not_182_out, OP5);
  not not_183 (not_183_out, OP4);
  not not_184 (not_184_out, OP3);
  not not_185 (not_185_out, OP2);
  not not_186 (not_186_out, OP1);
  not not_187 (not_187_out, OP0);
  not not_188 (not_188_out, F4);
  not not_189 (not_189_out, F3);
  not not_190 (not_190_out, F0);
  not not_191 (not_191_out, OP5);
  not not_192 (not_192_out, OP4);
  not not_193 (not_193_out, OP3);
  not not_194 (not_194_out, OP2);
  not not_195 (not_195_out, OP1);
  not not_196 (not_196_out, OP0);
  not not_197 (not_197_out, F5);
  not not_198 (not_198_out, F4);
  not not_199 (not_199_out, F1);
  not not_200 (not_200_out, F0);
  not not_201 (not_201_out, OP5);
  not not_202 (not_202_out, OP4);
  not not_203 (not_203_out, OP3);
  not not_204 (not_204_out, OP1);
  not not_205 (not_205_out, OP0);
  not not_206 (not_206_out, OP5);
  not not_207 (not_207_out, OP4);
  not not_208 (not_208_out, OP3);
  not not_209 (not_209_out, OP1);
  not not_210 (not_210_out, OP5);
  not not_211 (not_211_out, OP4);
  not not_212 (not_212_out, OP2);
  not not_213 (not_213_out, OP1);
  not not_214 (not_214_out, OP0);
  not not_215 (not_215_out, OP5);
  not not_216 (not_216_out, OP4);
  not not_217 (not_217_out, OP2);
  not not_218 (not_218_out, OP1);
  not not_219 (not_219_out, OP5);
  not not_220 (not_220_out, OP4);
  not not_221 (not_221_out, OP2);
  not not_222 (not_222_out, OP0);
  not not_223 (not_223_out, OP4);
  not not_224 (not_224_out, OP3);
  not not_225 (not_225_out, OP2);
  not not_226 (not_226_out, OP4);
  not not_227 (not_227_out, OP2);
  not not_228 (not_228_out, OP4);
  not not_229 (not_229_out, OP2);
  not not_230 (not_230_out, OP1);
  not not_231 (not_231_out, OP5);
  not not_232 (not_232_out, OP4);
  not not_233 (not_233_out, OP3);
  not not_234 (not_234_out, OP5);
  not not_235 (not_235_out, OP4);
  not not_236 (not_236_out, OP3);
  not not_237 (not_237_out, OP2);
  not not_238 (not_238_out, OP1);
  not not_239 (not_239_out, OP0);
  not not_240 (not_240_out, F5);
  not not_241 (not_241_out, F4);
  not not_242 (not_242_out, F3);
  not not_243 (not_243_out, F2);
  not not_244 (not_244_out, F1);
  not not_245 (not_245_out, F0);
  not not_246 (not_246_out, OP5);
  not not_247 (not_247_out, OP4);
  not not_248 (not_248_out, OP3);
  not not_249 (not_249_out, OP2);
  not not_250 (not_250_out, OP1);
  not not_251 (not_251_out, OP0);
  not not_252 (not_252_out, F5);
  not not_253 (not_253_out, F4);
  not not_254 (not_254_out, F3);
  not not_255 (not_255_out, F2);
  not not_256 (not_256_out, OP5);
  not not_257 (not_257_out, OP4);
  not not_258 (not_258_out, OP3);
  not not_259 (not_259_out, OP2);
  not not_260 (not_260_out, OP1);
  not not_261 (not_261_out, OP0);
  not not_262 (not_262_out, F5);
  not not_263 (not_263_out, F4);
  not not_264 (not_264_out, F3);
  not not_265 (not_265_out, F2);
  not not_266 (not_266_out, F0);
  not not_267 (not_267_out, OP5);
  not not_268 (not_268_out, OP4);
  not not_269 (not_269_out, OP3);
  not not_270 (not_270_out, OP2);
  not not_271 (not_271_out, OP1);
  not not_272 (not_272_out, OP0);
  not not_273 (not_273_out, F4);
  not not_274 (not_274_out, F3);
  not not_275 (not_275_out, F2);
  not not_276 (not_276_out, F1);
  not not_277 (not_277_out, F0);
  not not_278 (not_278_out, OP5);
  not not_279 (not_279_out, OP4);
  not not_280 (not_280_out, OP3);
  not not_281 (not_281_out, OP2);
  not not_282 (not_282_out, OP1);
  not not_283 (not_283_out, OP0);
  not not_284 (not_284_out, F4);
  not not_285 (not_285_out, F3);
  not not_286 (not_286_out, F2);
  not not_287 (not_287_out, F1);
  not not_288 (not_288_out, OP5);
  not not_289 (not_289_out, OP4);
  not not_290 (not_290_out, OP3);
  not not_291 (not_291_out, OP2);
  not not_292 (not_292_out, OP1);
  not not_293 (not_293_out, OP0);
  not not_294 (not_294_out, F4);
  not not_295 (not_295_out, F3);
  not not_296 (not_296_out, F2);
  not not_297 (not_297_out, F0);
  not not_298 (not_298_out, OP5);
  not not_299 (not_299_out, OP4);
  not not_300 (not_300_out, OP3);
  not not_301 (not_301_out, OP2);
  not not_302 (not_302_out, OP1);
  not not_303 (not_303_out, OP0);
  not not_304 (not_304_out, F4);
  not not_305 (not_305_out, F3);
  not not_306 (not_306_out, F1);
  not not_307 (not_307_out, F0);
  not not_308 (not_308_out, OP5);
  not not_309 (not_309_out, OP4);
  not not_310 (not_310_out, OP3);
  not not_311 (not_311_out, OP2);
  not not_312 (not_312_out, OP1);
  not not_313 (not_313_out, OP0);
  not not_314 (not_314_out, F4);
  not not_315 (not_315_out, F3);
  not not_316 (not_316_out, F1);
  not not_317 (not_317_out, OP5);
  not not_318 (not_318_out, OP4);
  not not_319 (not_319_out, OP3);
  not not_320 (not_320_out, OP2);
  not not_321 (not_321_out, OP1);
  not not_322 (not_322_out, OP0);
  not not_323 (not_323_out, F4);
  not not_324 (not_324_out, F3);
  not not_325 (not_325_out, OP5);
  not not_326 (not_326_out, OP4);
  not not_327 (not_327_out, OP3);
  not not_328 (not_328_out, OP2);
  not not_329 (not_329_out, OP1);
  not not_330 (not_330_out, OP0);
  not not_331 (not_331_out, F4);
  not not_332 (not_332_out, F2);
  not not_333 (not_333_out, F0);
  not not_334 (not_334_out, OP5);
  not not_335 (not_335_out, OP4);
  not not_336 (not_336_out, OP3);
  not not_337 (not_337_out, OP2);
  not not_338 (not_338_out, OP1);
  not not_339 (not_339_out, OP0);
  not not_340 (not_340_out, F4);
  not not_341 (not_341_out, F2);
  not not_342 (not_342_out, OP5);
  not not_343 (not_343_out, OP4);
  not not_344 (not_344_out, OP3);
  not not_345 (not_345_out, OP2);
  not not_346 (not_346_out, OP1);
  not not_347 (not_347_out, OP0);
  not not_348 (not_348_out, F5);
  not not_349 (not_349_out, F4);
  not not_350 (not_350_out, F3);
  not not_351 (not_351_out, F0);
  not not_352 (not_352_out, OP5);
  not not_353 (not_353_out, OP4);
  not not_354 (not_354_out, OP3);
  not not_355 (not_355_out, OP2);
  not not_356 (not_356_out, OP1);
  not not_357 (not_357_out, OP0);
  not not_358 (not_358_out, F4);
  not not_359 (not_359_out, F3);
  not not_360 (not_360_out, F0);
  not not_361 (not_361_out, OP5);
  not not_362 (not_362_out, OP4);
  not not_363 (not_363_out, OP3);
  not not_364 (not_364_out, OP1);
  not not_365 (not_365_out, OP0);
  not not_366 (not_366_out, OP5);
  not not_367 (not_367_out, OP4);
  not not_368 (not_368_out, OP3);
  not not_369 (not_369_out, OP1);
  not not_370 (not_370_out, OP5);
  not not_371 (not_371_out, OP4);
  not not_372 (not_372_out, OP3);
  not not_373 (not_373_out, OP2);
  not not_374 (not_374_out, OP1);
  not not_375 (not_375_out, OP0);
  not not_376 (not_376_out, F5);
  not not_377 (not_377_out, F4);
  not not_378 (not_378_out, F2);
  not not_379 (not_379_out, F1);
  not not_380 (not_380_out, F0);
  not not_381 (not_381_out, OP5);
  not not_382 (not_382_out, OP4);
  not not_383 (not_383_out, OP3);
  not not_384 (not_384_out, OP2);
  not not_385 (not_385_out, OP0);
  not not_386 (not_386_out, OP5);
  not not_387 (not_387_out, OP4);
  not not_388 (not_388_out, OP3);
  not not_389 (not_389_out, OP2);
  not not_390 (not_390_out, OP1);
  not not_391 (not_391_out, OP2);
  not not_392 (not_392_out, OP4);
  not not_393 (not_393_out, OP3);
  not not_394 (not_394_out, OP4);
  not not_395 (not_395_out, OP5);
  not not_396 (not_396_out, OP0);
  not not_397 (not_397_out, OP1);
  not not_398 (not_398_out, OP2);
  not not_399 (not_399_out, OP3);
  not not_400 (not_400_out, OP4);
  not not_401 (not_401_out, OP5);
  not not_402 (not_402_out, F0);
  not not_403 (not_403_out, F3);
  not not_404 (not_404_out, F4);
  not not_405 (not_405_out, F5);
  not not_406 (not_406_out, OP0);
  not not_407 (not_407_out, OP1);
  not not_408 (not_408_out, OP2);
  not not_409 (not_409_out, OP3);
  not not_410 (not_410_out, OP5);
  not not_411 (not_411_out, F0);
  not not_412 (not_412_out, F1);
  not not_413 (not_413_out, F2);
  not not_414 (not_414_out, F5);
  not not_415 (not_415_out, OP0);
  not not_416 (not_416_out, OP1);
  not not_417 (not_417_out, OP2);
  not not_418 (not_418_out, OP3);
  not not_419 (not_419_out, OP5);
  not not_420 (not_420_out, R0);
  not not_421 (not_421_out, R1);
  not not_422 (not_422_out, R2);
  not not_423 (not_423_out, R3);
  not not_424 (not_424_out, R4);
  not not_425 (not_425_out, OP0);
  not not_426 (not_426_out, OP1);
  not not_427 (not_427_out, OP2);
  not not_428 (not_428_out, OP3);
  not not_429 (not_429_out, OP5);
  not not_430 (not_430_out, R0);
  not not_431 (not_431_out, R1);
  not not_432 (not_432_out, R3);
  not not_433 (not_433_out, R4);
  and and_1 (MemToReg, OP5, not_1_out, not_2_out, not_3_out, OP1, OP0);
  and and_2 (and_2_out, OP5, not_4_out, OP3, not_5_out, OP1, OP0);
  and and_3 (and_3_out, OP5, not_6_out, OP3, not_7_out, not_8_out, OP0);
  and and_4 (and_4_out, not_9_out, not_10_out, OP3, not_11_out, not_12_out, not_13_out);
  and and_5 (and_5_out, not_14_out, not_15_out, OP3, OP2, not_16_out, not_17_out);
  and and_6 (and_6_out, not_18_out, not_19_out, OP3, not_20_out, not_21_out, OP0);
  and and_7 (and_7_out, not_22_out, not_23_out, OP3, not_24_out, OP1, not_25_out);
  and and_8 (and_8_out, not_26_out, not_27_out, OP3, OP2, not_28_out, OP0);
  and and_9 (and_9_out, OP5, not_29_out, not_30_out, not_31_out, OP1, OP0);
  and and_10 (and_10_out, OP5, not_32_out, OP3, not_33_out, OP1, OP0);
  and and_11 (and_11_out, OP5, not_34_out, OP3, not_35_out, not_36_out, OP0);
  and and_12 (and_12_out, not_37_out, not_38_out, not_39_out, not_40_out, not_41_out, not_42_out, not_43_out, not_44_out, not_45_out, not_46_out, not_47_out, not_48_out);
  and and_13 (and_13_out, not_49_out, not_50_out, not_51_out, not_52_out, not_53_out, not_54_out, not_55_out, not_56_out, not_57_out, not_58_out, F1, F0);
  and and_14 (and_14_out, not_59_out, not_60_out, not_61_out, not_62_out, not_63_out, not_64_out, not_65_out, not_66_out, not_67_out, not_68_out, F1, not_69_out);
  and and_15 (and_15_out, not_70_out, not_71_out, not_72_out, not_73_out, not_74_out, not_75_out, F5, not_76_out, not_77_out, not_78_out, not_79_out, not_80_out);
  and and_16 (and_16_out, not_81_out, not_82_out, not_83_out, not_84_out, not_85_out, not_86_out, F5, not_87_out, not_88_out, not_89_out, not_90_out, F0);
  and and_17 (and_17_out, not_91_out, not_92_out, not_93_out, not_94_out, not_95_out, not_96_out, F5, not_97_out, not_98_out, not_99_out, F1, not_100_out);
  and and_18 (and_18_out, not_101_out, not_102_out, not_103_out, not_104_out, not_105_out, not_106_out, F5, not_107_out, not_108_out, F2, not_109_out, not_110_out);
  and and_19 (and_19_out, not_111_out, not_112_out, not_113_out, not_114_out, not_115_out, not_116_out, F5, not_117_out, not_118_out, F2, not_119_out, F0);
  and and_20 (and_20_out, not_120_out, not_121_out, not_122_out, not_123_out, not_124_out, not_125_out, F5, not_126_out, not_127_out, F2, F1, F0);
  and and_21 (and_21_out, not_128_out, not_129_out, not_130_out, not_131_out, not_132_out, not_133_out, F5, not_134_out, F3, not_135_out, F1, not_136_out);
  and and_22 (and_22_out, not_137_out, not_138_out, not_139_out, not_140_out, not_141_out, not_142_out, F5, not_143_out, F3, not_144_out, F1, F0);
  and and_23 (and_23_out, not_145_out, not_146_out, not_147_out, not_148_out, OP1, OP0);
  and and_24 (and_24_out, not_149_out, not_150_out, OP3, not_151_out, not_152_out, not_153_out);
  and and_25 (and_25_out, not_154_out, not_155_out, OP3, OP2, not_156_out, not_157_out);
  and and_26 (and_26_out, not_158_out, not_159_out, OP3, not_160_out, not_161_out, OP0);
  and and_27 (and_27_out, not_162_out, not_163_out, OP3, not_164_out, OP1, not_165_out);
  and and_28 (and_28_out, not_166_out, not_167_out, OP3, OP2, not_168_out, OP0);
  and and_29 (and_29_out, OP5, not_169_out, not_170_out, not_171_out, OP1, OP0);
  and and_30 (and_30_out, not_172_out, not_173_out, not_174_out, not_175_out, not_176_out, not_177_out, not_178_out, not_179_out, not_180_out, F2, F1, not_181_out);
  and and_31 (and_31_out, not_182_out, not_183_out, not_184_out, not_185_out, not_186_out, not_187_out, F5, not_188_out, not_189_out, F2, F1, not_190_out);
  and and_32 (SysCALL, not_191_out, not_192_out, not_193_out, not_194_out, not_195_out, not_196_out, not_197_out, not_198_out, F3, F2, not_199_out, not_200_out);
  and and_33 (and_33_out, not_201_out, not_202_out, not_203_out, OP2, not_204_out, not_205_out);
  and and_34 (and_34_out, not_206_out, not_207_out, not_208_out, OP2, not_209_out, OP0);
  and and_35 (and_35_out, not_210_out, not_211_out, OP3, not_212_out, not_213_out, not_214_out);
  and and_36 (and_36_out, not_215_out, not_216_out, OP3, not_217_out, not_218_out, OP0);
  and and_37 (and_37_out, not_219_out, not_220_out, OP3, not_221_out, OP1, not_222_out);
  and and_38 (and_38_out, OP5, not_223_out, not_224_out, not_225_out, OP1, OP0);
  and and_39 (and_39_out, OP5, not_226_out, OP3, not_227_out, OP1, OP0);
  and and_40 (and_40_out, OP5, not_228_out, OP3, not_229_out, not_230_out, OP0);
  and and_41 (and_41_out, not_231_out, not_232_out, not_233_out, OP2, OP1, OP0);
  and and_42 (and_42_out, not_234_out, not_235_out, not_236_out, not_237_out, not_238_out, not_239_out, not_240_out, not_241_out, not_242_out, not_243_out, not_244_out, not_245_out);
  and and_43 (and_43_out, not_246_out, not_247_out, not_248_out, not_249_out, not_250_out, not_251_out, not_252_out, not_253_out, not_254_out, not_255_out, F1, F0);
  and and_44 (and_44_out, not_256_out, not_257_out, not_258_out, not_259_out, not_260_out, not_261_out, not_262_out, not_263_out, not_264_out, not_265_out, F1, not_266_out);
  and and_45 (and_45_out, not_267_out, not_268_out, not_269_out, not_270_out, not_271_out, not_272_out, F5, not_273_out, not_274_out, not_275_out, not_276_out, not_277_out);
  and and_46 (and_46_out, not_278_out, not_279_out, not_280_out, not_281_out, not_282_out, not_283_out, F5, not_284_out, not_285_out, not_286_out, not_287_out, F0);
  and and_47 (and_47_out, not_288_out, not_289_out, not_290_out, not_291_out, not_292_out, not_293_out, F5, not_294_out, not_295_out, not_296_out, F1, not_297_out);
  and and_48 (and_48_out, not_298_out, not_299_out, not_300_out, not_301_out, not_302_out, not_303_out, F5, not_304_out, not_305_out, F2, not_306_out, not_307_out);
  and and_49 (and_49_out, not_308_out, not_309_out, not_310_out, not_311_out, not_312_out, not_313_out, F5, not_314_out, not_315_out, F2, not_316_out, F0);
  and and_50 (and_50_out, not_317_out, not_318_out, not_319_out, not_320_out, not_321_out, not_322_out, F5, not_323_out, not_324_out, F2, F1, F0);
  and and_51 (and_51_out, not_325_out, not_326_out, not_327_out, not_328_out, not_329_out, not_330_out, F5, not_331_out, F3, not_332_out, F1, not_333_out);
  and and_52 (and_52_out, not_334_out, not_335_out, not_336_out, not_337_out, not_338_out, not_339_out, F5, not_340_out, F3, not_341_out, F1, F0);
  and and_53 (and_53_out, not_342_out, not_343_out, not_344_out, not_345_out, not_346_out, not_347_out, not_348_out, not_349_out, not_350_out, F2, F1, not_351_out);
  and and_54 (and_54_out, not_352_out, not_353_out, not_354_out, not_355_out, not_356_out, not_357_out, F5, not_358_out, not_359_out, F2, F1, not_360_out);
  and and_55 (BEQ, not_361_out, not_362_out, not_363_out, OP2, not_364_out, not_365_out);
  and and_56 (BNE, not_366_out, not_367_out, not_368_out, OP2, not_369_out, OP0);
  and and_57 (JR, not_370_out, not_371_out, not_372_out, not_373_out, not_374_out, not_375_out, not_376_out, not_377_out, F3, not_378_out, not_379_out, not_380_out);
  and and_58 (JMP, not_381_out, not_382_out, not_383_out, not_384_out, OP1, not_385_out);
  and and_59 (JAL, not_386_out, not_387_out, not_388_out, not_389_out, OP1, OP0);
  and and_60 (SH, OP0, not_390_out, not_391_out, OP3, not_392_out, OP5);
  and and_61 (BGTZ, OP0, OP1, OP2, not_393_out, not_394_out, not_395_out);
  and and_62 (SRLV, not_396_out, not_397_out, not_398_out, not_399_out, not_400_out, not_401_out, not_402_out, F1, F2, not_403_out, not_404_out, not_405_out);
  and and_63 (ERET, not_406_out, not_407_out, not_408_out, not_409_out, OP4, not_410_out, not_411_out, not_412_out, not_413_out, F3, F4, not_414_out);
  and and_64 (MFC0, not_415_out, not_416_out, not_417_out, not_418_out, OP4, not_419_out, not_420_out, not_421_out, not_422_out, not_423_out, not_424_out);
  and and_65 (MTC0, not_425_out, not_426_out, not_427_out, not_428_out, OP4, not_429_out, not_430_out, not_431_out, R2, not_432_out, not_433_out);
  or or_1 (MemWrite, and_2_out, and_3_out);
  or or_2 (ALU_SRC, and_4_out, and_5_out, and_6_out, and_7_out, and_8_out, and_9_out, and_10_out, and_11_out);
  or or_3 (SignedExt, and_33_out, and_34_out, and_35_out, and_36_out, and_37_out, and_38_out, and_39_out, and_40_out, and_41_out);
  or or_4 (RegWrite, and_12_out, and_13_out, and_14_out, and_15_out, and_16_out, and_17_out, and_18_out, and_19_out, and_20_out, and_21_out, and_22_out, and_23_out, and_24_out, and_25_out, and_26_out, and_27_out, and_28_out, and_29_out, and_30_out, and_31_out);
  or or_5 (RegDst, and_42_out, and_43_out, and_44_out, and_45_out, and_46_out, and_47_out, and_48_out, and_49_out, and_50_out, and_51_out, and_52_out, and_53_out, and_54_out);
endmodule

// ALU
module MIPS_ALU (
  input  [4:0] shamt,
  input  [31:0] X,
  input  [31:0] Y,
  input  [3:0] AluOP,
  output Equal,
  output [31:0] Result,
  output [31:0] Result_2
);

  wire [0:0] comparator_1_lt, comparator_2_lt;
  wire [31:0] adder_1_out, AND_out, divider_1_out, divider_1_rem, multiplier_1_cout, multiplier_1_out,
       NOR_out, OR_out, shifter_1_out, shifter_2_out, shifter_3_out, subtractor_1_out, XOR_out;

  assign AND_out = X & Y;  // AND_Gate AND, 32 bits wide
  assign OR_out = X | Y;  // OR_Gate OR, 32 bits wide
  Shifter #(.width(32)) shifter_1 (.in(Y), .\dist (shamt), .out(shifter_1_out));
  Shifter #(.width(32), .shift("ar")) shifter_2 (.in(Y), .\dist (shamt), .out(shifter_2_out));
  Shifter #(.width(32), .shift("lr")) shifter_3 (.in(Y), .\dist (shamt), .out(shifter_3_out));
  Multiplier #(.width(32)) multiplier_1 (.a(X), .b(Y), .out(multiplier_1_out), .cout(multiplier_1_cout));  // open: cin
  Divider #(.width(32)) divider_1 (.a(X), .b(Y), .out(divider_1_out), .rem(divider_1_rem));  // open: upper
  Adder #(.width(32)) adder_1 (.a(X), .b(Y), .out(adder_1_out));  // open: cin, cout
  Subtractor #(.width(32)) subtractor_1 (.a(X), .b(Y), .out(subtractor_1_out));  // open: bin, bout
  assign XOR_out = X ^ Y;  // XOR_Gate XOR, 32 bits wide
  assign NOR_out = ~(X | Y);  // NOR_Gate NOR, 32 bits wide
  Comparator #(.width(32)) comparator_1 (.a(X), .b(Y), .eq(Equal), .lt(comparator_1_lt[0]));  // open: gt
  Comparator #(.width(32), .mode("unsigned")) comparator_2 (.a(X), .b(Y), .lt(comparator_2_lt[0]));  // open: gt, eq
  Multiplexer #(.select(4), .width(32), .enable("false")) multiplexer_1 (
    .in0(shifter_1_out), .in1(shifter_2_out), .in2(shifter_3_out), .in3(multiplier_1_out),
    .in4(divider_1_out), .in5(adder_1_out), .in6(subtractor_1_out), .in7(AND_out), .in8(OR_out),
    .in9(XOR_out), .in10(NOR_out), .in11({{31{1'b0}}, comparator_1_lt[0]}),
    .in12({{31{1'b0}}, comparator_2_lt[0]}), .in13({32{1'b0}}), .in14({32{1'b0}}), .in15({32{1'b0}}),
    .out(Result), .sel(AluOP));
  Multiplexer #(.select(4), .width(32), .enable("false")) multiplexer_2 (
    .in0({32{1'b0}}), .in1({32{1'b0}}), .in2({32{1'b0}}), .in3(multiplier_1_cout), .in4(divider_1_rem),
    .in5({32{1'b0}}), .in6({32{1'b0}}), .in7({32{1'b0}}), .in8({32{1'b0}}), .in9({32{1'b0}}),
    .in10({32{1'b0}}), .in11({32{1'b0}}), .in12({32{1'b0}}), .in13({32{1'b0}}), .in14({32{1'b0}}),
    .in15({32{1'b0}}), .out(Result_2), .sel(AluOP));

  // Other names for the same wires on the sheet: Result2[31:0] = Result_2; S[3:0] = AluOP

  // Notes on the sheet:
  //   不要改变此引脚区域内容，也不要改变ALU封装形式
  //   输入引脚
  //   输出引脚
endmodule

module MIPS_Regifile (
  input  [31:0] Din,
  input  Clk,
  input  WE,
  input  [4:0] R1_num,
  input  [4:0] W_num,
  input  [4:0] R2_num,
  output [31:0] R1,
  output [31:0] R2
);

  // RegisterFile registerfile_1: pin names not known; wires that end beside it: Din, Clk, WE, W_num, R1_num, R2_num, R1, R2
endmodule

module \理想流水线  (
);

  wire and_1_out, and_2_out, and_4_out, and_5_out, and_6_out, and_7_out, and_8_out, and_9_out, CLK,
       comparator_1_eq, comparator_2_eq, comparator_3_gt, Equ, ex_mem_1_halt_2, Go, halt, id_ex_1_halt_2,
       IR1, IR2, IR3, JAL, Jump, not_1_out, not_2_out, not_3_out, not_4_out, not_5_out, or_4_out, regDst,
       RST, stall, syscall, W1, W2, W3, \硬布线控制器_1_signedext ;
  wire [1:1] \硬布线控制器_1_regwrite ;
  wire [2:0] ex_mem_1_memout, id_ex_1_memout, or_1_out, \硬布线控制器_1_memwrite ;
  wire [3:0] multiplexer_10_out, multiplexer_11_out, \硬布线控制器_1_alu_op ;
  wire [4:0] multiplexer_3_out, multiplexer_4_out, multiplexer_5_out, multiplexer_8_out, rW, \硬布线控制器_1_jmp ;
  wire [5:0] id_ex_1_exout, id_ex_1_ifout;
  wire [5:4] \硬布线控制器_1_alu_src ;
  wire [7:0] counter_1_q, ex_mem_1_wbout, id_ex_1_wbout, mem_wb_1_wbout;
  wire [15:0] \LoadUse次数 , \总周期数 , \插入气泡数 , \无条件分支数 , \条件分支成功数 ;
  wire [25:0] id_ex_1_jofout;
  wire [31:0] adder_1_out, adder_2_out, ex_mem_1_r2out, ex_mem_1_resout, EX_PC, id_ex_1_r1out, id_ex_1_r2out,
       ID_PC, if_id_1_insout, IF_PC, LedData, MEM_PC, mem_wb_1_memout, mem_wb_1_resout, mips_alu_1_result,
       mips_ram_1_p2, mips_ram_1_p8, multiplexer_1_out, multiplexer_2_out, multiplexer_7_out,
       multiplexer_9_out, multiplexer_13_out, R1, R2, registerfile_1_p2, registerfile_1_p10, rom_1_data,
       shifter_1_out, shifter_2_out, shifter_3_out, WB_PC;

  Button \u_总复位  (.out(RST));
  Button _1 (.out(IR1));
  Button _2 (.out(IR2));
  Button _3 (.out(IR3));
  not not_1 (not_1_out, halt);
  Button \u_继续运行  (.out(Go));
  LED led_1 (.in(W1));
  LED led_2 (.in(W2));
  LED led_3 (.in(W3));
  Register #(.width(32), .trigger("falling")) PC (
    .D(multiplexer_1_out), .en(not_1_out), .Q(IF_PC), .clk(CLK), .clr(RST));
  Adder #(.width(32)) adder_1 (.a(IF_PC), .b(32'h4), .out(adder_1_out));  // open: cin, cout
  Multiplexer #(.width(32), .enable("false")) multiplexer_1 (
    .in0(adder_1_out), .in1(multiplexer_9_out), .out(multiplexer_1_out), .sel(Jump));
  Counter counter_1 (.count(Go), .Q(counter_1_q), .clk(CLK), .clr(and_1_out));  // open: load, D, carry
  and and_1 (and_1_out, syscall, not_2_out);
  not not_2 (not_2_out, Go);
  Hex_Digit_Display hex_digit_display_1 (.value(LedData[31:28]));  // open: dp
  IF_ID if_id_1 (
    .Insin(rom_1_data), .PCin(adder_1_out), .CLK(CLK), .Insout(if_id_1_insout), .PCout(ID_PC),
    .\使能端_低电平有效_stall_高电平有效 (halt), .\异步清零 (RST));  // open: 同步清零_气泡_高电平有效, PJIn, PJOut
  ROM #(.addrWidth(10), .dataWidth(32)) rom_1 (.addr(IF_PC[11:2]), .data(rom_1_data), .sel(1'b1));
  Comparator #(.width(32)) comparator_1 (.a(R1), .b(32'h22), .eq(comparator_1_eq));  // open: gt, lt
  Comparator comparator_2 (.a(counter_1_q), .b({8{1'b0}}), .eq(comparator_2_eq));  // open: gt, lt
  Hex_Digit_Display hex_digit_display_2 (.value(LedData[27:24]));  // open: dp
  Hex_Digit_Display hex_digit_display_3 (.value(LedData[23:20]));  // open: dp
  and and_2 (and_2_out, comparator_1_eq, syscall);
  not not_3 (not_3_out, comparator_1_eq);
  Hex_Digit_Display hex_digit_display_4 (.value(LedData[15:12]));  // open: dp
  Hex_Digit_Display hex_digit_display_5 (.value(LedData[19:16]));  // open: dp
  \硬布线控制器  \u_硬布线控制器_1  (
    .Func(if_id_1_insout[5:0]), .OP(if_id_1_insout[31:26]), .ALU_OP(\硬布线控制器_1_alu_op ),
    .MemToReg(\硬布线控制器_1_memwrite [0]), .MemWrite(\硬布线控制器_1_memwrite [2]), .ALU_SRC(\硬布线控制器_1_alu_src [4]),
    .RegWrite(\硬布线控制器_1_regwrite [1]), .SysCALL(syscall), .SignedExt(\硬布线控制器_1_signedext ), .RegDst(regDst),
    .JR(\硬布线控制器_1_jmp [1]), .JMP(\硬布线控制器_1_jmp [0]), .Beq(\硬布线控制器_1_jmp [3]), .JAL(JAL),
    .Bne(\硬布线控制器_1_jmp [4]), .SH(\硬布线控制器_1_memwrite [2]), .BGTZ(\硬布线控制器_1_jmp [2]),
    .SRLV(\硬布线控制器_1_alu_src [5]));  // open: ERET, RS, MFC0, MTC0
  Shifter #(.width(32), .shift("ar")) shifter_1 (
    .in({if_id_1_insout[15:0], {16{1'b0}}}), .\dist (5'b10000), .out(shifter_1_out));
  and and_3 (halt, not_3_out, syscall, comparator_2_eq);
  Hex_Digit_Display hex_digit_display_6 (.value(LedData[7:4]));  // open: dp
  Hex_Digit_Display hex_digit_display_7 (.value(LedData[11:8]));  // open: dp
  Clock clock_1 (.out(CLK));
  Multiplexer #(.width(32), .enable("false")) multiplexer_2 (
    .in0({{16{1'b0}}, if_id_1_insout[15:0]}), .in1(shifter_1_out), .out(multiplexer_2_out),
    .sel(\硬布线控制器_1_signedext ));
  Multiplexer #(.width(5), .enable("false")) multiplexer_3 (
    .in0(if_id_1_insout[25:21]), .in1(5'b00010), .out(multiplexer_3_out), .sel(syscall));
  Multiplexer #(.width(5), .enable("false")) multiplexer_4 (
    .in0(if_id_1_insout[20:16]), .in1(5'b00100), .out(multiplexer_4_out), .sel(syscall));
  Multiplexer #(.width(5), .enable("false")) multiplexer_5 (
    .in0(if_id_1_insout[20:16]), .in1(if_id_1_insout[15:11]), .out(multiplexer_5_out), .sel(regDst));
  Multiplexer #(.width(5), .enable("false")) multiplexer_6 (
    .in0(multiplexer_5_out), .in1({5{1'b1}}), .out(rW), .sel(JAL));
  Register #(.width(32)) register_1 (.D(R2), .en(and_2_out), .Q(LedData), .clk(and_2_out), .clr(RST));
  Hex_Digit_Display hex_digit_display_8 (.value(LedData[3:0]));  // open: dp
  // RegisterFile registerfile_1: pin names not known; wires that end beside it: if_id_1_insout[25:0], registerfile_1_p2, CLK, mem_wb_1_wbout[1], mem_wb_1_wbout[7:3], multiplexer_3_out, multiplexer_4_out, R1, R2, registerfile_1_p10
  // Probe on mem_wb_1_wbout[7:3]
  ID_EX id_ex_1 (
    .WBin({rW, JAL, \硬布线控制器_1_regwrite [1], \硬布线控制器_1_memwrite [0]}),
    .Memin({{2{\硬布线控制器_1_memwrite [2]}}, \硬布线控制器_1_memwrite [0]}), .R1in(R1), .R2in(R2), .CLK(CLK),
    .WBout(id_ex_1_wbout), .Memout(id_ex_1_memout), .R1out(id_ex_1_r1out), .R2out(id_ex_1_r2out),
    .\使能端_低电平有效_stall_高电平有效 (1'b0), .PCin(ID_PC), .PCout(EX_PC), .Immin(multiplexer_2_out),
    .Immout(registerfile_1_p10), .Jofin(if_id_1_insout[25:0]), .Jofout(id_ex_1_jofout),
    .IFout(id_ex_1_ifout), .IFin({JAL, \硬布线控制器_1_jmp }), .Exin({\硬布线控制器_1_alu_src , \硬布线控制器_1_alu_op }),
    .Exout(id_ex_1_exout), .\异步清零 (RST), .Halt(halt), .Halt_2(id_ex_1_halt_2));  // open: 同步清零_气泡_高电平有效, Intin, Intout
  // Probe on \总周期数 
  // Probe on \无条件分支数 
  // Probe on \条件分支成功数 
  // Probe on \插入气泡数 
  // Probe on \LoadUse次数 
  Multiplexer #(.width(32), .enable("false")) multiplexer_7 (
    .in0(id_ex_1_r2out), .in1(registerfile_1_p10), .out(multiplexer_7_out), .sel(id_ex_1_exout[4]));
  Shifter #(.width(32)) shifter_2 (.in(registerfile_1_p10), .\dist (5'b00010), .out(shifter_2_out));
  not not_4 (not_4_out, Equ);
  Comparator #(.width(32)) comparator_3 (.a(id_ex_1_r1out), .b({32{1'b0}}), .gt(comparator_3_gt));  // open: eq, lt
  // Probe on IF_PC[11:0]
  MIPS_ALU mips_alu_1 (
    .X(id_ex_1_r1out), .Y(multiplexer_7_out), .AluOP(id_ex_1_exout[3:0]), .Equal(Equ),
    .Result(mips_alu_1_result), .shamt(multiplexer_8_out));  // open: Result_2
  Multiplexer #(.width(5), .enable("false")) multiplexer_8 (
    .in0(registerfile_1_p10[10:6]), .in1(id_ex_1_r1out[4:0]), .out(multiplexer_8_out), .sel(id_ex_1_exout[5]));
  Adder #(.width(32)) adder_2 (.a(EX_PC), .b(shifter_2_out), .out(adder_2_out));  // open: cin, cout
  or or_1 (or_1_out[0], id_ex_1_ifout[0], id_ex_1_ifout[5]);
  and and_4 (and_4_out, id_ex_1_ifout[3], Equ);
  and and_5 (and_5_out, id_ex_1_ifout[4], not_4_out);
  or or_2 (or_1_out[2], and_4_out, and_5_out, and_6_out);
  and and_6 (and_6_out, id_ex_1_ifout[2], comparator_3_gt);
  // Probe on ID_PC[11:0]
  EX_MEM ex_mem_1 (
    .WBin(id_ex_1_wbout), .WBout(ex_mem_1_wbout), .Memin(id_ex_1_memout), .Memout(ex_mem_1_memout),
    .Resin(mips_alu_1_result), .Resout(ex_mem_1_resout), .R2in(id_ex_1_r2out), .R2out(ex_mem_1_r2out),
    .CLK(CLK), .\使能端_低电平有效_stall_高电平有效 (1'b0), .PCin(EX_PC), .PCout(MEM_PC), .\异步清零 (RST),
    .Halt(id_ex_1_halt_2), .Halt_2(ex_mem_1_halt_2));  // open: 同步清零_气泡_高电平有效, R1in, R1out, Intin, Intout
  // Probe on EX_PC[11:0]
  // Probe on MEM_PC[11:0]
  Multiplexer #(.select(3), .width(32), .enable("false")) multiplexer_9 (
    .in0(EX_PC), .in1({EX_PC[31:28], id_ex_1_jofout, 2'b00}), .in2(id_ex_1_r1out), .in3({32{1'b0}}),
    .in4(adder_2_out), .in5({32{1'b0}}), .in6({32{1'b0}}), .in7({32{1'b0}}), .out(multiplexer_9_out),
    .sel({or_1_out[2], id_ex_1_ifout[1], or_1_out[0]}));
  or or_3 (Jump, or_1_out[0], id_ex_1_ifout[1], or_1_out[2]);
  not not_5 (not_5_out, stall);
  and and_7 (and_7_out, not_5_out, or_4_out);
  or or_4 (or_4_out, or_1_out[0], id_ex_1_ifout[1]);
  and and_8 (and_8_out, not_5_out, or_1_out[2]);
  // Probe on WB_PC[11:0]
  Multiplexer #(.width(4), .enable("false")) multiplexer_10 (
    .in0(4'b1111), .in1(multiplexer_11_out), .out(multiplexer_10_out), .sel(ex_mem_1_memout[2]));
  Multiplexer #(.width(4), .enable("false")) multiplexer_11 (
    .in0(4'b0011), .in1(4'b1100), .out(multiplexer_11_out), .sel(ex_mem_1_resout[1]));
  Counter #(.width(16), .max('hffff)) counter_2 (
    .count(not_5_out), .Q(\总周期数 ), .clk(CLK), .clr(RST));  // open: load, D, carry
  Counter #(.width(16), .max('hffff)) counter_3 (
    .count(and_7_out), .Q(\无条件分支数 ), .clk(CLK), .clr(RST));  // open: load, D, carry
  Counter #(.width(16), .max('hffff)) counter_4 (
    .count(and_8_out), .Q(\条件分支成功数 ), .clk(CLK), .clr(RST));  // open: load, D, carry
  // MIPS_RAM mips_ram_1: pin names not known; wires that end beside it: ex_mem_1_resout[21:2], mips_ram_1_p2, ex_mem_1_memout[1], multiplexer_10_out, CLK, ex_mem_1_memout[0], RST, mips_ram_1_p8
  Multiplexer #(.width(32), .enable("false")) multiplexer_12 (
    .in0(ex_mem_1_r2out), .in1(shifter_3_out), .out(mips_ram_1_p2), .sel(and_9_out));
  and and_9 (and_9_out, ex_mem_1_memout[2], ex_mem_1_resout[1]);
  Shifter #(.width(32)) shifter_3 (.in(ex_mem_1_r2out), .\dist (5'b10000), .out(shifter_3_out));
  MEM_WB mem_wb_1 (
    .WBin(ex_mem_1_wbout), .WBout(mem_wb_1_wbout), .memin(mips_ram_1_p8), .memout(mem_wb_1_memout),
    .Resin(ex_mem_1_resout), .Resout(mem_wb_1_resout), .CLK(CLK), .\使能端_低电平有效_stall_高电平有效 (1'b0),
    .PCin(MEM_PC), .PCout(WB_PC), .\异步清零 (RST), .Halt(ex_mem_1_halt_2), .Halt_2(stall));  // open: 同步清零_气泡_高电平有效, R1in, R1out, R2in, R2out, Intin, Intout
  Multiplexer #(.width(32), .enable("false")) multiplexer_13 (
    .in0(mem_wb_1_resout), .in1(mem_wb_1_memout), .out(multiplexer_13_out), .sel(mem_wb_1_wbout[0]));
  Multiplexer #(.width(32), .enable("false")) multiplexer_14 (
    .in0(multiplexer_13_out), .in1(WB_PC), .out(registerfile_1_p2), .sel(mem_wb_1_wbout[2]));

  // Notes on the sheet:
  //   中断源
  //   中断等待指示
  //   指令存储器
  //   PC+4
  //   contents of rom_1 (hex, n*v repeats v):
  //   20100000 20110001 20120002 20130003 36100000 36310001 36520002 36730003 ae100000 ae110004 ae120008
  //   ae13000c 2002000a 0 0 0 c
  //   Jmp
  //   Jr
  //   SignedExt
  //   Sh
  //   Bgtz
  //   Srlv
  //   OP
  //   FUNC
  //   数码管输出
  //   Beq
  //   Bne
  //   MemToReg
  //   MemWrite
  //   AluOP
  //   AluSrcB
  //   RegWrite
  //   JAL
  //   rs
  //   rt
  //   rd
  //   流水调试日志用
endmodule
// 源寄存器使用情况
module \源寄存器使用情况  (
  input  OP0,
  input  OP1,
  input  OP2,
  input  OP3,
  input  OP4,
  input  OP5,
  input  F0,
  input  F1,
  input  F2,
  input  F3,
  input  F4,
  input  F5,
  output R1_Used,
  output R2_Used
);

  wire and_1_out, and_2_out, and_3_out, and_4_out, and_5_out, and_6_out, and_7_out, and_8_out, and_9_out,
       and_10_out, and_11_out, and_12_out, and_13_out, and_14_out, and_15_out, and_16_out, and_17_out,
       and_18_out, and_19_out, and_20_out, and_21_out, and_22_out, and_23_out, and_24_out, and_25_out,
       and_26_out, and_27_out, and_28_out, and_29_out, and_30_out, and_31_out, and_32_out, and_33_out,
       and_34_out, and_35_out, and_36_out, and_37_out, and_38_out, and_39_out, and_40_out, and_41_out,
       not_1_out, not_2_out, not_3_out, not_4_out, not_5_out, not_6_out, not_7_out, not_8_out, not_9_out,
       not_10_out, not_11_out, not_12_out, not_13_out, not_14_out, not_15_out, not_16_out, not_17_out,
       not_18_out, not_19_out, not_20_out, not_21_out, not_22_out, not_23_out, not_24_out, not_25_out,
       not_26_out, not_27_out, not_28_out, not_29_out, not_30_out, not_31_out, not_32_out, not_33_out,
       not_34_out, not_35_out, not_36_out, not_37_out, not_38_out, not_39_out, not_40_out, not_41_out,
       not_42_out, not_43_out, not_44_out, not_45_out, not_46_out, not_47_out, not_48_out, not_49_out,
       not_50_out, not_51_out, not_52_out, not_53_out, not_54_out, not_55_out, not_56_out, not_57_out,
       not_58_out, not_59_out, not_60_out, not_61_out, not_62_out, not_63_out, not_64_out, not_65_out,
       not_66_out, not_67_out, not_68_out, not_69_out, not_70_out, not_71_out, not_72_out, not_73_out,
       not_74_out, not_75_out, not_76_out, not_77_out, not_78_out, not_79_out, not_80_out, not_81_out,
       not_82_out, not_83_out, not_84_out, not_85_out, not_86_out, not_87_out, not_88_out, not_89_out,
       not_90_out, not_91_out, not_92_out, not_93_out, not_94_out, not_95_out, not_96_out, not_97_out,
       not_98_out, not_99_out, not_100_out, not_101_out, not_102_out, not_103_out, not_104_out, not_105_out,
       not_106_out, not_107_out, not_108_out, not_109_out, not_110_out, not_111_out, not_112_out,
       not_113_out, not_114_out, not_115_out, not_116_out, not_117_out, not_118_out, not_119_out,
       not_120_out, not_121_out, not_122_out, not_123_out, not_124_out, not_125_out, not_126_out,
       not_127_out, not_128_out, not_129_out, not_130_out, not_131_out, not_132_out, not_133_out,
       not_134_out, not_135_out, not_136_out, not_137_out, not_138_out, not_139_out, not_140_out,
       not_141_out, not_142_out, not_143_out, not_144_out, not_145_out, not_146_out, not_147_out,
       not_148_out, not_149_out, not_150_out, not_151_out, not_152_out, not_153_out, not_154_out,
       not_155_out, not_156_out, not_157_out, not_158_out, not_159_out, not_160_out, not_161_out,
       not_162_out, not_163_out, not_164_out, not_165_out, not_166_out, not_167_out, not_168_out,
       not_169_out, not_170_out, not_171_out, not_172_out, not_173_out, not_174_out, not_175_out,
       not_176_out, not_177_out, not_178_out, not_179_out, not_180_out, not_181_out, not_182_out,
       not_183_out, not_184_out, not_185_out, not_186_out, not_187_out, not_188_out, not_189_out,
       not_190_out, not_191_out, not_192_out, not_193_out, not_194_out, not_195_out, not_196_out,
       not_197_out, not_198_out, not_199_out, not_200_out, not_201_out, not_202_out, not_203_out,
       not_204_out, not_205_out, not_206_out, not_207_out, not_208_out, not_209_out, not_210_out,
       not_211_out, not_212_out, not_213_out, not_214_out, not_215_out, not_216_out, not_217_out,
       not_218_out, not_219_out, not_220_out, not_221_out, not_222_out, not_223_out, not_224_out,
       not_225_out, not_226_out, not_227_out, not_228_out, not_229_out, not_230_out, not_231_out,
       not_232_out, not_233_out, not_234_out, not_235_out, not_236_out, not_237_out, not_238_out,
       not_239_out, not_240_out, not_241_out, not_242_out, not_243_out, not_244_out, not_245_out,
       not_246_out, not_247_out, not_248_out, not_249_out, not_250_out, not_251_out, not_252_out,
       not_253_out, not_254_out, not_255_out, not_256_out, not_257_out, not_258_out, not_259_out,
       not_260_out, not_261_out, not_262_out, not_263_out, not_264_out, not_265_out, not_266_out,
       not_267_out, not_268_out, not_269_out, not_270_out, not_271_out, not_272_out, not_273_out,
       not_274_out, not_275_out, not_276_out, not_277_out, not_278_out, not_279_out, not_280_out,
       not_281_out, not_282_out, not_283_out, not_284_out, not_285_out, not_286_out, not_287_out,
       not_288_out, not_289_out, not_290_out, not_291_out, not_292_out, not_293_out, not_294_out,
       not_295_out, not_296_out, not_297_out, not_298_out, not_299_out, not_300_out, not_301_out,
       not_302_out, not_303_out, not_304_out, not_305_out, not_306_out;

  not not_1 (not_1_out, OP5);
  not not_2 (not_2_out, OP4);
  not not_3 (not_3_out, OP3);
  not not_4 (not_4_out, OP2);
  not not_5 (not_5_out, OP1);
  not not_6 (not_6_out, OP0);
  not not_7 (not_7_out, F4);
  not not_8 (not_8_out, F3);
  not not_9 (not_9_out, F2);
  not not_10 (not_10_out, F1);
  not not_11 (not_11_out, F0);
  not not_12 (not_12_out, OP5);
  not not_13 (not_13_out, OP4);
  not not_14 (not_14_out, OP3);
  not not_15 (not_15_out, OP2);
  not not_16 (not_16_out, OP1);
  not not_17 (not_17_out, OP0);
  not not_18 (not_18_out, F4);
  not not_19 (not_19_out, F3);
  not not_20 (not_20_out, F2);
  not not_21 (not_21_out, F1);
  not not_22 (not_22_out, OP5);
  not not_23 (not_23_out, OP4);
  not not_24 (not_24_out, OP3);
  not not_25 (not_25_out, OP2);
  not not_26 (not_26_out, OP1);
  not not_27 (not_27_out, OP0);
  not not_28 (not_28_out, F4);
  not not_29 (not_29_out, F3);
  not not_30 (not_30_out, F2);
  not not_31 (not_31_out, F0);
  not not_32 (not_32_out, OP5);
  not not_33 (not_33_out, OP4);
  not not_34 (not_34_out, OP3);
  not not_35 (not_35_out, OP2);
  not not_36 (not_36_out, OP1);
  not not_37 (not_37_out, OP0);
  not not_38 (not_38_out, F4);
  not not_39 (not_39_out, F3);
  not not_40 (not_40_out, F1);
  not not_41 (not_41_out, F0);
  not not_42 (not_42_out, OP5);
  not not_43 (not_43_out, OP4);
  not not_44 (not_44_out, OP3);
  not not_45 (not_45_out, OP2);
  not not_46 (not_46_out, OP1);
  not not_47 (not_47_out, OP0);
  not not_48 (not_48_out, F4);
  not not_49 (not_49_out, F3);
  not not_50 (not_50_out, F1);
  not not_51 (not_51_out, OP5);
  not not_52 (not_52_out, OP4);
  not not_53 (not_53_out, OP3);
  not not_54 (not_54_out, OP2);
  not not_55 (not_55_out, OP1);
  not not_56 (not_56_out, OP0);
  not not_57 (not_57_out, F4);
  not not_58 (not_58_out, F3);
  not not_59 (not_59_out, OP5);
  not not_60 (not_60_out, OP4);
  not not_61 (not_61_out, OP3);
  not not_62 (not_62_out, OP2);
  not not_63 (not_63_out, OP1);
  not not_64 (not_64_out, OP0);
  not not_65 (not_65_out, F4);
  not not_66 (not_66_out, F2);
  not not_67 (not_67_out, F0);
  not not_68 (not_68_out, OP5);
  not not_69 (not_69_out, OP4);
  not not_70 (not_70_out, OP3);
  not not_71 (not_71_out, OP2);
  not not_72 (not_72_out, OP1);
  not not_73 (not_73_out, OP0);
  not not_74 (not_74_out, F4);
  not not_75 (not_75_out, F2);
  not not_76 (not_76_out, OP5);
  not not_77 (not_77_out, OP4);
  not not_78 (not_78_out, OP3);
  not not_79 (not_79_out, OP2);
  not not_80 (not_80_out, OP1);
  not not_81 (not_81_out, OP0);
  not not_82 (not_82_out, F5);
  not not_83 (not_83_out, F4);
  not not_84 (not_84_out, F2);
  not not_85 (not_85_out, F1);
  not not_86 (not_86_out, F0);
  not not_87 (not_87_out, OP5);
  not not_88 (not_88_out, OP4);
  not not_89 (not_89_out, OP3);
  not not_90 (not_90_out, OP2);
  not not_91 (not_91_out, OP1);
  not not_92 (not_92_out, OP0);
  not not_93 (not_93_out, F5);
  not not_94 (not_94_out, F4);
  not not_95 (not_95_out, F1);
  not not_96 (not_96_out, F0);
  not not_97 (not_97_out, OP5);
  not not_98 (not_98_out, OP4);
  not not_99 (not_99_out, OP3);
  not not_100 (not_100_out, OP1);
  not not_101 (not_101_out, OP0);
  not not_102 (not_102_out, OP5);
  not not_103 (not_103_out, OP4);
  not not_104 (not_104_out, OP3);
  not not_105 (not_105_out, OP1);
  not not_106 (not_106_out, OP5);
  not not_107 (not_107_out, OP4);
  not not_108 (not_108_out, OP2);
  not not_109 (not_109_out, OP1);
  not not_110 (not_110_out, OP0);
  not not_111 (not_111_out, OP5);
  not not_112 (not_112_out, OP4);
  not not_113 (not_113_out, OP1);
  not not_114 (not_114_out, OP0);
  not not_115 (not_115_out, OP5);
  not not_116 (not_116_out, OP4);
  not not_117 (not_117_out, OP2);
  not not_118 (not_118_out, OP1);
  not not_119 (not_119_out, OP5);
  not not_120 (not_120_out, OP4);
  not not_121 (not_121_out, OP2);
  not not_122 (not_122_out, OP0);
  not not_123 (not_123_out, OP5);
  not not_124 (not_124_out, OP4);
  not not_125 (not_125_out, OP1);
  not not_126 (not_126_out, OP4);
  not not_127 (not_127_out, OP3);
  not not_128 (not_128_out, OP2);
  not not_129 (not_129_out, OP4);
  not not_130 (not_130_out, OP2);
  not not_131 (not_131_out, OP5);
  not not_132 (not_132_out, OP4);
  not not_133 (not_133_out, OP3);
  not not_134 (not_134_out, OP2);
  not not_135 (not_135_out, OP1);
  not not_136 (not_136_out, OP0);
  not not_137 (not_137_out, F5);
  not not_138 (not_138_out, F4);
  not not_139 (not_139_out, F3);
  not not_140 (not_140_out, F0);
  not not_141 (not_141_out, OP5);
  not not_142 (not_142_out, OP4);
  not not_143 (not_143_out, OP3);
  not not_144 (not_144_out, OP2);
  not not_145 (not_145_out, OP1);
  not not_146 (not_146_out, OP0);
  not not_147 (not_147_out, F4);
  not not_148 (not_148_out, F3);
  not not_149 (not_149_out, F0);
  not not_150 (not_150_out, OP4);
  not not_151 (not_151_out, OP2);
  not not_152 (not_152_out, OP1);
  not not_153 (not_153_out, OP5);
  not not_154 (not_154_out, OP4);
  not not_155 (not_155_out, OP3);
  not not_156 (not_156_out, OP5);
  not not_157 (not_157_out, OP4);
  not not_158 (not_158_out, OP3);
  not not_159 (not_159_out, OP2);
  not not_160 (not_160_out, OP1);
  not not_161 (not_161_out, OP0);
  not not_162 (not_162_out, F5);
  not not_163 (not_163_out, F4);
  not not_164 (not_164_out, F3);
  not not_165 (not_165_out, F2);
  not not_166 (not_166_out, F1);
  not not_167 (not_167_out, F0);
  not not_168 (not_168_out, OP5);
  not not_169 (not_169_out, OP4);
  not not_170 (not_170_out, OP3);
  not not_171 (not_171_out, OP2);
  not not_172 (not_172_out, OP1);
  not not_173 (not_173_out, OP0);
  not not_174 (not_174_out, F5);
  not not_175 (not_175_out, F4);
  not not_176 (not_176_out, F3);
  not not_177 (not_177_out, F2);
  not not_178 (not_178_out, OP5);
  not not_179 (not_179_out, OP4);
  not not_180 (not_180_out, OP3);
  not not_181 (not_181_out, OP2);
  not not_182 (not_182_out, OP1);
  not not_183 (not_183_out, OP0);
  not not_184 (not_184_out, F5);
  not not_185 (not_185_out, F4);
  not not_186 (not_186_out, F3);
  not not_187 (not_187_out, F2);
  not not_188 (not_188_out, F0);
  not not_189 (not_189_out, OP5);
  not not_190 (not_190_out, OP4);
  not not_191 (not_191_out, OP3);
  not not_192 (not_192_out, OP2);
  not not_193 (not_193_out, OP1);
  not not_194 (not_194_out, OP0);
  not not_195 (not_195_out, F4);
  not not_196 (not_196_out, F3);
  not not_197 (not_197_out, F2);
  not not_198 (not_198_out, F1);
  not not_199 (not_199_out, F0);
  not not_200 (not_200_out, OP5);
  not not_201 (not_201_out, OP4);
  not not_202 (not_202_out, OP3);
  not not_203 (not_203_out, OP2);
  not not_204 (not_204_out, OP1);
  not not_205 (not_205_out, OP0);
  not not_206 (not_206_out, F4);
  not not_207 (not_207_out, F3);
  not not_208 (not_208_out, F2);
  not not_209 (not_209_out, F1);
  not not_210 (not_210_out, OP5);
  not not_211 (not_211_out, OP4);
  not not_212 (not_212_out, OP3);
  not not_213 (not_213_out, OP2);
  not not_214 (not_214_out, OP1);
  not not_215 (not_215_out, OP0);
  not not_216 (not_216_out, F4);
  not not_217 (not_217_out, F3);
  not not_218 (not_218_out, F2);
  not not_219 (not_219_out, F0);
  not not_220 (not_220_out, OP5);
  not not_221 (not_221_out, OP4);
  not not_222 (not_222_out, OP3);
  not not_223 (not_223_out, OP2);
  not not_224 (not_224_out, OP1);
  not not_225 (not_225_out, OP0);
  not not_226 (not_226_out, F4);
  not not_227 (not_227_out, F3);
  not not_228 (not_228_out, F1);
  not not_229 (not_229_out, F0);
  not not_230 (not_230_out, OP5);
  not not_231 (not_231_out, OP4);
  not not_232 (not_232_out, OP3);
  not not_233 (not_233_out, OP2);
  not not_234 (not_234_out, OP1);
  not not_235 (not_235_out, OP0);
  not not_236 (not_236_out, F4);
  not not_237 (not_237_out, F3);
  not not_238 (not_238_out, F1);
  not not_239 (not_239_out, OP5);
  not not_240 (not_240_out, OP4);
  not not_241 (not_241_out, OP3);
  not not_242 (not_242_out, OP2);
  not not_243 (not_243_out, OP1);
  not not_244 (not_244_out, OP0);
  not not_245 (not_245_out, F4);
  not not_246 (not_246_out, F3);
  not not_247 (not_247_out, OP5);
  not not_248 (not_248_out, OP4);
  not not_249 (not_249_out, OP3);
  not not_250 (not_250_out, OP2);
  not not_251 (not_251_out, OP1);
  not not_252 (not_252_out, OP0);
  not not_253 (not_253_out, F4);
  not not_254 (not_254_out, F2);
  not not_255 (not_255_out, F0);
  not not_256 (not_256_out, OP5);
  not not_257 (not_257_out, OP4);
  not not_258 (not_258_out, OP3);
  not not_259 (not_259_out, OP2);
  not not_260 (not_260_out, OP1);
  not not_261 (not_261_out, OP0);
  not not_262 (not_262_out, F4);
  not not_263 (not_263_out, F2);
  not not_264 (not_264_out, OP5);
  not not_265 (not_265_out, OP4);
  not not_266 (not_266_out, OP3);
  not not_267 (not_267_out, OP2);
  not not_268 (not_268_out, OP1);
  not not_269 (not_269_out, OP0);
  not not_270 (not_270_out, F5);
  not not_271 (not_271_out, F4);
  not not_272 (not_272_out, F1);
  not not_273 (not_273_out, F0);
  not not_274 (not_274_out, OP5);
  not not_275 (not_275_out, OP4);
  not not_276 (not_276_out, OP3);
  not not_277 (not_277_out, OP1);
  not not_278 (not_278_out, OP0);
  not not_279 (not_279_out, OP5);
  not not_280 (not_280_out, OP4);
  not not_281 (not_281_out, OP3);
  not not_282 (not_282_out, OP1);
  not not_283 (not_283_out, OP4);
  not not_284 (not_284_out, OP2);
  not not_285 (not_285_out, OP5);
  not not_286 (not_286_out, OP4);
  not not_287 (not_287_out, OP3);
  not not_288 (not_288_out, OP2);
  not not_289 (not_289_out, OP1);
  not not_290 (not_290_out, OP0);
  not not_291 (not_291_out, F5);
  not not_292 (not_292_out, F4);
  not not_293 (not_293_out, F3);
  not not_294 (not_294_out, F0);
  not not_295 (not_295_out, OP5);
  not not_296 (not_296_out, OP4);
  not not_297 (not_297_out, OP3);
  not not_298 (not_298_out, OP2);
  not not_299 (not_299_out, OP1);
  not not_300 (not_300_out, OP0);
  not not_301 (not_301_out, F4);
  not not_302 (not_302_out, F3);
  not not_303 (not_303_out, F0);
  not not_304 (not_304_out, OP4);
  not not_305 (not_305_out, OP2);
  not not_306 (not_306_out, OP1);
  and and_1 (and_1_out, not_1_out, not_2_out, not_3_out, not_4_out, not_5_out, not_6_out, F5, not_7_out, not_8_out, not_9_out, not_10_out, not_11_out);
  and and_2 (and_2_out, not_12_out, not_13_out, not_14_out, not_15_out, not_16_out, not_17_out, F5, not_18_out, not_19_out, not_20_out, not_21_out, F0);
  and and_3 (and_3_out, not_22_out, not_23_out, not_24_out, not_25_out, not_26_out, not_27_out, F5, not_28_out, not_29_out, not_30_out, F1, not_31_out);
  and and_4 (and_4_out, not_32_out, not_33_out, not_34_out, not_35_out, not_36_out, not_37_out, F5, not_38_out, not_39_out, F2, not_40_out, not_41_out);
  and and_5 (and_5_out, not_42_out, not_43_out, not_44_out, not_45_out, not_46_out, not_47_out, F5, not_48_out, not_49_out, F2, not_50_out, F0);
  and and_6 (and_6_out, not_51_out, not_52_out, not_53_out, not_54_out, not_55_out, not_56_out, F5, not_57_out, not_58_out, F2, F1, F0);
  and and_7 (and_7_out, not_59_out, not_60_out, not_61_out, not_62_out, not_63_out, not_64_out, F5, not_65_out, F3, not_66_out, F1, not_67_out);
  and and_8 (and_8_out, not_68_out, not_69_out, not_70_out, not_71_out, not_72_out, not_73_out, F5, not_74_out, F3, not_75_out, F1, F0);
  and and_9 (and_9_out, not_76_out, not_77_out, not_78_out, not_79_out, not_80_out, not_81_out, not_82_out, not_83_out, F3, not_84_out, not_85_out, not_86_out);
  and and_10 (and_10_out, not_87_out, not_88_out, not_89_out, not_90_out, not_91_out, not_92_out, not_93_out, not_94_out, F3, F2, not_95_out, not_96_out);
  and and_11 (and_11_out, not_97_out, not_98_out, not_99_out, OP2, not_100_out, not_101_out);
  and and_12 (and_12_out, not_102_out, not_103_out, not_104_out, OP2, not_105_out, OP0);
  and and_13 (and_13_out, not_106_out, not_107_out, OP3, not_108_out, not_109_out, not_110_out);
  and and_14 (and_14_out, not_111_out, not_112_out, OP3, OP2, not_113_out, not_114_out);
  and and_15 (and_15_out, not_115_out, not_116_out, OP3, not_117_out, not_118_out, OP0);
  and and_16 (and_16_out, not_119_out, not_120_out, OP3, not_121_out, OP1, not_122_out);
  and and_17 (and_17_out, not_123_out, not_124_out, OP3, OP2, not_125_out, OP0);
  and and_18 (and_18_out, OP5, not_126_out, not_127_out, not_128_out, OP1, OP0);
  and and_19 (and_19_out, OP5, not_129_out, OP3, not_130_out, OP1, OP0);
  and and_20 (and_20_out, not_131_out, not_132_out, not_133_out, not_134_out, not_135_out, not_136_out, not_137_out, not_138_out, not_139_out, F2, F1, not_140_out);
  and and_21 (and_21_out, not_141_out, not_142_out, not_143_out, not_144_out, not_145_out, not_146_out, F5, not_147_out, not_148_out, F2, F1, not_149_out);
  and and_22 (and_22_out, OP5, not_150_out, OP3, not_151_out, not_152_out, OP0);
  and and_23 (and_23_out, not_153_out, not_154_out, not_155_out, OP2, OP1, OP0);
  and and_24 (and_24_out, not_156_out, not_157_out, not_158_out, not_159_out, not_160_out, not_161_out, not_162_out, not_163_out, not_164_out, not_165_out, not_166_out, not_167_out);
  and and_25 (and_25_out, not_168_out, not_169_out, not_170_out, not_171_out, not_172_out, not_173_out, not_174_out, not_175_out, not_176_out, not_177_out, F1, F0);
  and and_26 (and_26_out, not_178_out, not_179_out, not_180_out, not_181_out, not_182_out, not_183_out, not_184_out, not_185_out, not_186_out, not_187_out, F1, not_188_out);
  and and_27 (and_27_out, not_189_out, not_190_out, not_191_out, not_192_out, not_193_out, not_194_out, F5, not_195_out, not_196_out, not_197_out, not_198_out, not_199_out);
  and and_28 (and_28_out, not_200_out, not_201_out, not_202_out, not_203_out, not_204_out, not_205_out, F5, not_206_out, not_207_out, not_208_out, not_209_out, F0);
  and and_29 (and_29_out, not_210_out, not_211_out, not_212_out, not_213_out, not_214_out, not_215_out, F5, not_216_out, not_217_out, not_218_out, F1, not_219_out);
  and and_30 (and_30_out, not_220_out, not_221_out, not_222_out, not_223_out, not_224_out, not_225_out, F5, not_226_out, not_227_out, F2, not_228_out, not_229_out);
  and and_31 (and_31_out, not_230_out, not_231_out, not_232_out, not_233_out, not_234_out, not_235_out, F5, not_236_out, not_237_out, F2, not_238_out, F0);
  and and_32 (and_32_out, not_239_out, not_240_out, not_241_out, not_242_out, not_243_out, not_244_out, F5, not_245_out, not_246_out, F2, F1, F0);
  and and_33 (and_33_out, not_247_out, not_248_out, not_249_out, not_250_out, not_251_out, not_252_out, F5, not_253_out, F3, not_254_out, F1, not_255_out);
  and and_34 (and_34_out, not_256_out, not_257_out, not_258_out, not_259_out, not_260_out, not_261_out, F5, not_262_out, F3, not_263_out, F1, F0);
  and and_35 (and_35_out, not_264_out, not_265_out, not_266_out, not_267_out, not_268_out, not_269_out, not_270_out, not_271_out, F3, F2, not_272_out, not_273_out);
  and and_36 (and_36_out, not_274_out, not_275_out, not_276_out, OP2, not_277_out, not_278_out);
  and and_37 (and_37_out, not_279_out, not_280_out, not_281_out, OP2, not_282_out, OP0);
  and and_38 (and_38_out, OP5, not_283_out, OP3, not_284_out, OP1, OP0);
  and and_39 (and_39_out, not_285_out, not_286_out, not_287_out, not_288_out, not_289_out, not_290_out, not_291_out, not_292_out, not_293_out, F2, F1, not_294_out);
  and and_40 (and_40_out, not_295_out, not_296_out, not_297_out, not_298_out, not_299_out, not_300_out, F5, not_301_out, not_302_out, F2, F1, not_303_out);
  and and_41 (and_41_out, OP5, not_304_out, OP3, not_305_out, not_306_out, OP0);
  or or_1 (R1_Used, and_1_out, and_2_out, and_3_out, and_4_out, and_5_out, and_6_out, and_7_out, and_8_out, and_9_out, and_10_out, and_11_out, and_12_out, and_13_out, and_14_out, and_15_out, and_16_out, and_17_out, and_18_out, and_19_out, and_20_out, and_21_out, and_22_out, and_23_out);
  or or_2 (R2_Used, and_24_out, and_25_out, and_26_out, and_27_out, and_28_out, and_29_out, and_30_out, and_31_out, and_32_out, and_33_out, and_34_out, and_35_out, and_36_out, and_37_out, and_38_out, and_39_out, and_40_out, and_41_out);
endmodule

// 数据相关检测
module \数据相关检测  (
  input  [5:0] OP,
  input  [4:0] EX_WriteReg_num,
  input  EX_RegWrite,
  input  [4:0] MEM_WriteReg_num,
  input  MEM_RegWrite,
  input  [5:0] Func,
  input  [4:0] ID_R1_num,
  input  [4:0] ID_R2_num,
  output \数据相关 
);

  wire and_1_out, and_2_out, and_3_out, and_4_out, comparator_1_eq, comparator_2_eq, comparator_3_eq,
       comparator_4_eq, comparator_5_eq, comparator_6_eq, not_1_out, not_2_out, R1_Used, R2_Used,
       \源寄存器使用情况_1_r1_used , \源寄存器使用情况_1_r2_used ;

  \源寄存器使用情况  \u_源寄存器使用情况_1  (
    .OP0(OP[0]), .OP1(OP[1]), .OP2(OP[2]), .OP3(OP[3]), .OP4(OP[4]), .OP5(OP[5]), .F0(Func[0]), .F1(Func[1]),
    .F2(Func[2]), .F3(Func[3]), .F4(Func[4]), .F5(Func[5]), .R1_Used(\源寄存器使用情况_1_r1_used ),
    .R2_Used(\源寄存器使用情况_1_r2_used ));
  Comparator #(.width(5)) comparator_1 (.a(ID_R1_num), .b(EX_WriteReg_num), .eq(comparator_1_eq));  // open: gt, lt
  Comparator #(.width(5)) comparator_2 (.a(ID_R2_num), .b(EX_WriteReg_num), .eq(comparator_2_eq));  // open: gt, lt
  Comparator #(.width(5)) comparator_3 (.a(ID_R1_num), .b(MEM_WriteReg_num), .eq(comparator_3_eq));  // open: gt, lt
  Comparator #(.width(5)) comparator_4 (.a(ID_R2_num), .b(MEM_WriteReg_num), .eq(comparator_4_eq));  // open: gt, lt
  Comparator #(.width(5)) comparator_5 (.a(ID_R1_num), .b({5{1'b0}}), .eq(comparator_5_eq));  // open: gt, lt
  Comparator #(.width(5)) comparator_6 (.a(ID_R2_num), .b({5{1'b0}}), .eq(comparator_6_eq));  // open: gt, lt
  and and_1 (and_1_out, R1_Used, comparator_1_eq, EX_RegWrite);
  and and_2 (and_2_out, R2_Used, comparator_2_eq, EX_RegWrite);
  and and_3 (and_3_out, R1_Used, comparator_3_eq, MEM_RegWrite);
  and and_4 (and_4_out, comparator_4_eq, R2_Used, MEM_RegWrite);
  not not_1 (not_1_out, comparator_5_eq);
  and and_5 (R1_Used, not_1_out, \源寄存器使用情况_1_r1_used );
  and and_6 (R2_Used, \源寄存器使用情况_1_r2_used , not_2_out);
  not not_2 (not_2_out, comparator_6_eq);
  or or_1 (\数据相关 , and_1_out, and_2_out, and_3_out, and_4_out);

  // Other names for the same wires on the sheet: OP_CODE[5:0] = OP
endmodule

// 数据相关检测-redirect
module \数据相关检测_重定向  (
  input  [5:0] OP,
  input  [4:0] EX_WriteReg_num,
  input  EX_RegWrite,
  input  [4:0] MEM_WriteReg_num,
  input  MEM_RegWrite,
  input  [4:0] ID_R1_num,
  input  [5:0] Func,
  input  EX_MemToReg,
  input  [4:0] ID_R2_num,
  output [1:0] R1_sel,
  output [1:0] R2_sel,
  output loadUse
);

  wire and_3_out, and_4_out, comparator_1_eq, comparator_2_eq, comparator_3_eq, comparator_4_eq,
       comparator_5_eq, comparator_6_eq, not_1_out, not_2_out, or_3_out, R1_Used, R2_Used,
       \源寄存器使用情况_1_r1_used , \源寄存器使用情况_1_r2_used ;

  \源寄存器使用情况  \u_源寄存器使用情况_1  (
    .OP0(OP[0]), .OP1(OP[1]), .OP2(OP[2]), .OP3(OP[3]), .OP4(OP[4]), .OP5(OP[5]), .F0(Func[0]), .F1(Func[1]),
    .F2(Func[2]), .F3(Func[3]), .F4(Func[4]), .F5(Func[5]), .R1_Used(\源寄存器使用情况_1_r1_used ),
    .R2_Used(\源寄存器使用情况_1_r2_used ));
  Comparator #(.width(5)) comparator_1 (.a(ID_R1_num), .b(EX_WriteReg_num), .eq(comparator_1_eq));  // open: gt, lt
  Comparator #(.width(5)) comparator_2 (.a(ID_R2_num), .b(EX_WriteReg_num), .eq(comparator_2_eq));  // open: gt, lt
  Comparator #(.width(5)) comparator_3 (.a(ID_R1_num), .b(MEM_WriteReg_num), .eq(comparator_3_eq));  // open: gt, lt
  Comparator #(.width(5)) comparator_4 (.a(ID_R2_num), .b(MEM_WriteReg_num), .eq(comparator_4_eq));  // open: gt, lt
  Comparator #(.width(5)) comparator_5 (.a(ID_R1_num), .b({5{1'b0}}), .eq(comparator_5_eq));  // open: gt, lt
  Comparator #(.width(5)) comparator_6 (.a(ID_R2_num), .b({5{1'b0}}), .eq(comparator_6_eq));  // open: gt, lt
  and and_1 (R1_sel[1], R1_Used, comparator_1_eq, EX_RegWrite);
  and and_2 (R2_sel[1], R2_Used, comparator_2_eq, EX_RegWrite);
  and and_3 (and_3_out, R1_Used, comparator_3_eq, MEM_RegWrite);
  and and_4 (and_4_out, comparator_4_eq, R2_Used, MEM_RegWrite);
  not not_1 (not_1_out, comparator_5_eq);
  and and_5 (R1_Used, not_1_out, \源寄存器使用情况_1_r1_used );
  and and_6 (R2_Used, \源寄存器使用情况_1_r2_used , not_2_out);
  not not_2 (not_2_out, comparator_6_eq);
  or or_1 (R1_sel[0], R1_sel[1], and_3_out);
  or or_2 (R2_sel[0], R2_sel[1], and_4_out);
  or or_3 (or_3_out, R1_sel[1], R2_sel[1]);
  and and_7 (loadUse, or_3_out, EX_MemToReg);

  // Other names for the same wires on the sheet: OP_CODE[5:0] = OP; R1_conflict = R1_sel[0]; R2_conflict = R2_sel[0]
endmodule

// IF/ID
module IF_ID (
  input  [31:0] Insin,
  input  [31:0] PCin,
  input  PJIn,
  input  CLK,
  input  \同步清零_气泡_高电平有效 ,
  input  \使能端_低电平有效_stall_高电平有效 ,
  input  \异步清零 ,
  output [31:0] Insout,
  output [31:0] PCout,
  output PJOut
);

  wire multiplexer_3_out, not_1_out;
  wire [31:0] multiplexer_1_out, multiplexer_2_out;

  Multiplexer #(.width(32), .enable("false")) multiplexer_1 (
    .in0(Insin), .in1({32{1'b0}}), .out(multiplexer_1_out), .sel(\同步清零_气泡_高电平有效 ));
  Multiplexer #(.width(32), .enable("false")) multiplexer_2 (
    .in0(PCin), .in1({32{1'b0}}), .out(multiplexer_2_out), .sel(\同步清零_气泡_高电平有效 ));
  Multiplexer #(.enable("false")) multiplexer_3 (
    .in0(PJIn), .in1(1'b0), .out(multiplexer_3_out), .sel(\同步清零_气泡_高电平有效 ));
  not not_1 (not_1_out, \使能端_低电平有效_stall_高电平有效 );
  Register #(.width(32)) register_1 (.D(multiplexer_1_out), .en(not_1_out), .Q(Insout), .clk(CLK), .clr(\异步清零 ));
  Register #(.width(32)) register_2 (.D(multiplexer_2_out), .en(not_1_out), .Q(PCout), .clk(CLK), .clr(\异步清零 ));
  Register #(.width(1)) register_3 (.D(multiplexer_3_out), .en(not_1_out), .Q(PJOut), .clk(CLK), .clr(\异步清零 ));

  // Notes on the sheet:
  //   同步清零_气泡_高电平有效: pull=down
  //   异步清零: pull=down
  //   使能端_低电平有效_stall_高电平有效: pull=down
endmodule

// ID/EX
module ID_EX (
  input  [7:0] Intin,
  input  [7:0] WBin,
  input  [2:0] Memin,
  input  [5:0] Exin,
  input  [5:0] IFin,
  input  [25:0] Jofin,
  input  [31:0] Immin,
  input  [31:0] R1in,
  input  [31:0] R2in,
  input  [31:0] PCin,
  input  Halt,
  input  CLK,
  input  \同步清零_气泡_高电平有效 ,
  input  \使能端_低电平有效_stall_高电平有效 ,
  input  \异步清零 ,
  output [7:0] Intout,
  output [7:0] WBout,
  output [2:0] Memout,
  output [5:0] Exout,
  output [5:0] IFout,
  output [25:0] Jofout,
  output [31:0] Immout,
  output [31:0] R1out,
  output [31:0] R2out,
  output [31:0] PCout,
  output Halt_2
);

  wire multiplexer_11_out, not_1_out;
  wire [2:0] multiplexer_3_out;
  wire [5:0] multiplexer_4_out, multiplexer_5_out;
  wire [7:0] multiplexer_1_out, multiplexer_2_out;
  wire [25:0] multiplexer_6_out;
  wire [31:0] multiplexer_7_out, multiplexer_8_out, multiplexer_9_out, multiplexer_10_out;

  Multiplexer #(.width(8), .enable("false")) multiplexer_1 (
    .in0(Intin), .in1({8{1'b0}}), .out(multiplexer_1_out), .sel(\同步清零_气泡_高电平有效 ));
  Multiplexer #(.width(8), .enable("false")) multiplexer_2 (
    .in0(WBin), .in1({8{1'b0}}), .out(multiplexer_2_out), .sel(\同步清零_气泡_高电平有效 ));
  Multiplexer #(.width(3), .enable("false")) multiplexer_3 (
    .in0(Memin), .in1(3'b000), .out(multiplexer_3_out), .sel(\同步清零_气泡_高电平有效 ));
  Multiplexer #(.width(6), .enable("false")) multiplexer_4 (
    .in0(Exin), .in1({6{1'b0}}), .out(multiplexer_4_out), .sel(\同步清零_气泡_高电平有效 ));
  Multiplexer #(.width(6), .enable("false")) multiplexer_5 (
    .in0(IFin), .in1({6{1'b0}}), .out(multiplexer_5_out), .sel(\同步清零_气泡_高电平有效 ));
  Multiplexer #(.width(26), .enable("false")) multiplexer_6 (
    .in0(Jofin), .in1({26{1'b0}}), .out(multiplexer_6_out), .sel(\同步清零_气泡_高电平有效 ));
  Multiplexer #(.width(32), .enable("false")) multiplexer_7 (
    .in0(Immin), .in1({32{1'b0}}), .out(multiplexer_7_out), .sel(\同步清零_气泡_高电平有效 ));
  Multiplexer #(.width(32), .enable("false")) multiplexer_8 (
    .in0(R1in), .in1({32{1'b0}}), .out(multiplexer_8_out), .sel(\同步清零_气泡_高电平有效 ));
  Multiplexer #(.width(32), .enable("false")) multiplexer_9 (
    .in0(R2in), .in1({32{1'b0}}), .out(multiplexer_9_out), .sel(\同步清零_气泡_高电平有效 ));
  Multiplexer #(.width(32), .enable("false")) multiplexer_10 (
    .in0(PCin), .in1({32{1'b0}}), .out(multiplexer_10_out), .sel(\同步清零_气泡_高电平有效 ));
  Multiplexer #(.enable("false")) multiplexer_11 (
    .in0(Halt), .in1(1'b0), .out(multiplexer_11_out), .sel(\同步清零_气泡_高电平有效 ));
  not not_1 (not_1_out, \使能端_低电平有效_stall_高电平有效 );
  Register register_1 (.D(multiplexer_1_out), .en(not_1_out), .Q(Intout), .clk(CLK), .clr(\异步清零 ));
  Register register_2 (.D(multiplexer_2_out), .en(not_1_out), .Q(WBout), .clk(CLK), .clr(\异步清零 ));
  Register #(.width(3)) register_3 (.D(multiplexer_3_out), .en(not_1_out), .Q(Memout), .clk(CLK), .clr(\异步清零 ));
  Register #(.width(6)) register_4 (.D(multiplexer_4_out), .en(not_1_out), .Q(Exout), .clk(CLK), .clr(\异步清零 ));
  Register #(.width(6)) register_5 (.D(multiplexer_5_out), .en(not_1_out), .Q(IFout), .clk(CLK), .clr(\异步清零 ));
  Register #(.width(26)) register_6 (.D(multiplexer_6_out), .en(not_1_out), .Q(Jofout), .clk(CLK), .clr(\异步清零 ));
  Register #(.width(32)) register_7 (.D(multiplexer_7_out), .en(not_1_out), .Q(Immout), .clk(CLK), .clr(\异步清零 ));
  Register #(.width(32)) register_8 (.D(multiplexer_8_out), .en(not_1_out), .Q(R1out), .clk(CLK), .clr(\异步清零 ));
  Register #(.width(32)) register_9 (.D(multiplexer_9_out), .en(not_1_out), .Q(R2out), .clk(CLK), .clr(\异步清零 ));
  Register #(.width(32)) register_10 (.D(multiplexer_10_out), .en(not_1_out), .Q(PCout), .clk(CLK), .clr(\异步清零 ));
  Register #(.width(1)) register_11 (.D(multiplexer_11_out), .en(not_1_out), .Q(Halt_2), .clk(CLK), .clr(\异步清零 ));

  // Notes on the sheet:
  //   使能端_低电平有效_stall_高电平有效: pull=down
  //   异步清零: pull=down
  //   同步清零_气泡_高电平有效: pull=down
endmodule

// ID/EX-redirect
module ID_EX_redirect (
  input  [3:0] Sel_in,
  input  [7:0] WBin,
  input  [7:0] Intin,
  input  [2:0] Memin,
  input  [5:0] Exin,
  input  [5:0] IFin,
  input  [25:0] Jofin,
  input  [31:0] Immin,
  input  [31:0] R1in,
  input  [31:0] R2in,
  input  [31:0] PCin,
  input  Halt,
  input  PJin,
  input  CLK,
  input  \同步清零_气泡_高电平有效 ,
  input  \使能端_低电平有效_stall_高电平有效 ,
  input  \异步清零 ,
  output [3:0] Sel_out,
  output [7:0] WBout,
  output [7:0] Intout,
  output [2:0] Memout,
  output [5:0] Exout,
  output [5:0] IFout,
  output [25:0] Jofout,
  output [31:0] Immout,
  output [31:0] R1out,
  output [31:0] R2out,
  output [31:0] PCout,
  output Halt_2,
  output PJOut
);

  wire multiplexer_12_out, multiplexer_13_out, not_1_out;
  wire [2:0] multiplexer_4_out;
  wire [3:0] multiplexer_1_out;
  wire [5:0] multiplexer_5_out, multiplexer_6_out;
  wire [7:0] multiplexer_2_out, multiplexer_3_out;
  wire [25:0] multiplexer_7_out;
  wire [31:0] multiplexer_8_out, multiplexer_9_out, multiplexer_10_out, multiplexer_11_out;

  Multiplexer #(.width(4), .enable("false")) multiplexer_1 (
    .in0(Sel_in), .in1(4'b0000), .out(multiplexer_1_out), .sel(\同步清零_气泡_高电平有效 ));
  Multiplexer #(.width(8), .enable("false")) multiplexer_2 (
    .in0(WBin), .in1({8{1'b0}}), .out(multiplexer_2_out), .sel(\同步清零_气泡_高电平有效 ));
  Multiplexer #(.width(8), .enable("false")) multiplexer_3 (
    .in0(Intin), .in1({8{1'b0}}), .out(multiplexer_3_out), .sel(\同步清零_气泡_高电平有效 ));
  Multiplexer #(.width(3), .enable("false")) multiplexer_4 (
    .in0(Memin), .in1(3'b000), .out(multiplexer_4_out), .sel(\同步清零_气泡_高电平有效 ));
  Multiplexer #(.width(6), .enable("false")) multiplexer_5 (
    .in0(Exin), .in1({6{1'b0}}), .out(multiplexer_5_out), .sel(\同步清零_气泡_高电平有效 ));
  Multiplexer #(.width(6), .enable("false")) multiplexer_6 (
    .in0(IFin), .in1({6{1'b0}}), .out(multiplexer_6_out), .sel(\同步清零_气泡_高电平有效 ));
  Multiplexer #(.width(26), .enable("false")) multiplexer_7 (
    .in0(Jofin), .in1({26{1'b0}}), .out(multiplexer_7_out), .sel(\同步清零_气泡_高电平有效 ));
  Multiplexer #(.width(32), .enable("false")) multiplexer_8 (
    .in0(Immin), .in1({32{1'b0}}), .out(multiplexer_8_out), .sel(\同步清零_气泡_高电平有效 ));
  Multiplexer #(.width(32), .enable("false")) multiplexer_9 (
    .in0(R1in), .in1({32{1'b0}}), .out(multiplexer_9_out), .sel(\同步清零_气泡_高电平有效 ));
  Multiplexer #(.width(32), .enable("false")) multiplexer_10 (
    .in0(R2in), .in1({32{1'b0}}), .out(multiplexer_10_out), .sel(\同步清零_气泡_高电平有效 ));
  Multiplexer #(.width(32), .enable("false")) multiplexer_11 (
    .in0(PCin), .in1({32{1'b0}}), .out(multiplexer_11_out), .sel(\同步清零_气泡_高电平有效 ));
  Multiplexer #(.enable("false")) multiplexer_12 (
    .in0(Halt), .in1(1'b0), .out(multiplexer_12_out), .sel(\同步清零_气泡_高电平有效 ));
  Multiplexer #(.enable("false")) multiplexer_13 (
    .in0(PJin), .in1(1'b0), .out(multiplexer_13_out), .sel(\同步清零_气泡_高电平有效 ));
  not not_1 (not_1_out, \使能端_低电平有效_stall_高电平有效 );
  Register #(.width(4)) register_1 (.D(multiplexer_1_out), .en(not_1_out), .Q(Sel_out), .clk(CLK), .clr(\异步清零 ));
  Register register_2 (.D(multiplexer_2_out), .en(not_1_out), .Q(WBout), .clk(CLK));  // open: clr
  Register register_3 (.D(multiplexer_3_out), .en(not_1_out), .Q(Intout), .clk(CLK), .clr(\异步清零 ));
  Register #(.width(3)) register_4 (.D(multiplexer_4_out), .en(not_1_out), .Q(Memout), .clk(CLK), .clr(\异步清零 ));
  Register #(.width(6)) register_5 (.D(multiplexer_5_out), .en(not_1_out), .Q(Exout), .clk(CLK), .clr(\异步清零 ));
  Register #(.width(6)) register_6 (.D(multiplexer_6_out), .en(not_1_out), .Q(IFout), .clk(CLK), .clr(\异步清零 ));
  Register #(.width(26)) register_7 (.D(multiplexer_7_out), .en(not_1_out), .Q(Jofout), .clk(CLK), .clr(\异步清零 ));
  Register #(.width(32)) register_8 (.D(multiplexer_8_out), .en(not_1_out), .Q(Immout), .clk(CLK), .clr(\异步清零 ));
  Register #(.width(32)) register_9 (.D(multiplexer_9_out), .en(not_1_out), .Q(R1out), .clk(CLK), .clr(\异步清零 ));
  Register #(.width(32)) register_10 (.D(multiplexer_10_out), .en(not_1_out), .Q(R2out), .clk(CLK), .clr(\异步清零 ));
  Register #(.width(32)) register_11 (.D(multiplexer_11_out), .en(not_1_out), .Q(PCout), .clk(CLK), .clr(\异步清零 ));
  Register #(.width(1)) register_12 (.D(multiplexer_12_out), .en(not_1_out), .Q(Halt_2), .clk(CLK), .clr(\异步清零 ));
  Register #(.width(1)) register_13 (.D(multiplexer_13_out), .en(not_1_out), .Q(PJOut), .clk(CLK), .clr(\异步清零 ));

  // Notes on the sheet:
  //   使能端_低电平有效_stall_高电平有效: pull=down
  //   异步清零: pull=down
  //   同步清零_气泡_高电平有效: pull=down
endmodule

// EX/MEM
module EX_MEM (
  input  [7:0] Intin,
  input  [7:0] WBin,
  input  [2:0] Memin,
  input  [31:0] Resin,
  input  [31:0] R1in,
  input  [31:0] R2in,
  input  [31:0] PCin,
  input  Halt,
  input  CLK,
  input  \同步清零_气泡_高电平有效 ,
  input  \使能端_低电平有效_stall_高电平有效 ,
  input  \异步清零 ,
  output [7:0] Intout,
  output [7:0] WBout,
  output [2:0] Memout,
  output [31:0] Resout,
  output [31:0] R1out,
  output [31:0] R2out,
  output [31:0] PCout,
  output Halt_2
);

  wire multiplexer_8_out, not_1_out;
  wire [2:0] multiplexer_3_out;
  wire [7:0] multiplexer_1_out, multiplexer_2_out;
  wire [31:0] multiplexer_4_out, multiplexer_5_out, multiplexer_6_out, multiplexer_7_out;

  Multiplexer #(.width(8), .enable("false")) multiplexer_1 (
    .in0(Intin), .in1({8{1'b0}}), .out(multiplexer_1_out), .sel(\同步清零_气泡_高电平有效 ));
  Multiplexer #(.width(8), .enable("false")) multiplexer_2 (
    .in0(WBin), .in1({8{1'b0}}), .out(multiplexer_2_out), .sel(\同步清零_气泡_高电平有效 ));
  Multiplexer #(.width(3), .enable("false")) multiplexer_3 (
    .in0(Memin), .in1(3'b000), .out(multiplexer_3_out), .sel(\同步清零_气泡_高电平有效 ));
  Multiplexer #(.width(32), .enable("false")) multiplexer_4 (
    .in0(Resin), .in1({32{1'b0}}), .out(multiplexer_4_out), .sel(\同步清零_气泡_高电平有效 ));
  Multiplexer #(.width(32), .enable("false")) multiplexer_5 (
    .in0(R1in), .in1({32{1'b0}}), .out(multiplexer_5_out), .sel(\同步清零_气泡_高电平有效 ));
  Multiplexer #(.width(32), .enable("false")) multiplexer_6 (
    .in0(R2in), .in1({32{1'b0}}), .out(multiplexer_6_out), .sel(\同步清零_气泡_高电平有效 ));
  Multiplexer #(.width(32), .enable("false")) multiplexer_7 (
    .in0(PCin), .in1({32{1'b0}}), .out(multiplexer_7_out), .sel(\同步清零_气泡_高电平有效 ));
  Multiplexer #(.enable("false")) multiplexer_8 (
    .in0(Halt), .in1(1'b0), .out(multiplexer_8_out), .sel(\同步清零_气泡_高电平有效 ));
  not not_1 (not_1_out, \使能端_低电平有效_stall_高电平有效 );
  Register register_1 (.D(multiplexer_1_out), .en(not_1_out), .Q(Intout), .clk(CLK), .clr(\异步清零 ));
  Register register_2 (.D(multiplexer_2_out), .en(not_1_out), .Q(WBout), .clk(CLK), .clr(\异步清零 ));
  Register #(.width(3)) register_3 (.D(multiplexer_3_out), .en(not_1_out), .Q(Memout), .clk(CLK), .clr(\异步清零 ));
  Register #(.width(32)) register_4 (.D(multiplexer_4_out), .en(not_1_out), .Q(Resout), .clk(CLK), .clr(\异步清零 ));
  Register #(.width(32)) register_5 (.D(multiplexer_5_out), .en(not_1_out), .Q(R1out), .clk(CLK), .clr(\异步清零 ));
  Register #(.width(32)) register_6 (.D(multiplexer_6_out), .en(not_1_out), .Q(R2out), .clk(CLK), .clr(\异步清零 ));
  Register #(.width(32)) register_7 (.D(multiplexer_7_out), .en(not_1_out), .Q(PCout), .clk(CLK), .clr(\异步清零 ));
  Register #(.width(1)) register_8 (.D(multiplexer_8_out), .en(not_1_out), .Q(Halt_2), .clk(CLK), .clr(\异步清零 ));

  // Notes on the sheet:
  //   使能端_低电平有效_stall_高电平有效: pull=down
  //   异步清零: pull=down
  //   同步清零_气泡_高电平有效: pull=down
endmodule

// MEM/WB
module MEM_WB (
  input  [7:0] Intin,
  input  [7:0] WBin,
  input  [31:0] memin,
  input  [31:0] R1in,
  input  [31:0] R2in,
  input  [31:0] Resin,
  input  [31:0] PCin,
  input  Halt,
  input  CLK,
  input  \同步清零_气泡_高电平有效 ,
  input  \使能端_低电平有效_stall_高电平有效 ,
  input  \异步清零 ,
  output [7:0] Intout,
  output [7:0] WBout,
  output [31:0] memout,
  output [31:0] R1out,
  output [31:0] R2out,
  output [31:0] Resout,
  output [31:0] PCout,
  output Halt_2
);

  wire multiplexer_8_out, not_1_out;
  wire [7:0] multiplexer_1_out, multiplexer_2_out;
  wire [31:0] multiplexer_3_out, multiplexer_4_out, multiplexer_5_out, multiplexer_6_out, multiplexer_7_out;

  Multiplexer #(.width(8), .enable("false")) multiplexer_1 (
    .in0(Intin), .in1({8{1'b0}}), .out(multiplexer_1_out), .sel(\同步清零_气泡_高电平有效 ));
  Multiplexer #(.width(8), .enable("false")) multiplexer_2 (
    .in0(WBin), .in1({8{1'b0}}), .out(multiplexer_2_out), .sel(\同步清零_气泡_高电平有效 ));
  Multiplexer #(.width(32), .enable("false")) multiplexer_3 (
    .in0(memin), .in1({32{1'b0}}), .out(multiplexer_3_out), .sel(\同步清零_气泡_高电平有效 ));
  Multiplexer #(.width(32), .enable("false")) multiplexer_4 (
    .in0(R1in), .in1({32{1'b0}}), .out(multiplexer_4_out), .sel(\同步清零_气泡_高电平有效 ));
  Multiplexer #(.width(32), .enable("false")) multiplexer_5 (
    .in0(R2in), .in1({32{1'b0}}), .out(multiplexer_5_out), .sel(\同步清零_气泡_高电平有效 ));
  Multiplexer #(.width(32), .enable("false")) multiplexer_6 (
    .in0(Resin), .in1({32{1'b0}}), .out(multiplexer_6_out), .sel(\同步清零_气泡_高电平有效 ));
  Multiplexer #(.width(32), .enable("false")) multiplexer_7 (
    .in0(PCin), .in1({32{1'b0}}), .out(multiplexer_7_out), .sel(\同步清零_气泡_高电平有效 ));
  Multiplexer #(.enable("false")) multiplexer_8 (
    .in0(Halt), .in1(1'b0), .out(multiplexer_8_out), .sel(\同步清零_气泡_高电平有效 ));
  not not_1 (not_1_out, \使能端_低电平有效_stall_高电平有效 );
  Register register_1 (.D(multiplexer_1_out), .en(not_1_out), .Q(Intout), .clk(CLK), .clr(\异步清零 ));
  Register register_2 (.D(multiplexer_2_out), .en(not_1_out), .Q(WBout), .clk(CLK), .clr(\异步清零 ));
  Register #(.width(32)) register_3 (.D(multiplexer_3_out), .en(not_1_out), .Q(memout), .clk(CLK), .clr(\异步清零 ));
  Register #(.width(32)) register_4 (.D(multiplexer_4_out), .en(not_1_out), .Q(R1out), .clk(CLK), .clr(\异步清零 ));
  Register #(.width(32)) register_5 (.D(multiplexer_5_out), .en(not_1_out), .Q(R2out), .clk(CLK), .clr(\异步清零 ));
  Register #(.width(32)) register_6 (.D(multiplexer_6_out), .en(not_1_out), .Q(Resout), .clk(CLK), .clr(\异步清零 ));
  Register #(.width(32)) register_7 (.D(multiplexer_7_out), .en(not_1_out), .Q(PCout), .clk(CLK), .clr(\异步清零 ));
  Register #(.width(1)) register_8 (.D(multiplexer_8_out), .en(not_1_out), .Q(Halt_2), .clk(CLK), .clr(\异步清零 ));

  // Notes on the sheet:
  //   同步清零_气泡_高电平有效: pull=down
  //   异步清零: pull=down
  //   使能端_低电平有效_stall_高电平有效: pull=down
endmodule

module \气泡流水线  (
);

  wire and_1_out, and_2_out, and_3_out, and_4_out, and_5_out, and_6_out, and_8_out, and_9_out, and_13_out,
       and_14_out, and_15_out, and_16_out, and_17_out, and_18_out, and_19_out, and_20_out, and_21_out,
       and_22_out, and_23_out, bgtz, CLK, comparator_1_eq, comparator_2_eq, comparator_3_gt, comparator_4_eq,
       comparator_5_eq, comparator_6_gt, comparator_7_eq, d_ff_1_q, d_ff_2_q, d_ff_3_q, d_ff_4_q, d_ff_5_q,
       d_ff_6_q, demultiplexer_1_out1, demultiplexer_1_out2, demultiplexer_1_out3, Equ, eret, ereti,
       ex_mem_1_halt_2, ext, Go, halt, id_ex_1_halt_2, IE, IR1, IR2, IR3, j, JAL, jr, Jump, MFC0, MTC0,
       MTC0id, nohalt, or_1_out, or_5_out, or_6_out, or_7_out, or_8_out, or_9_out, or_10_out, or_11_out,
       or_12_out, or_13_out, or_14_out, or_15_out, or_18_out, or_20_out, or_21_out, priority_encoder_1_gs,
       regDst, registerfile_1_p3, related, RST, sh, srlv, syscall, W1, W2, W3, \中断请求 , \同步清零1 , \同步清零2 ,
       \同步清零3 , \硬布线控制器_1_syscall ;
  wire [0:0] \硬布线控制器_1_mfc0 ;
  wire [1:0] IR, multiplexer_11_out, \中断编号 , \硬布线控制器_1_regwrite ;
  wire [1:1] \硬布线控制器_1_memwrite ;
  wire [2:0] ex_mem_1_memout, id_ex_1_memout, id_ex_1_wbout, or_16_out;
  wire [3:0] id_ex_1_exout, multiplexer_16_out, multiplexer_17_out, \硬布线控制器_1_alu_op ;
  wire [4:0] edID, id_ex_1_immout_2, id_ex_1_r1out, id_ex_1_wbout_2, multiplexer_6_out, multiplexer_13_out,
       R1id, R2id, rd, rW;
  wire [4:3] \硬布线控制器_1_beq ;
  wire [4:4] \硬布线控制器_1_alu_src ;
  wire [5:0] func, id_ex_1_ifout, op;
  wire [5:4] id_ex_1_exout_2;
  wire [7:0] ex_mem_1_intout, ex_mem_1_wbout, id_ex_1_intout, mem_wb_1_wbout;
  wire [15:0] adder_5_out, \总周期数 , \插入气泡数 , \无条件分支数 , \条件分支成功数 ;
  wire [25:6] if_id_1_insout;
  wire [27:2] id_ex_1_jofout;
  wire [31:0] adder_2_out, adder_3_out, adder_4_out, and_24_out, and_25_out, and_26_out, and_27_out,
       and_28_out, copro, EPC, ex_mem_1_r1out, ex_mem_1_r2out, ex_mem_1_resout, EX_PC, id_ex_1_immout,
       id_ex_1_r2out, ID_PC, IF_PC, IntVec, LedData, MEM_PC, mem_wb_1_memout, mem_wb_1_resout,
       mips_alu_1_result, mips_ram_1_p2, mips_ram_1_p8, multiplexer_1_out, multiplexer_2_out,
       multiplexer_4_out, multiplexer_7_out, multiplexer_12_out, multiplexer_19_out, multiplexer_20_out,
       PC_4, PCin, PCinCom, R1, R2, registerfile_1_p1, registerfile_1_p7, registerfile_1_p8, rom_1_data,
       shifter_1_out, shifter_2_out, shifter_3_out, WB_PC;
  wire [31:5] id_ex_1_r1out_2;

  Button \u_总复位  (.out(RST));
  Button _1 (.out(IR1));
  Button _2 (.out(IR2));
  Button _3 (.out(IR3));
  Button \u_继续运行  (.out(Go));
  LED led_1 (.in(W1));
  LED led_2 (.in(W2));
  LED led_3 (.in(W3));
  and and_1 (and_1_out, ~halt, or_1_out);  // AND_Gate
  or or_1 (or_1_out, Jump, ~related, \中断请求 , eret);  // OR_Gate
  or or_2 (W1, d_ff_4_q, d_ff_1_q);
  or or_3 (W2, d_ff_5_q, d_ff_2_q);
  or or_4 (W3, d_ff_6_q, d_ff_3_q);
  Comparator #(.width(5), .mode("unsigned")) comparator_1 (.a(rd), .b(5'b01100), .eq(comparator_1_eq));  // open: gt, lt
  Hex_Digit_Display hex_digit_display_1 (.value(LedData[31:28]));  // open: dp
  Register #(.width(32)) PC (.D(PCin), .en(and_1_out), .Q(IF_PC), .clk(CLK), .clr(RST));
  Multiplexer #(.width(32), .enable("false")) multiplexer_1 (
    .in0(PC_4), .in1(PCinCom), .out(multiplexer_1_out), .sel(Jump));
  D_Flip_Flop d_ff_1 (.clk(IR1), .D(1'b1), .Q(d_ff_1_q), .reset(d_ff_4_q));  // open: Qn, preset, en
  D_Flip_Flop d_ff_2 (.clk(IR2), .D(1'b1), .Q(d_ff_2_q), .reset(d_ff_5_q));  // open: Qn, preset, en
  D_Flip_Flop d_ff_3 (.clk(IR3), .D(1'b1), .Q(d_ff_3_q), .reset(d_ff_6_q));  // open: Qn, preset, en
  or or_5 (or_5_out, d_ff_3_q, d_ff_6_q);
  and and_2 (and_2_out, MTC0, comparator_1_eq);
  Hex_Digit_Display hex_digit_display_2 (.value(LedData[23:20]));  // open: dp
  Hex_Digit_Display hex_digit_display_3 (.value(LedData[27:24]));  // open: dp
  Adder #(.width(32)) adder_1 (.a(IF_PC), .b(32'h4), .out(PC_4));  // open: cin, cout
  Multiplexer #(.width(32), .enable("false")) multiplexer_2 (
    .in0(multiplexer_1_out), .in1(IntVec), .out(multiplexer_2_out), .sel(\中断请求 ));
  or or_6 (or_6_out, d_ff_1_q, d_ff_4_q);
  and and_3 (and_3_out, or_6_out, ~\同步清零1 );  // AND_Gate
  or or_7 (or_7_out, d_ff_2_q, d_ff_5_q);
  and and_4 (and_4_out, or_7_out, ~\同步清零2 );  // AND_Gate
  and and_5 (and_5_out, or_5_out, ~\同步清零3 );  // AND_Gate
  or or_8 (or_8_out, \中断请求 , eret, and_2_out);
  Hex_Digit_Display hex_digit_display_4 (.value(LedData[19:16]));  // open: dp
  Hex_Digit_Display hex_digit_display_5 (.value(LedData[15:12]));  // open: dp
  IF_ID if_id_1 (
    .Insin(rom_1_data), .PCin(IF_PC), .CLK(CLK),
    .Insout({op, if_id_1_insout[25:16], edID, if_id_1_insout[10:6], func}), .PCout(ID_PC),
    .\同步清零_气泡_高电平有效 (or_11_out), .\使能端_低电平有效_stall_高电平有效 (or_9_out), .\异步清零 (RST));  // open: PJIn, PJOut
  ROM #(.addrWidth(10), .dataWidth(32)) rom_1 (.addr(IF_PC[11:2]), .data(rom_1_data), .sel(1'b1));
  or or_9 (or_9_out, ~or_10_out, halt);  // OR_Gate
  or or_10 (or_10_out, Jump, ~related);  // OR_Gate
  or or_11 (or_11_out, \中断请求 , eret, Jump);
  Multiplexer #(.width(32), .enable("false")) multiplexer_3 (
    .in0(multiplexer_2_out), .in1(EPC), .out(PCin), .sel(eret));
  D_Flip_Flop d_ff_4 (.clk(CLK), .D(and_3_out), .Q(d_ff_4_q));  // open: Qn, preset, en, reset
  D_Flip_Flop d_ff_5 (.clk(CLK), .D(and_4_out), .Q(d_ff_5_q));  // open: Qn, preset, en, reset
  D_Flip_Flop d_ff_6 (.clk(CLK), .D(and_5_out), .Q(d_ff_6_q));  // open: Qn, preset, en, reset
  D_Flip_Flop d_ff_7 (.clk(CLK), .D(IE), .Qn(IE), .en(or_8_out), .reset(RST));  // open: Q, preset
  Comparator #(.width(5), .mode("unsigned")) comparator_2 (.a(rd), .b(5'b01110), .eq(comparator_2_eq));  // open: gt, lt
  Hex_Digit_Display hex_digit_display_6 (.value(LedData[7:4]));  // open: dp
  Hex_Digit_Display hex_digit_display_7 (.value(LedData[11:8]));  // open: dp
  Clock clock_1 (.out(CLK));
  and and_6 (and_6_out, MTC0, comparator_2_eq);
  Hex_Digit_Display hex_digit_display_8 (.value(LedData[3:0]));  // open: dp
  \硬布线控制器  \u_硬布线控制器_1  (
    .Func(func), .OP(op), .ALU_OP(\硬布线控制器_1_alu_op ), .MemToReg(\硬布线控制器_1_regwrite [0]),
    .MemWrite(\硬布线控制器_1_memwrite [1]), .ALU_SRC(\硬布线控制器_1_alu_src [4]), .RegWrite(\硬布线控制器_1_regwrite [1]),
    .SysCALL(\硬布线控制器_1_syscall ), .SignedExt(ext), .RegDst(regDst), .JR(jr), .JMP(j),
    .Beq(\硬布线控制器_1_beq [3]), .JAL(JAL), .Bne(\硬布线控制器_1_beq [4]), .SH(sh), .BGTZ(bgtz), .SRLV(srlv),
    .ERET(ereti), .RS(if_id_1_insout[25:21]), .MFC0(\硬布线控制器_1_mfc0 [0]), .MTC0(MTC0id));
  Priority_Encoder #(.select(2)) priority_encoder_1 (
    .in0(1'b1), .in1(d_ff_4_q), .in2(d_ff_5_q), .in3(d_ff_6_q), .out(\中断编号 ), .gs(priority_encoder_1_gs),
    .en_in(1'b1));  // open: en_out
  Comparator #(.width(2), .mode("unsigned")) comparator_3 (.a(\中断编号 ), .b(IR), .gt(comparator_3_gt));  // open: eq, lt
  Multiplexer #(.width(32), .enable("false")) multiplexer_4 (
    .in0(MEM_PC), .in1(R2), .out(multiplexer_4_out), .sel(and_6_out));
  or or_12 (or_12_out, \中断请求 , and_6_out);
  and and_7 (\中断请求 , priority_encoder_1_gs, IE, comparator_3_gt);
  Register #(.width(32)) u_EPC (.D(multiplexer_4_out), .en(or_12_out), .Q(EPC), .clk(CLK), .clr(RST));
  // Probe on \总周期数 
  // Probe on \无条件分支数 
  // Probe on \条件分支成功数 
  // Probe on \插入气泡数 
  // Probe on {16{1'b0}}
  Shifter #(.width(32), .shift("ar")) shifter_1 (
    .in({edID, if_id_1_insout[10:6], func, {16{1'b0}}}), .\dist (5'b10000), .out(shifter_1_out));
  Multiplexer #(.width(5), .enable("false")) multiplexer_5 (
    .in0(if_id_1_insout[25:21]), .in1(5'b00010), .out(R1id), .sel(\硬布线控制器_1_syscall ));
  Multiplexer #(.width(5), .enable("false")) multiplexer_6 (
    .in0(if_id_1_insout[20:16]), .in1(edID), .out(multiplexer_6_out), .sel(regDst));
  Comparator #(.width(5), .mode("unsigned")) comparator_4 (.a(rd), .b(5'b01000), .eq(comparator_4_eq));  // open: gt, lt
  // Probe on IF_PC[11:0]
  Multiplexer #(.width(32), .enable("false")) multiplexer_7 (
    .in0({{16{1'b0}}, edID, if_id_1_insout[10:6], func}), .in1(shifter_1_out), .out(multiplexer_7_out),
    .sel(ext));
  // RegisterFile registerfile_1: pin names not known; wires that end beside it: registerfile_1_p1, CLK, registerfile_1_p3, mem_wb_1_wbout[7:3], R1id, R2id, registerfile_1_p7, registerfile_1_p8
  Multiplexer #(.width(5), .enable("false")) multiplexer_8 (
    .in0(if_id_1_insout[20:16]), .in1(5'b00100), .out(R2id), .sel(\硬布线控制器_1_syscall ));
  Multiplexer #(.width(5), .enable("false")) multiplexer_9 (
    .in0(multiplexer_6_out), .in1({5{1'b1}}), .out(rW), .sel(JAL));
  Comparator #(.width(32)) comparator_5 (.a(R1), .b(32'h22), .eq(comparator_5_eq));  // open: gt, lt
  and and_8 (and_8_out, MFC0, comparator_4_eq);
  and and_9 (and_9_out, MTC0, comparator_4_eq);
  Demultiplexer #(.select(2), .enable("false")) demultiplexer_1 (
    .out1(demultiplexer_1_out1), .out2(demultiplexer_1_out2), .out3(demultiplexer_1_out3), .in(1'b1), .sel(IR));  // open: out0
  // Probe on ID_PC[11:0]
  ID_EX id_ex_1 (
    .WBin({rW, JAL, \硬布线控制器_1_regwrite }), .Memin({sh, \硬布线控制器_1_memwrite [1], \硬布线控制器_1_regwrite [0]}),
    .R1in(registerfile_1_p7), .R2in(registerfile_1_p8), .CLK(CLK), .WBout({id_ex_1_wbout_2, id_ex_1_wbout}),
    .Memout(id_ex_1_memout), .R1out({id_ex_1_r1out_2, id_ex_1_r1out}), .R2out(id_ex_1_r2out),
    .\同步清零_气泡_高电平有效 (or_13_out), .\使能端_低电平有效_stall_高电平有效 (halt), .PCin(ID_PC), .PCout(EX_PC),
    .Immin(multiplexer_7_out), .Immout({id_ex_1_immout[31:11], id_ex_1_immout_2, id_ex_1_immout[5:0]}),
    .Jofin({if_id_1_insout[25:16], edID, if_id_1_insout[10:6], func}), .Jofout(id_ex_1_jofout),
    .IFout({id_ex_1_ifout[5:2], or_16_out[1], id_ex_1_ifout[0]}), .IFin({JAL, \硬布线控制器_1_beq , bgtz, jr, j}),
    .Exin({srlv, \硬布线控制器_1_alu_src [4], \硬布线控制器_1_alu_op }), .Exout({id_ex_1_exout_2, id_ex_1_exout}),
    .\异步清零 (RST), .Halt(\硬布线控制器_1_syscall ), .Halt_2(id_ex_1_halt_2),
    .Intin({edID, ereti, MTC0id, \硬布线控制器_1_mfc0 [0]}), .Intout(id_ex_1_intout));
  or or_13 (or_13_out, \中断请求 , Jump, related, eret);
  Multiplexer #(.select(2), .width(32), .enable("false")) multiplexer_10 (
    .in0(32'h3310), .in1(32'h10), .in2(32'h3110), .in3(32'h3210), .out(IntVec), .sel(\中断编号 ));
  Multiplexer #(.width(2), .enable("false")) multiplexer_11 (
    .in0(\中断编号 ), .in1(R2[1:0]), .out(multiplexer_11_out), .sel(and_9_out));
  or or_14 (or_14_out, and_8_out, and_9_out);
  and and_10 (\同步清零1 , and_9_out, demultiplexer_1_out1);
  and and_11 (\同步清零2 , demultiplexer_1_out2, and_9_out);
  and and_12 (\同步清零3 , demultiplexer_1_out3, and_9_out);
  // Probe on EX_PC[11:0]
  // Probe on MEM_PC[11:0]
  \数据相关检测  \u_数据相关检测_1  (
    .OP(op), .EX_WriteReg_num(id_ex_1_wbout_2), .EX_RegWrite(id_ex_1_wbout[1]),
    .MEM_WriteReg_num(ex_mem_1_wbout[7:3]), .MEM_RegWrite(ex_mem_1_wbout[1]), .\数据相关 (related), .Func(func),
    .ID_R1_num(R1id), .ID_R2_num(R2id));
  and and_13 (and_13_out, comparator_5_eq, syscall);
  and and_14 (and_14_out, ~comparator_5_eq, syscall);  // AND_Gate
  or or_15 (or_15_out, Go, RST);
  Register #(.width(2)) u_IR (.D(multiplexer_11_out), .en(or_14_out), .Q(IR), .clk(CLK), .clr(RST));
  // Probe on WB_PC[11:0]
  Adder #(.width(32)) adder_2 (.a(EX_PC), .b(32'h4), .out(adder_2_out));  // open: cin, cout
  Register #(.width(32)) register_1 (.D(R2), .en(and_13_out), .Q(LedData), .clk(and_13_out), .clr(RST));
  D_Flip_Flop d_ff_8 (.clk(CLK), .D(and_14_out), .Q(halt), .Qn(nohalt), .preset(1'b0), .en(nohalt), .reset(or_15_out));
  Multiplexer #(.width(32), .enable("false")) multiplexer_12 (
    .in0(id_ex_1_r2out), .in1({id_ex_1_immout[31:11], id_ex_1_immout_2, id_ex_1_immout[5:0]}),
    .out(multiplexer_12_out), .sel(id_ex_1_exout_2[4]));
  Multiplexer #(.width(5), .enable("false")) multiplexer_13 (
    .in0(id_ex_1_immout_2), .in1(id_ex_1_r1out), .out(multiplexer_13_out), .sel(id_ex_1_exout_2[5]));
  Shifter #(.width(32)) shifter_2 (
    .in({id_ex_1_immout[31:11], id_ex_1_immout_2, id_ex_1_immout[5:0]}), .\dist (5'b00010),
    .out(shifter_2_out));
  and and_15 (and_15_out, id_ex_1_ifout[3], Equ);
  and and_16 (and_16_out, id_ex_1_ifout[4], ~Equ);  // AND_Gate
  and and_17 (and_17_out, id_ex_1_ifout[2], comparator_6_gt);
  Comparator #(.width(32)) comparator_6 (
    .a({id_ex_1_r1out_2, id_ex_1_r1out}), .b({32{1'b0}}), .gt(comparator_6_gt));  // open: eq, lt
  Comparator #(.width(5), .mode("unsigned")) comparator_7 (.a(rd), .b(5'b01110), .eq(comparator_7_eq));  // open: gt, lt
  LED led_4 (.in(\中断请求 ));
  // Probe on \中断编号 
  // Probe on IR
  LED led_5 (.in(IE));
  MIPS_ALU mips_alu_1 (
    .X({id_ex_1_r1out_2, id_ex_1_r1out}), .Y(multiplexer_12_out), .AluOP(id_ex_1_exout), .Equal(Equ),
    .Result(mips_alu_1_result), .shamt(multiplexer_13_out));  // open: Result_2
  Adder #(.width(32)) adder_3 (.a(adder_2_out), .b(shifter_2_out), .out(adder_3_out));  // open: cin, cout
  or or_16 (or_16_out[0], id_ex_1_ifout[0], id_ex_1_ifout[5]);
  or or_17 (or_16_out[2], and_15_out, and_16_out, and_17_out);
  and and_18 (and_18_out, nohalt, ~\中断请求 );  // AND_Gate
  and and_19 (and_19_out, ~Jump, related);  // AND_Gate
  Multiplexer #(.width(32), .enable("false")) multiplexer_14 (
    .in0({{30{1'b0}}, IR}), .in1(EPC), .out(copro), .sel(comparator_7_eq));
  EX_MEM ex_mem_1 (
    .WBin({id_ex_1_wbout_2, id_ex_1_wbout}), .WBout(ex_mem_1_wbout), .Memin(id_ex_1_memout),
    .Memout(ex_mem_1_memout), .Resin(mips_alu_1_result), .Resout(ex_mem_1_resout), .R2in(id_ex_1_r2out),
    .R2out(ex_mem_1_r2out), .CLK(CLK), .\同步清零_气泡_高电平有效 (or_18_out), .\使能端_低电平有效_stall_高电平有效 (halt),
    .PCin(EX_PC), .PCout(MEM_PC), .\异步清零 (RST), .Halt(id_ex_1_halt_2), .Halt_2(ex_mem_1_halt_2),
    .R1in({id_ex_1_r1out_2, id_ex_1_r1out}), .R1out(ex_mem_1_r1out), .Intin(id_ex_1_intout),
    .Intout(ex_mem_1_intout));
  Multiplexer #(.select(3), .width(32), .enable("false")) multiplexer_15 (
    .in0(adder_2_out), .in1({adder_2_out[31:28], id_ex_1_jofout, 2'b00}),
    .in2({id_ex_1_r1out_2, id_ex_1_r1out}), .in3({32{1'b0}}), .in4(adder_3_out), .in5({32{1'b0}}),
    .in6({32{1'b0}}), .in7({32{1'b0}}), .out(PCinCom), .sel(or_16_out));
  or or_18 (or_18_out, eret, \中断请求 );
  or or_19 (Jump, or_16_out[2], or_16_out[0], or_16_out[1]);
  and and_20 (and_20_out, and_18_out, or_20_out);
  or or_20 (or_20_out, or_16_out[0], or_16_out[1]);
  and and_21 (and_21_out, and_18_out, or_16_out[2]);
  and and_22 (and_22_out, ~and_14_out, nohalt, and_19_out);  // AND_Gate
  Counter #(.width(16), .max('hffff)) counter_1 (
    .count(and_18_out), .Q(\总周期数 ), .clk(CLK), .clr(RST));  // open: load, D, carry
  Counter #(.width(16), .max('hffff)) counter_2 (
    .count(and_20_out), .Q(\无条件分支数 ), .clk(CLK), .clr(RST));  // open: load, D, carry
  Counter #(.width(16), .max('hffff)) counter_3 (
    .count(and_21_out), .Q(\条件分支成功数 ), .clk(CLK), .clr(RST));  // open: load, D, carry
  Counter #(.width(16), .max('hffff)) counter_4 (
    .count(and_22_out), .Q(\插入气泡数 ), .clk(CLK), .clr(RST));  // open: load, D, carry
  Multiplexer #(.width(4), .enable("false")) multiplexer_16 (
    .in0(4'b1111), .in1(multiplexer_17_out), .out(multiplexer_16_out), .sel(ex_mem_1_memout[2]));
  Multiplexer #(.width(4), .enable("false")) multiplexer_17 (
    .in0(4'b0011), .in1(4'b1100), .out(multiplexer_17_out), .sel(ex_mem_1_resout[1]));
  // MIPS_RAM mips_ram_1: pin names not known; wires that end beside it: ex_mem_1_resout[21:2], mips_ram_1_p2, ex_mem_1_memout[1], multiplexer_16_out, CLK, ex_mem_1_memout[0], RST, mips_ram_1_p8
  Multiplexer #(.width(32), .enable("false")) multiplexer_18 (
    .in0(ex_mem_1_r2out), .in1(shifter_3_out), .out(mips_ram_1_p2), .sel(and_23_out));
  and and_23 (and_23_out, ex_mem_1_memout[2], ex_mem_1_resout[1]);
  Shifter #(.width(32)) shifter_3 (.in(ex_mem_1_r2out), .\dist (5'b10000), .out(shifter_3_out));
  MEM_WB mem_wb_1 (
    .WBin(ex_mem_1_wbout), .WBout(mem_wb_1_wbout), .memin(mips_ram_1_p8), .memout(mem_wb_1_memout),
    .Resin(ex_mem_1_resout), .Resout(mem_wb_1_resout), .CLK(CLK), .\同步清零_气泡_高电平有效 (or_21_out),
    .\使能端_低电平有效_stall_高电平有效 (halt), .PCin(MEM_PC), .PCout(WB_PC), .\异步清零 (RST), .Halt(ex_mem_1_halt_2),
    .Halt_2(syscall), .R1in(ex_mem_1_r1out), .R1out(R1), .R2in(ex_mem_1_r2out), .R2out(R2),
    .Intin(ex_mem_1_intout), .Intout({rd, eret, MTC0, MFC0}));
  or or_21 (or_21_out, eret, \中断请求 );
  Multiplexer #(.width(32), .enable("false")) multiplexer_19 (
    .in0(mem_wb_1_resout), .in1(mem_wb_1_memout), .out(multiplexer_19_out), .sel(mem_wb_1_wbout[0]));
  Adder #(.width(32)) adder_4 (.a(WB_PC), .b(32'h4), .out(adder_4_out));  // open: cin, cout
  Multiplexer #(.width(32), .enable("false")) multiplexer_20 (
    .in0(multiplexer_19_out), .in1(adder_4_out), .out(multiplexer_20_out), .sel(mem_wb_1_wbout[2]));
  or or_22 (registerfile_1_p3, MFC0, mem_wb_1_wbout[1]);
  Multiplexer #(.width(32), .enable("false")) multiplexer_21 (
    .in0(multiplexer_20_out), .in1(copro), .out(registerfile_1_p1), .sel(MFC0));
  Adder #(.width(16)) adder_5 (.a(\总周期数 ), .b(16'h1), .out(adder_5_out));  // open: cin, cout
  assign and_24_out = IF_PC & 32'h7ff;  // AND_Gate and_24, 32 bits wide
  assign and_25_out = ID_PC & 32'h7ff;  // AND_Gate and_25, 32 bits wide
  assign and_26_out = EX_PC & 32'h7ff;  // AND_Gate and_26, 32 bits wide
  assign and_27_out = MEM_PC & 32'h7ff;  // AND_Gate and_27, 32 bits wide
  assign and_28_out = WB_PC & 32'h7ff;  // AND_Gate and_28, 32 bits wide
  // Probe on adder_5_out
  // Probe on and_24_out
  // Probe on and_25_out
  // Probe on and_26_out
  // Probe on and_27_out
  // Probe on and_28_out

  // Notes on the sheet:
  //   中断源
  //   中断等待指示
  //   指令存储器
  //   数码管输出
  //   contents of rom_1 (hex, n*v repeats v):
  //   20110001 8000c05 20110001 20120002 20130003 8000c09 20110001 20120002 20130003 8000c0d 20110001
  //   20120002 20130003 8000c11 20110001 20120002 20130003 c000cf8 20100001 20110001 118fc0 112020
  //   20020022 c 118882 12200001 8000c15 112020 20020022 c 20110001 118880 112020 20020022 c 12200001
  //   8000c1f 20110001 118fc0 112020 20020022 c 1188c3 112020 20020022 c 118903 112020 20020022 c 118903
  //   112020 20020022 c 118903 112020 20020022 c 118903 112020 20020022 c 118903 112020 20020022 c 118903
  //   112020 20020022 c 118903 112020 20020022 c 20100001 109fc0 139fc3 8021 2012000c 24160003 26100001
  //   3210000f 20080008 20090001 139900 2709825 132020 20020022 c 1094022 1500fff9 22100001 2018000f
  //   2188024 108700 20080008 20090001 139902 2709825 132021 20020022 c 1094022 1500fff9 108702 2c9b022
  //   12c00001 8000c50 4020 1084027 84400 3508ffff 82021 20020022 c 2010ffff 20110000 ae300000 22100001
  //   22310004 ae300000 22100001 22310004 ae300000 22100001 22310004 ae300000 22100001 22310004 ae300000
  //   22100001 22310004 ae300000 22100001 22310004 ae300000 22100001 22310004 ae300000 22100001 22310004
  //   ae300000 22100001 22310004 ae300000 22100001 22310004 ae300000 22100001 22310004 ae300000 22100001
  //   22310004 ae300000 22100001 22310004 ae300000 22100001 22310004 ae300000 22100001 22310004 ae300000
  //   22100001 22310004 22100001 8020 2011003c 8e130000 8e340000 274402a 11000002 ae330000 ae140000
  //   2231fffc 1611fff8 102020 20020022 c 22100004 2011003c 1611fff2 20020032 c 20080001 20090003 20110876
  //   118d00 112020 20020022 c 200b0008 1118806 1318806 112020 20020022 c 216bffff 1560fff9 2002000a c
  //   2008ffff 20117777 112020 20020022 c 200b0010 2288826 112020 20020022 c 216bffff 1560fffa 2002000a c
  //   20090000 200b0020 20110001 20120001 a5310000 112020 20020022 c 2328820 21290002 216bffff 1560fff8
  //   200b0010 20090000 8d310000 112020 20020022 c 21290004 216bffff 1560fff9 2002000a c 2011000f 112020
  //   20020022 c 2231ffff 1e20fffb 2002000a c 2002000a c 20100000 22100001 102020 20020022 c 22100002
  //   102020 20020022 c 22100003 102020 20020022 c 22100004 102020 20020022 c 22100005 102020 20020022 c
  //   22100006 102020 20020022 c 22100007 102020 20020022 c 22100008 102020 20020022 20020022 c 3e00008
  //   Beq
  //   Bne
  //   rs
  //   rt
  //   rd
  //   MemToReg
  //   MemWrite
  //   AluOP
  //   AluSrcB
  //   RegWrite
  //   流水调试日志用
  //   Filling bubble pipeline needs 4 cycles
endmodule

module \重定向流水线  (
);

  wire and_1_out, and_2_out, and_3_out, and_4_out, and_5_out, and_6_out, and_8_out, and_9_out, and_10_out,
       and_11_out, and_12_out, and_13_out, and_14_out, and_18_out, and_19_out, and_20_out, and_21_out,
       and_22_out, bgtz, CLK, comparator_1_eq, comparator_2_eq, comparator_3_gt, comparator_4_gt,
       comparator_5_eq, comparator_6_eq, comparator_7_gt, comparator_8_eq, d_ff_1_q, d_ff_2_q, d_ff_3_q,
       d_ff_4_q, d_ff_5_q, d_ff_6_q, demultiplexer_1_out1, demultiplexer_1_out2, demultiplexer_1_out3, Equ,
       eret, ereti, ex_mem_1_halt_2, ext, Go, halt, id_ex_redirect_1_halt_2, IE, IR1, IR2, IR3, j, JAL, jr,
       Jump, loaduse, MFC0, MTC0, MTC0id, nohalt, not_1_out, or_1_out, or_5_out, or_6_out, or_7_out,
       or_8_out, or_9_out, or_10_out, or_11_out, or_12_out, or_13_out, or_14_out, or_18_out, or_19_out,
       or_20_out, priority_encoder_1_gs, regDst, registerfile_1_p3, RST, sh, srlv, syscall, W1, W2, W3,
       \中断请求 , \同步清零1 , \同步清零2 , \同步清零3 , \硬布线控制器_1_syscall ;
  wire [0:0] \硬布线控制器_1_mfc0 ;
  wire [1:0] IR, multiplexer_12_out, \中断编号 , \硬布线控制器_1_regwrite ;
  wire [1:1] \硬布线控制器_1_memwrite ;
  wire [2:0] ex_mem_1_memout, id_ex_redirect_1_memout, id_ex_redirect_1_wbout, or_15_out;
  wire [3:0] adder_2_out_2, id_ex_redirect_1_exout, id_ex_redirect_1_sel_out, multiplexer_18_out,
       multiplexer_19_out, \数据相关检测_重定向_1_r1_sel , \硬布线控制器_1_alu_op ;
  wire [4:0] id_ex_redirect_1_immout_2, id_ex_redirect_1_wbout_2, multiplexer_7_out, multiplexer_11_out,
       R1id, R2id, rd, rdID, rW;
  wire [4:3] \硬布线控制器_1_beq ;
  wire [4:4] \硬布线控制器_1_alu_src ;
  wire [5:0] func, id_ex_redirect_1_ifout, op;
  wire [5:4] id_ex_redirect_1_exout_2;
  wire [7:0] ex_mem_1_intout, ex_mem_1_wbout, id_ex_redirect_1_intout, mem_wb_1_wbout;
  wire [15:0] \LoadUse次数 , \总周期数 , \无条件分支数 , \条件分支成功数 ;
  wire [25:6] if_id_1_insout;
  wire [27:0] adder_2_out;
  wire [27:2] id_ex_redirect_1_jofout;
  wire [31:0] adder_3_out, adder_4_out, copro, EPC, ex_mem_1_r1out, ex_mem_1_r2out, ex_mem_1_resout, EX_PC,
       id_ex_redirect_1_immout, id_ex_redirect_1_r1out, id_ex_redirect_1_r2out, ID_PC, IF_PC, IntVec,
       LedData, MEM_PC, mem_wb_1_memout, mem_wb_1_resout, mips_alu_1_result, mips_ram_1_p2, mips_ram_1_p8,
       multiplexer_1_out, multiplexer_2_out, multiplexer_4_out, multiplexer_9_out, multiplexer_14_out,
       multiplexer_16_out, multiplexer_21_out, multiplexer_22_out, PC_4, PCin, PCinCom, R1, R1ex, R2,
       registerfile_1_p1, registerfile_1_p7, registerfile_1_p8, rom_1_data, shifter_1_out, shifter_2_out,
       shifter_3_out, WB_PC;

  Button \u_总复位  (.out(RST));
  Button _1 (.out(IR1));
  Button _2 (.out(IR2));
  Button _3 (.out(IR3));
  Button \u_继续运行  (.out(Go));
  LED led_1 (.in(W1));
  LED led_2 (.in(W2));
  LED led_3 (.in(W3));
  Register #(.width(32)) PC (.D(PCin), .en(and_1_out), .Q(IF_PC), .clk(CLK), .clr(RST));
  and and_1 (and_1_out, nohalt, or_1_out);
  or or_1 (or_1_out, ~loaduse, \中断请求 , eret);  // OR_Gate
  Multiplexer #(.width(32), .enable("false")) multiplexer_1 (
    .in0(PC_4), .in1(PCinCom), .out(multiplexer_1_out), .sel(Jump));
  or or_2 (W1, d_ff_4_q, d_ff_1_q);
  or or_3 (W2, d_ff_5_q, d_ff_2_q);
  or or_4 (W3, d_ff_6_q, d_ff_3_q);
  Comparator #(.width(5), .mode("unsigned")) comparator_1 (.a(rd), .b(5'b01100), .eq(comparator_1_eq));  // open: gt, lt
  Hex_Digit_Display hex_digit_display_1 (.value(LedData[31:28]));  // open: dp
  D_Flip_Flop d_ff_1 (.clk(IR1), .D(1'b1), .Q(d_ff_1_q), .reset(d_ff_4_q));  // open: Qn, preset, en
  D_Flip_Flop d_ff_2 (.clk(IR2), .D(1'b1), .Q(d_ff_2_q), .reset(d_ff_5_q));  // open: Qn, preset, en
  D_Flip_Flop d_ff_3 (.clk(IR3), .D(1'b1), .Q(d_ff_3_q), .reset(d_ff_6_q));  // open: Qn, preset, en
  or or_5 (or_5_out, d_ff_3_q, d_ff_6_q);
  and and_2 (and_2_out, MTC0, comparator_1_eq);
  Hex_Digit_Display hex_digit_display_2 (.value(LedData[27:24]));  // open: dp
  Hex_Digit_Display hex_digit_display_3 (.value(LedData[23:20]));  // open: dp
  // Probe on IF_PC
  // Probe on ID_PC
  // Probe on EX_PC
  // Probe on MEM_PC
  // Probe on WB_PC
  Adder #(.width(32)) adder_1 (.a(IF_PC), .b(32'h4), .out(PC_4));  // open: cin, cout
  Multiplexer #(.width(32), .enable("false")) multiplexer_2 (
    .in0(multiplexer_1_out), .in1(IntVec), .out(multiplexer_2_out), .sel(\中断请求 ));
  or or_6 (or_6_out, d_ff_1_q, d_ff_4_q);
  and and_3 (and_3_out, or_6_out, ~\同步清零1 );  // AND_Gate
  or or_7 (or_7_out, d_ff_2_q, d_ff_5_q);
  and and_4 (and_4_out, or_7_out, ~\同步清零2 );  // AND_Gate
  and and_5 (and_5_out, or_5_out, ~\同步清零3 );  // AND_Gate
  or or_8 (or_8_out, \中断请求 , eret, and_2_out);
  Hex_Digit_Display hex_digit_display_4 (.value(LedData[15:12]));  // open: dp
  Hex_Digit_Display hex_digit_display_5 (.value(LedData[19:16]));  // open: dp
  ROM #(.addrWidth(10), .dataWidth(32)) rom_1 (.addr(IF_PC[11:2]), .data(rom_1_data), .sel(1'b1));
  Multiplexer #(.width(32), .enable("false")) multiplexer_3 (
    .in0(multiplexer_2_out), .in1(EPC), .out(PCin), .sel(eret));
  D_Flip_Flop d_ff_4 (.clk(CLK), .D(and_3_out), .Q(d_ff_4_q));  // open: Qn, preset, en, reset
  D_Flip_Flop d_ff_5 (.clk(CLK), .D(and_4_out), .Q(d_ff_5_q));  // open: Qn, preset, en, reset
  D_Flip_Flop d_ff_6 (.clk(CLK), .D(and_5_out), .Q(d_ff_6_q));  // open: Qn, preset, en, reset
  D_Flip_Flop d_ff_7 (.clk(CLK), .D(IE), .Qn(IE), .en(or_8_out), .reset(RST));  // open: Q, preset
  Comparator #(.width(5), .mode("unsigned")) comparator_2 (.a(rd), .b(5'b01110), .eq(comparator_2_eq));  // open: gt, lt
  Hex_Digit_Display hex_digit_display_6 (.value(LedData[11:8]));  // open: dp
  Hex_Digit_Display hex_digit_display_7 (.value(LedData[7:4]));  // open: dp
  Clock clock_1 (.out(CLK));
  IF_ID if_id_1 (
    .Insin(rom_1_data), .PCin(IF_PC), .CLK(CLK),
    .Insout({op, if_id_1_insout[25:16], rdID, if_id_1_insout[10:6], func}), .PCout(ID_PC),
    .\同步清零_气泡_高电平有效 (or_10_out), .\使能端_低电平有效_stall_高电平有效 (or_9_out), .\异步清零 (RST));  // open: PJIn, PJOut
  or or_9 (or_9_out, loaduse, halt);
  or or_10 (or_10_out, Jump, \中断请求 , eret);
  and and_6 (and_6_out, MTC0, comparator_2_eq);
  Hex_Digit_Display hex_digit_display_8 (.value(LedData[3:0]));  // open: dp
  Priority_Encoder #(.select(2)) priority_encoder_1 (
    .in0(1'b1), .in1(d_ff_4_q), .in2(d_ff_5_q), .in3(d_ff_6_q), .out(\中断编号 ), .gs(priority_encoder_1_gs),
    .en_in(1'b1));  // open: en_out
  Comparator #(.width(2), .mode("unsigned")) comparator_3 (.a(\中断编号 ), .b(IR), .gt(comparator_3_gt));  // open: eq, lt
  Comparator #(.width(32), .mode("unsigned")) comparator_4 (
    .a(MEM_PC), .b(32'hf), .gt(comparator_4_gt));  // open: eq, lt
  Multiplexer #(.width(32), .enable("false")) multiplexer_4 (
    .in0(MEM_PC), .in1(R2), .out(multiplexer_4_out), .sel(and_6_out));
  or or_11 (or_11_out, \中断请求 , and_6_out);
  \硬布线控制器  \u_硬布线控制器_1  (
    .Func(func), .OP(op), .ALU_OP(\硬布线控制器_1_alu_op ), .MemToReg(\硬布线控制器_1_regwrite [0]),
    .MemWrite(\硬布线控制器_1_memwrite [1]), .ALU_SRC(\硬布线控制器_1_alu_src [4]), .RegWrite(\硬布线控制器_1_regwrite [1]),
    .SysCALL(\硬布线控制器_1_syscall ), .SignedExt(ext), .RegDst(regDst), .JR(jr), .JMP(j),
    .Beq(\硬布线控制器_1_beq [3]), .JAL(JAL), .Bne(\硬布线控制器_1_beq [4]), .SH(sh), .BGTZ(bgtz), .SRLV(srlv),
    .ERET(ereti), .RS(if_id_1_insout[25:21]), .MFC0(\硬布线控制器_1_mfc0 [0]), .MTC0(MTC0id));
  and and_7 (\中断请求 , priority_encoder_1_gs, IE, comparator_3_gt, comparator_4_gt);
  Register #(.width(32)) u_EPC (.D(multiplexer_4_out), .en(or_11_out), .Q(EPC), .clk(CLK), .clr(RST));
  // Probe on \总周期数 
  // Probe on \无条件分支数 
  // Probe on \条件分支成功数 
  // Probe on {16{1'b0}}
  // Probe on \LoadUse次数 
  Shifter #(.width(32), .shift("ar")) shifter_1 (
    .in({rdID, if_id_1_insout[10:6], func, {16{1'b0}}}), .\dist (5'b10000), .out(shifter_1_out));
  Multiplexer #(.width(5), .enable("false")) multiplexer_5 (
    .in0(if_id_1_insout[25:21]), .in1(5'b00010), .out(R1id), .sel(\硬布线控制器_1_syscall ));
  Multiplexer #(.width(5), .enable("false")) multiplexer_6 (
    .in0(if_id_1_insout[20:16]), .in1(5'b00100), .out(R2id), .sel(\硬布线控制器_1_syscall ));
  Multiplexer #(.width(5), .enable("false")) multiplexer_7 (
    .in0(if_id_1_insout[20:16]), .in1(rdID), .out(multiplexer_7_out), .sel(regDst));
  Multiplexer #(.width(5), .enable("false")) multiplexer_8 (
    .in0(multiplexer_7_out), .in1({5{1'b1}}), .out(rW), .sel(JAL));
  Comparator #(.width(32)) comparator_5 (.a(R1), .b(32'h22), .eq(comparator_5_eq));  // open: gt, lt
  // Probe on IF_PC[11:0]
  Multiplexer #(.width(32), .enable("false")) multiplexer_9 (
    .in0({{16{1'b0}}, rdID, if_id_1_insout[10:6], func}), .in1(shifter_1_out), .out(multiplexer_9_out),
    .sel(ext));
  // RegisterFile registerfile_1: pin names not known; wires that end beside it: registerfile_1_p1, CLK, registerfile_1_p3, mem_wb_1_wbout[7:3], R1id, R2id, registerfile_1_p7, registerfile_1_p8
  // Probe on ID_PC[11:0]
  and and_8 (and_8_out, comparator_5_eq, syscall);
  and and_9 (and_9_out, ~comparator_5_eq, syscall);  // AND_Gate
  or or_12 (or_12_out, Go, RST);
  // Probe on MEM_PC[11:0]
  // Probe on EX_PC[11:0]
  Adder #(.width(32)) adder_2 (.a(EX_PC), .b(32'h4), .out({adder_2_out_2, adder_2_out}));  // open: cin, cout
  or or_13 (or_13_out, Jump, loaduse, \中断请求 , eret);
  Register #(.width(32)) register_1 (.D(R2), .en(and_8_out), .Q(LedData), .clk(and_8_out), .clr(RST));
  D_Flip_Flop d_ff_8 (.clk(CLK), .D(and_9_out), .Q(halt), .Qn(nohalt), .preset(1'b0), .en(nohalt), .reset(or_12_out));
  Multiplexer #(.select(2), .width(32), .enable("false")) multiplexer_10 (
    .in0(32'h3310), .in1(32'h10), .in2(32'h3110), .in3(32'h3210), .out(IntVec), .sel(\中断编号 ));
  Comparator #(.width(5), .mode("unsigned")) comparator_6 (.a(rd), .b(5'b01000), .eq(comparator_6_eq));  // open: gt, lt
  // Probe on WB_PC[11:0]
  \数据相关检测_重定向  \u_数据相关检测_重定向_1  (
    .OP(op), .EX_WriteReg_num(id_ex_redirect_1_wbout_2), .EX_RegWrite(id_ex_redirect_1_wbout[1]),
    .MEM_WriteReg_num(ex_mem_1_wbout[7:3]), .MEM_RegWrite(ex_mem_1_wbout[1]), .Func(func), .ID_R1_num(R1id),
    .ID_R2_num(R2id), .EX_MemToReg(id_ex_redirect_1_memout[0]), .R1_sel(\数据相关检测_重定向_1_r1_sel [1:0]),
    .R2_sel(\数据相关检测_重定向_1_r1_sel [3:2]), .loadUse(loaduse));
  ID_EX_redirect id_ex_redirect_1 (
    .Sel_in(\数据相关检测_重定向_1_r1_sel ), .WBin({rW, JAL, \硬布线控制器_1_regwrite }),
    .Memin({sh, \硬布线控制器_1_memwrite [1], \硬布线控制器_1_regwrite [0]}),
    .Exin({srlv, \硬布线控制器_1_alu_src [4], \硬布线控制器_1_alu_op }), .IFin({JAL, \硬布线控制器_1_beq , bgtz, jr, j}),
    .Jofin({if_id_1_insout[25:16], rdID, if_id_1_insout[10:6], func}), .Immin(multiplexer_9_out),
    .R1in(registerfile_1_p7), .R2in(registerfile_1_p8), .PCin(ID_PC), .Halt(\硬布线控制器_1_syscall ), .CLK(CLK),
    .Sel_out(id_ex_redirect_1_sel_out), .WBout({id_ex_redirect_1_wbout_2, id_ex_redirect_1_wbout}),
    .Memout(id_ex_redirect_1_memout), .Exout({id_ex_redirect_1_exout_2, id_ex_redirect_1_exout}),
    .IFout({id_ex_redirect_1_ifout[5:2], or_15_out[1], id_ex_redirect_1_ifout[0]}),
    .Jofout(id_ex_redirect_1_jofout),
    .Immout({id_ex_redirect_1_immout[31:11], id_ex_redirect_1_immout_2, id_ex_redirect_1_immout[5:0]}),
    .R1out(id_ex_redirect_1_r1out), .R2out(id_ex_redirect_1_r2out), .PCout(EX_PC),
    .Halt_2(id_ex_redirect_1_halt_2), .\同步清零_气泡_高电平有效 (or_13_out), .\异步清零 (RST),
    .\使能端_低电平有效_stall_高电平有效 (halt), .Intin({rdID, ereti, MTC0id, \硬布线控制器_1_mfc0 [0]}),
    .Intout(id_ex_redirect_1_intout));  // open: PJin, PJOut
  and and_10 (and_10_out, MFC0, comparator_6_eq);
  and and_11 (and_11_out, MTC0, comparator_6_eq);
  Demultiplexer #(.select(2), .enable("false")) demultiplexer_1 (
    .out1(demultiplexer_1_out1), .out2(demultiplexer_1_out2), .out3(demultiplexer_1_out3), .in(1'b1), .sel(IR));  // open: out0
  Multiplexer #(.width(5), .enable("false")) multiplexer_11 (
    .in0(id_ex_redirect_1_immout_2), .in1(R1ex[4:0]), .out(multiplexer_11_out),
    .sel(id_ex_redirect_1_exout_2[5]));
  Shifter #(.width(32)) shifter_2 (
    .in({id_ex_redirect_1_immout[31:11], id_ex_redirect_1_immout_2, id_ex_redirect_1_immout[5:0]}),
    .\dist (5'b00010), .out(shifter_2_out));
  and and_12 (and_12_out, id_ex_redirect_1_ifout[3], Equ);
  and and_13 (and_13_out, id_ex_redirect_1_ifout[4], ~Equ);  // AND_Gate
  and and_14 (and_14_out, id_ex_redirect_1_ifout[2], comparator_7_gt);
  Comparator #(.width(32)) comparator_7 (.a(R1ex), .b({32{1'b0}}), .gt(comparator_7_gt));  // open: eq, lt
  Comparator #(.width(5), .mode("unsigned")) comparator_8 (.a(rd), .b(5'b01110), .eq(comparator_8_eq));  // open: gt, lt
  Multiplexer #(.width(2), .enable("false")) multiplexer_12 (
    .in0(\中断编号 ), .in1(R2[1:0]), .out(multiplexer_12_out), .sel(and_11_out));
  or or_14 (or_14_out, and_10_out, and_11_out);
  and and_15 (\同步清零1 , and_11_out, demultiplexer_1_out1);
  and and_16 (\同步清零2 , demultiplexer_1_out2, and_11_out);
  and and_17 (\同步清零3 , demultiplexer_1_out3, and_11_out);
  LED led_4 (.in(\中断请求 ));
  // Probe on \中断编号 
  // Probe on IR
  LED led_5 (.in(IE));
  Multiplexer #(.select(2), .width(32), .enable("false")) multiplexer_13 (
    .in0(id_ex_redirect_1_r1out), .in1(registerfile_1_p1), .in3(ex_mem_1_resout), .out(R1ex),
    .sel(id_ex_redirect_1_sel_out[1:0]));  // open: in2
  Multiplexer #(.select(2), .width(32), .enable("false")) multiplexer_14 (
    .in0(id_ex_redirect_1_r2out), .in1(registerfile_1_p1), .in3(ex_mem_1_resout), .out(multiplexer_14_out),
    .sel(id_ex_redirect_1_sel_out[3:2]));  // open: in2
  Adder #(.width(32)) adder_3 (
    .a({adder_2_out_2, adder_2_out}), .b(shifter_2_out), .out(adder_3_out));  // open: cin, cout
  or or_15 (or_15_out[0], id_ex_redirect_1_ifout[0], id_ex_redirect_1_ifout[5]);
  or or_16 (or_15_out[2], and_12_out, and_13_out, and_14_out);
  not not_1 (not_1_out, Jump);
  and and_18 (and_18_out, not_1_out, loaduse);
  Multiplexer #(.width(32), .enable("false")) multiplexer_15 (
    .in0({{30{1'b0}}, IR}), .in1(EPC), .out(copro), .sel(comparator_8_eq));
  Register #(.width(2)) u_IR (.D(multiplexer_12_out), .en(or_14_out), .Q(IR), .clk(CLK), .clr(RST));
  Multiplexer #(.width(32), .enable("false")) multiplexer_16 (
    .in0(multiplexer_14_out),
    .in1({id_ex_redirect_1_immout[31:11], id_ex_redirect_1_immout_2, id_ex_redirect_1_immout[5:0]}),
    .out(multiplexer_16_out), .sel(id_ex_redirect_1_exout_2[4]));
  Multiplexer #(.select(3), .width(32), .enable("false")) multiplexer_17 (
    .in0({adder_2_out_2, adder_2_out}), .in1({adder_2_out_2, id_ex_redirect_1_jofout, 2'b00}), .in2(R1ex),
    .in3({32{1'b0}}), .in4(adder_3_out), .in5({32{1'b0}}), .in6({32{1'b0}}), .in7({32{1'b0}}), .out(PCinCom),
    .sel(or_15_out));
  or or_17 (Jump, or_15_out[2], or_15_out[0], or_15_out[1]);
  and and_19 (and_19_out, nohalt, or_18_out);
  or or_18 (or_18_out, or_15_out[0], or_15_out[1]);
  and and_20 (and_20_out, nohalt, or_15_out[2]);
  and and_21 (and_21_out, ~halt, and_18_out);  // AND_Gate
  EX_MEM ex_mem_1 (
    .WBin({id_ex_redirect_1_wbout_2, id_ex_redirect_1_wbout}), .WBout(ex_mem_1_wbout),
    .Memin(id_ex_redirect_1_memout), .Memout(ex_mem_1_memout), .Resin(mips_alu_1_result),
    .Resout(ex_mem_1_resout), .R2in(multiplexer_14_out), .R2out(ex_mem_1_r2out), .CLK(CLK),
    .\同步清零_气泡_高电平有效 (or_19_out), .\使能端_低电平有效_stall_高电平有效 (halt), .PCin(EX_PC), .PCout(MEM_PC), .\异步清零 (RST),
    .Halt(id_ex_redirect_1_halt_2), .Halt_2(ex_mem_1_halt_2), .R1in(R1ex), .R1out(ex_mem_1_r1out),
    .Intin(id_ex_redirect_1_intout), .Intout(ex_mem_1_intout));
  MIPS_ALU mips_alu_1 (
    .X(R1ex), .Y(multiplexer_16_out), .AluOP(id_ex_redirect_1_exout), .Equal(Equ),
    .Result(mips_alu_1_result), .shamt(multiplexer_11_out));  // open: Result_2
  or or_19 (or_19_out, \中断请求 , eret);
  Counter #(.width(16), .max('hffff)) counter_1 (
    .count(nohalt), .Q(\总周期数 ), .clk(CLK), .clr(RST));  // open: load, D, carry
  Counter #(.width(16), .max('hffff)) counter_2 (
    .count(and_19_out), .Q(\无条件分支数 ), .clk(CLK), .clr(RST));  // open: load, D, carry
  Counter #(.width(16), .max('hffff)) counter_3 (
    .count(and_20_out), .Q(\条件分支成功数 ), .clk(CLK), .clr(RST));  // open: load, D, carry
  Counter #(.width(16), .max('hffff)) counter_4 (
    .count(and_21_out), .Q(\LoadUse次数 ), .clk(CLK), .clr(RST));  // open: load, D, carry
  and and_22 (and_22_out, ex_mem_1_memout[2], ex_mem_1_resout[1]);
  Multiplexer #(.width(4), .enable("false")) multiplexer_18 (
    .in0(4'b1111), .in1(multiplexer_19_out), .out(multiplexer_18_out), .sel(ex_mem_1_memout[2]));
  Multiplexer #(.width(4), .enable("false")) multiplexer_19 (
    .in0(4'b0011), .in1(4'b1100), .out(multiplexer_19_out), .sel(ex_mem_1_resout[1]));
  // MIPS_RAM mips_ram_1: pin names not known; wires that end beside it: ex_mem_1_resout[21:2], mips_ram_1_p2, ex_mem_1_memout[1], multiplexer_18_out, CLK, ex_mem_1_memout[0], RST, mips_ram_1_p8
  Multiplexer #(.width(32), .enable("false")) multiplexer_20 (
    .in0(ex_mem_1_r2out), .in1(shifter_3_out), .out(mips_ram_1_p2), .sel(and_22_out));
  or or_20 (or_20_out, \中断请求 , eret);
  Shifter #(.width(32)) shifter_3 (.in(ex_mem_1_r2out), .\dist (5'b10000), .out(shifter_3_out));
  MEM_WB mem_wb_1 (
    .WBin(ex_mem_1_wbout), .WBout(mem_wb_1_wbout), .memin(mips_ram_1_p8), .memout(mem_wb_1_memout),
    .Resin(ex_mem_1_resout), .Resout(mem_wb_1_resout), .CLK(CLK), .\同步清零_气泡_高电平有效 (or_20_out),
    .\使能端_低电平有效_stall_高电平有效 (halt), .PCin(MEM_PC), .PCout(WB_PC), .\异步清零 (RST), .Halt(ex_mem_1_halt_2),
    .Halt_2(syscall), .R1in(ex_mem_1_r1out), .R1out(R1), .R2in(ex_mem_1_r2out), .R2out(R2),
    .Intin(ex_mem_1_intout), .Intout({rd, eret, MTC0, MFC0}));
  Multiplexer #(.width(32), .enable("false")) multiplexer_21 (
    .in0(mem_wb_1_resout), .in1(mem_wb_1_memout), .out(multiplexer_21_out), .sel(mem_wb_1_wbout[0]));
  Adder #(.width(32)) adder_4 (.a(WB_PC), .b(32'h4), .out(adder_4_out));  // open: cin, cout
  Multiplexer #(.width(32), .enable("false")) multiplexer_22 (
    .in0(multiplexer_21_out), .in1(adder_4_out), .out(multiplexer_22_out), .sel(mem_wb_1_wbout[2]));
  Multiplexer #(.width(32), .enable("false")) multiplexer_23 (
    .in0(multiplexer_22_out), .in1(copro), .out(registerfile_1_p1), .sel(MFC0));
  or or_21 (registerfile_1_p3, MFC0, mem_wb_1_wbout[1]);

  // Notes on the sheet:
  //   中断源
  //   中断等待指示
  //   指令存储器
  //   数码管输出
  //   contents of rom_1 (hex, n*v repeats v):
  //   20110001 8000c05 20110001 20120002 20130003 8000c09 20110001 20120002 20130003 8000c0d 20110001
  //   20120002 20130003 8000c11 20110001 20120002 20130003 c000cf8 20100001 20110001 118fc0 112020
  //   20020022 c 118882 12200001 8000c15 112020 20020022 c 20110001 118880 112020 20020022 c 12200001
  //   8000c1f 20110001 118fc0 112020 20020022 c 1188c3 112020 20020022 c 118903 112020 20020022 c 118903
  //   112020 20020022 c 118903 112020 20020022 c 118903 112020 20020022 c 118903 112020 20020022 c 118903
  //   112020 20020022 c 118903 112020 20020022 c 20100001 109fc0 139fc3 8021 2012000c 24160003 26100001
  //   3210000f 20080008 20090001 139900 2709825 132020 20020022 c 1094022 1500fff9 22100001 2018000f
  //   2188024 108700 20080008 20090001 139902 2709825 132021 20020022 c 1094022 1500fff9 108702 2c9b022
  //   12c00001 8000c50 4020 1084027 84400 3508ffff 82021 20020022 c 2010ffff 20110000 ae300000 22100001
  //   22310004 ae300000 22100001 22310004 ae300000 22100001 22310004 ae300000 22100001 22310004 ae300000
  //   22100001 22310004 ae300000 22100001 22310004 ae300000 22100001 22310004 ae300000 22100001 22310004
  //   ae300000 22100001 22310004 ae300000 22100001 22310004 ae300000 22100001 22310004 ae300000 22100001
  //   22310004 ae300000 22100001 22310004 ae300000 22100001 22310004 ae300000 22100001 22310004 ae300000
  //   22100001 22310004 22100001 8020 2011003c 8e130000 8e340000 274402a 11000002 ae330000 ae140000
  //   2231fffc 1611fff8 102020 20020022 c 22100004 2011003c 1611fff2 20020032 c 20080001 20090003 20110876
  //   118d00 112020 20020022 c 200b0008 1118806 1318806 112020 20020022 c 216bffff 1560fff9 2002000a c
  //   2008ffff 20117777 112020 20020022 c 200b0010 2288826 112020 20020022 c 216bffff 1560fffa 2002000a c
  //   20090000 200b0020 20110001 20120001 a5310000 112020 20020022 c 2328820 21290002 216bffff 1560fff8
  //   200b0010 20090000 8d310000 112020 20020022 c 21290004 216bffff 1560fff9 2002000a c 2011000f 112020
  //   20020022 c 2231ffff 1e20fffb 2002000a c 2002000a c 20100000 22100001 102020 20020022 c 22100002
  //   102020 20020022 c 22100003 102020 20020022 c 22100004 102020 20020022 c 22100005 102020 20020022 c
  //   22100006 102020 20020022 c 22100007 102020 20020022 c 22100008 102020 20020022 20020022 c 3e00008
  //   rs
  //   rt
  //   rd
  //   Beq
  //   Bne
  //   MemToReg
  //   MemWrite
  //   AluOP
  //   AluSrcB
  //   RegWrite
  //   流水调试日志用
  //   Filling redirected pipeline needs 4 cycles
endmodule

module \双位预测状态机  (
  input  CLK,
  input  branch,
  input  RST,
  output PJump
);

  wire and_1_out, and_2_out, and_3_out, and_4_out, and_5_out, not_1_out, or_1_out, or_2_out, S0_q, S0_qn,
       S1_qn;

  D_Flip_Flop S1 (.clk(CLK), .D(or_1_out), .Q(PJump), .Qn(S1_qn), .preset(1'b0), .en(1'b1), .reset(RST));
  not not_1 (not_1_out, branch);
  D_Flip_Flop S0 (.clk(CLK), .D(or_2_out), .Q(S0_q), .Qn(S0_qn), .preset(1'b0), .en(1'b1), .reset(RST));
  and and_1 (and_1_out, PJump, not_1_out, S0_qn);
  and and_2 (and_2_out, branch, S0_q);
  and and_3 (and_3_out, PJump, branch, S0_qn);
  and and_4 (and_4_out, PJump, not_1_out, S0_qn);
  and and_5 (and_5_out, S1_qn, branch, S0_qn);
  or or_1 (or_1_out, and_1_out, and_2_out, and_3_out);
  or or_2 (or_2_out, and_4_out, and_5_out);
endmodule

// FSM
module \双位预测次态产生器  (
  input  [1:0] Sn,
  input  Branch,
  output [1:0] Sn_1
);

  wire and_1_out, and_2_out, and_3_out, and_4_out, and_5_out, not_1_out, not_2_out, not_3_out;

  not not_1 (not_1_out, Sn[1]);
  not not_2 (not_2_out, Branch);
  not not_3 (not_3_out, Sn[0]);
  and and_1 (and_1_out, Sn[1], not_2_out, not_3_out);
  and and_2 (and_2_out, Branch, Sn[0]);
  and and_3 (and_3_out, Sn[1], Branch, not_3_out);
  and and_4 (and_4_out, Sn[1], not_2_out, not_3_out);
  and and_5 (and_5_out, not_1_out, Branch, not_3_out);
  or or_1 (Sn_1[1], and_1_out, and_2_out, and_3_out);
  or or_2 (Sn_1[0], and_4_out, and_5_out);

  // Other names for the same wires on the sheet: S0 = Sn[0]; PJump = Sn[1]; S1 = Sn[1]; S0n_1 = Sn_1[0];
  //   S1n_1 = Sn_1[1]
endmodule

// Max3
module Max3 (
  input  [15:0] Y,
  input  [15:0] X,
  input  [2:0] Y_num,
  input  [2:0] X_num,
  output [15:0] MAX,
  output [2:0] Max_num
);

  wire comparator_1_eq, comparator_1_gt, or_1_out;

  Multiplexer #(.width(16), .enable("false")) multiplexer_1 (.in0(Y), .in1(X), .out(MAX), .sel(or_1_out));
  Comparator #(.width(16), .mode("unsigned")) comparator_1 (
    .a(X), .b(Y), .gt(comparator_1_gt), .eq(comparator_1_eq));  // open: lt
  or or_1 (or_1_out, comparator_1_gt, comparator_1_eq);
  Multiplexer #(.width(3), .enable("false")) multiplexer_2 (.in0(Y_num), .in1(X_num), .out(Max_num), .sel(or_1_out));

  // Notes on the sheet:
  //   输出两个输入中的较大值，并输出较大值的3位编号
endmodule

// BHT
module BHT (
  input  CLK,
  input  [31:0] PC_target,
  input  [31:0] Tag,
  input  WE,
  input  [31:0] TagW,
  input  [1:0] Init_state,
  input  Branch,
  output Jump,
  output [31:0] PC_target_out
);

  wire and_1_out, and_2_out, and_3_out, and_4_out, and_5_out, and_6_out, and_7_out, and_8_out, and_9_out,
       and_10_out, and_11_out, and_12_out, and_13_out, and_14_out, and_15_out, and_16_out, and_17_out,
       and_18_out, comparator_1_eq, comparator_2_eq, comparator_3_eq, comparator_4_eq, comparator_5_eq,
       comparator_6_eq, comparator_7_eq, comparator_8_eq, comparator_9_eq, comparator_10_eq,
       comparator_11_eq, comparator_12_eq, comparator_13_eq, comparator_14_eq, comparator_15_eq,
       comparator_16_eq, Hit, HitW, L0, L1, L2, L3, L4, L5, L6, L7, Miss, MissW, or_1_out, or_2_out,
       or_3_out, or_4_out, or_5_out, or_6_out, or_7_out, or_8_out, or_9_out, or_10_out, or_11_out, or_12_out,
       or_13_out, or_14_out, or_15_out, or_16_out, R0, R1, R2, R3, R4, R5, R6, R7, V0, V1, V2, V3, V4, V5,
       V6, V7, WL0, WL1, WL2, WL3, WL4, WL5, WL6, WL7;
  wire [1:0] NeSt, Pst, PstR, \双位预测次态产生器_1_sn_1 , \状态位_2_q , \状态位_3_q , \状态位_4_q , \状态位_5_q , \状态位_6_q ,
       \状态位_7_q , \状态位_8_q , \状态位_q ;
  wire [2:0] max3_1_max_num, max3_2_max_num, max3_3_max_num, max3_4_max_num, max3_5_max_num, max3_6_max_num,
       max3_7_max_num;
  wire [15:0] C0, C1, C2, C3, C4, C5, C6, C7, max3_1_max, max3_2_max, max3_3_max, max3_4_max, max3_5_max,
       max3_6_max;
  wire [31:0] Tag0, Tag1, Tag2, Tag3, Tag4, Tag5, Tag6, Tag7, \分支目标地址_2_q , \分支目标地址_3_q , \分支目标地址_4_q ,
       \分支目标地址_5_q , \分支目标地址_6_q , \分支目标地址_7_q , \分支目标地址_8_q , \分支目标地址_q ;

  and and_1 (and_1_out, Hit, L0);
  and and_2 (and_2_out, Hit, L1);
  and and_3 (and_3_out, Hit, L2);
  and and_4 (and_4_out, Hit, L3);
  and and_5 (and_5_out, Hit, L4);
  and and_6 (and_6_out, Hit, L5);
  and and_7 (and_7_out, Hit, L6);
  and and_8 (and_8_out, Hit, L7);
  and and_9 (and_9_out, WL0, HitW);
  and and_10 (and_10_out, WL1, HitW);
  and and_11 (and_11_out, WL2, HitW);
  and and_12 (and_12_out, WL3, HitW);
  and and_13 (and_13_out, WL4, HitW);
  and and_14 (and_14_out, WL5, HitW);
  and and_15 (and_15_out, WL6, HitW);
  and and_16 (and_16_out, WL7, HitW);
  Max3 max3_1 (.Y(C1), .X(C0), .Y_num(3'b001), .X_num(3'b000), .MAX(max3_1_max), .Max_num(max3_1_max_num));
  Max3 max3_2 (.Y(C3), .X(C2), .Y_num(3'b011), .X_num(3'b010), .MAX(max3_2_max), .Max_num(max3_2_max_num));
  Max3 max3_3 (.Y(C5), .X(C4), .Y_num(3'b101), .X_num(3'b100), .MAX(max3_3_max), .Max_num(max3_3_max_num));
  Max3 max3_4 (.Y(C7), .X(C6), .Y_num(3'b111), .X_num(3'b110), .MAX(max3_4_max), .Max_num(max3_4_max_num));
  Register #(.width(1), .trigger("falling")) \u_有效位  (.D(1'b1), .en(R0), .Q(V0), .clk(CLK), .clr(1'b0));
  Register #(.width(1), .trigger("falling")) \u_有效位_2  (.D(1'b1), .en(R1), .Q(V1), .clk(CLK), .clr(1'b0));
  Register #(.width(1), .trigger("falling")) \u_有效位_3  (.D(1'b1), .en(R2), .Q(V2), .clk(CLK), .clr(1'b0));
  Register #(.width(1), .trigger("falling")) \u_有效位_4  (.D(1'b1), .en(R3), .Q(V3), .clk(CLK), .clr(1'b0));
  Register #(.width(1), .trigger("falling")) \u_有效位_5  (.D(1'b1), .en(R4), .Q(V4), .clk(CLK), .clr(1'b0));
  Register #(.width(1), .trigger("falling")) \u_有效位_6  (.D(1'b1), .en(R5), .Q(V5), .clk(CLK), .clr(1'b0));
  Register #(.width(1), .trigger("falling")) \u_有效位_7  (.D(1'b1), .en(R6), .Q(V6), .clk(CLK), .clr(1'b0));
  Register #(.width(1), .trigger("falling")) \u_有效位_8  (.D(1'b1), .en(R7), .Q(V7), .clk(CLK), .clr(1'b0));
  Max3 max3_5 (
    .Y(max3_2_max), .X(max3_1_max), .Y_num(max3_2_max_num), .X_num(max3_1_max_num), .MAX(max3_5_max),
    .Max_num(max3_5_max_num));
  Max3 max3_6 (
    .Y(max3_4_max), .X(max3_3_max), .Y_num(max3_4_max_num), .X_num(max3_3_max_num), .MAX(max3_6_max),
    .Max_num(max3_6_max_num));
  Register #(.width(32), .trigger("falling")) \u_标记位  (.D(TagW), .en(R0), .Q(Tag0), .clk(CLK), .clr(1'b0));
  Register #(.width(32), .trigger("falling")) \u_标记位_2  (.D(TagW), .en(R1), .Q(Tag1), .clk(CLK), .clr(1'b0));
  Register #(.width(32), .trigger("falling")) \u_标记位_3  (.D(TagW), .en(R2), .Q(Tag2), .clk(CLK), .clr(1'b0));
  Register #(.width(32), .trigger("falling")) \u_标记位_4  (.D(TagW), .en(R3), .Q(Tag3), .clk(CLK), .clr(1'b0));
  Register #(.width(32), .trigger("falling")) \u_标记位_5  (.D(TagW), .en(R4), .Q(Tag4), .clk(CLK), .clr(1'b0));
  Register #(.width(32), .trigger("falling")) \u_标记位_6  (.D(TagW), .en(R5), .Q(Tag5), .clk(CLK), .clr(1'b0));
  Register #(.width(32), .trigger("falling")) \u_标记位_7  (.D(TagW), .en(R6), .Q(Tag6), .clk(CLK), .clr(1'b0));
  Register #(.width(32), .trigger("falling")) \u_标记位_8  (.D(TagW), .en(R7), .Q(Tag7), .clk(CLK), .clr(1'b0));
  Max3 max3_7 (
    .Y(max3_6_max), .X(max3_5_max), .Y_num(max3_6_max_num), .X_num(max3_5_max_num), .Max_num(max3_7_max_num));  // open: MAX
  Demultiplexer #(.select(3), .enable("false")) demultiplexer_1 (
    .out0(R0), .out1(R1), .out2(R2), .out3(R3), .out4(R4), .out5(R5), .out6(R6), .out7(R7), .in(and_17_out),
    .sel(max3_7_max_num));
  and and_17 (and_17_out, WE, MissW);
  Register #(.width(2), .trigger("falling")) \u_状态位  (.D(NeSt), .en(or_1_out), .Q(\状态位_q ), .clk(CLK), .clr(1'b0));
  assign Pst = and_9_out ? \状态位_q  : 2'bz;  // Controlled_Buffer controlled_buffer_1
  or or_1 (or_1_out, and_9_out, R0);
  assign Pst = and_10_out ? \状态位_2_q  : 2'bz;  // Controlled_Buffer controlled_buffer_2
  Register #(.width(2), .trigger("falling")) \u_状态位_2  (.D(NeSt), .en(or_2_out), .Q(\状态位_2_q ), .clk(CLK), .clr(1'b0));
  or or_2 (or_2_out, and_10_out, R1);
  Register #(.width(2), .trigger("falling")) \u_状态位_3  (.D(NeSt), .en(or_3_out), .Q(\状态位_3_q ), .clk(CLK), .clr(1'b0));
  assign Pst = and_11_out ? \状态位_3_q  : 2'bz;  // Controlled_Buffer controlled_buffer_3
  or or_3 (or_3_out, and_11_out, R2);
  Register #(.width(2), .trigger("falling")) \u_状态位_4  (.D(NeSt), .en(or_4_out), .Q(\状态位_4_q ), .clk(CLK), .clr(1'b0));
  assign Pst = and_12_out ? \状态位_4_q  : 2'bz;  // Controlled_Buffer controlled_buffer_4
  or or_4 (or_4_out, and_12_out, R3);
  assign Pst = and_13_out ? \状态位_5_q  : 2'bz;  // Controlled_Buffer controlled_buffer_5
  Register #(.width(2), .trigger("falling")) \u_状态位_5  (.D(NeSt), .en(or_5_out), .Q(\状态位_5_q ), .clk(CLK), .clr(1'b0));
  or or_5 (or_5_out, and_13_out, R4);
  assign Pst = and_14_out ? \状态位_6_q  : 2'bz;  // Controlled_Buffer controlled_buffer_6
  Register #(.width(2), .trigger("falling")) \u_状态位_6  (.D(NeSt), .en(or_6_out), .Q(\状态位_6_q ), .clk(CLK), .clr(1'b0));
  or or_6 (or_6_out, and_14_out, R5);
  Register #(.width(2), .trigger("falling")) \u_状态位_7  (.D(NeSt), .en(or_7_out), .Q(\状态位_7_q ), .clk(CLK), .clr(1'b0));
  assign Pst = and_15_out ? \状态位_7_q  : 2'bz;  // Controlled_Buffer controlled_buffer_7
  or or_7 (or_7_out, and_15_out, R6);
  assign Pst = and_16_out ? \状态位_8_q  : 2'bz;  // Controlled_Buffer controlled_buffer_8
  Register #(.width(2), .trigger("falling")) \u_状态位_8  (.D(NeSt), .en(or_8_out), .Q(\状态位_8_q ), .clk(CLK), .clr(1'b0));
  or or_8 (or_8_out, and_16_out, R7);
  assign PstR = and_1_out ? \状态位_q  : 2'bz;  // Controlled_Buffer controlled_buffer_9
  assign PstR = and_2_out ? \状态位_2_q  : 2'bz;  // Controlled_Buffer controlled_buffer_10
  assign PstR = and_3_out ? \状态位_3_q  : 2'bz;  // Controlled_Buffer controlled_buffer_11
  assign PstR = and_4_out ? \状态位_4_q  : 2'bz;  // Controlled_Buffer controlled_buffer_12
  assign PstR = and_5_out ? \状态位_5_q  : 2'bz;  // Controlled_Buffer controlled_buffer_13
  assign PstR = and_6_out ? \状态位_6_q  : 2'bz;  // Controlled_Buffer controlled_buffer_14
  assign PstR = and_7_out ? \状态位_7_q  : 2'bz;  // Controlled_Buffer controlled_buffer_15
  assign PstR = and_8_out ? \状态位_8_q  : 2'bz;  // Controlled_Buffer controlled_buffer_16
  and and_18 (and_18_out, WE, MissW);
  \双位预测次态产生器  \u_双位预测次态产生器_1  (.Sn(Pst), .Branch(Branch), .Sn_1(\双位预测次态产生器_1_sn_1 ));
  Counter #(.width(16), .max('hffff), .ongoal("stay"), .trigger("falling")) \u_计数位  (
    .count(or_9_out), .Q(C0), .clk(CLK), .clr(and_9_out));  // open: load, D, carry
  or or_9 (or_9_out, WE, Hit);
  Counter #(.width(16), .max('hffff), .ongoal("stay"), .trigger("falling")) \u_计数位_2  (
    .count(or_10_out), .Q(C1), .clk(CLK), .clr(and_10_out));  // open: load, D, carry
  or or_10 (or_10_out, WE, Hit);
  Counter #(.width(16), .max('hffff), .ongoal("stay"), .trigger("falling")) \u_计数位_3  (
    .count(or_11_out), .Q(C2), .clk(CLK), .clr(and_11_out));  // open: load, D, carry
  or or_11 (or_11_out, WE, Hit);
  Counter #(.width(16), .max('hffff), .ongoal("stay"), .trigger("falling")) \u_计数位_4  (
    .count(or_12_out), .Q(C3), .clk(CLK), .clr(and_12_out));  // open: load, D, carry
  or or_12 (or_12_out, WE, Hit);
  Counter #(.width(16), .max('hffff), .ongoal("stay"), .trigger("falling")) \u_计数位_5  (
    .count(or_13_out), .Q(C4), .clk(CLK), .clr(and_13_out));  // open: load, D, carry
  or or_13 (or_13_out, WE, Hit);
  Counter #(.width(16), .max('hffff), .ongoal("stay"), .trigger("falling")) \u_计数位_6  (
    .count(or_14_out), .Q(C5), .clk(CLK), .clr(and_14_out));  // open: load, D, carry
  or or_14 (or_14_out, WE, Hit);
  Counter #(.width(16), .max('hffff), .ongoal("stay"), .trigger("falling")) \u_计数位_7  (
    .count(or_15_out), .Q(C6), .clk(CLK), .clr(and_15_out));  // open: load, D, carry
  or or_15 (or_15_out, WE, Hit);
  Counter #(.width(16), .max('hffff), .ongoal("stay"), .trigger("falling")) \u_计数位_8  (
    .count(or_16_out), .Q(C7), .clk(CLK), .clr(and_16_out));  // open: load, D, carry
  or or_16 (or_16_out, WE, Hit);
  Multiplexer #(.width(2), .enable("false")) multiplexer_1 (
    .in0(\双位预测次态产生器_1_sn_1 ), .in1(Init_state), .out(NeSt), .sel(and_18_out));
  Multiplexer #(.enable("false")) multiplexer_2 (.in0(PstR[1]), .in1(1'b0), .out(Jump), .sel(Miss));
  Register #(.width(32), .trigger("falling")) \u_分支目标地址  (
    .D(PC_target), .en(R0), .Q(\分支目标地址_q ), .clk(CLK), .clr(1'b0));
  assign PC_target_out = and_1_out ? \分支目标地址_q  : 32'bz;  // Controlled_Buffer controlled_buffer_17
  Register #(.width(32), .trigger("falling")) \u_分支目标地址_2  (
    .D(PC_target), .en(R1), .Q(\分支目标地址_2_q ), .clk(CLK), .clr(1'b0));
  assign PC_target_out = and_2_out ? \分支目标地址_2_q  : 32'bz;  // Controlled_Buffer controlled_buffer_18
  Register #(.width(32), .trigger("falling")) \u_分支目标地址_3  (
    .D(PC_target), .en(R2), .Q(\分支目标地址_3_q ), .clk(CLK), .clr(1'b0));
  assign PC_target_out = and_3_out ? \分支目标地址_3_q  : 32'bz;  // Controlled_Buffer controlled_buffer_19
  Register #(.width(32), .trigger("falling")) \u_分支目标地址_4  (
    .D(PC_target), .en(R3), .Q(\分支目标地址_4_q ), .clk(CLK), .clr(1'b0));
  assign PC_target_out = and_4_out ? \分支目标地址_4_q  : 32'bz;  // Controlled_Buffer controlled_buffer_20
  assign PC_target_out = and_5_out ? \分支目标地址_5_q  : 32'bz;  // Controlled_Buffer controlled_buffer_21
  Register #(.width(32), .trigger("falling")) \u_分支目标地址_5  (
    .D(PC_target), .en(R4), .Q(\分支目标地址_5_q ), .clk(CLK), .clr(1'b0));
  Register #(.width(32), .trigger("falling")) \u_分支目标地址_6  (
    .D(PC_target), .en(R5), .Q(\分支目标地址_6_q ), .clk(CLK), .clr(1'b0));
  assign PC_target_out = and_6_out ? \分支目标地址_6_q  : 32'bz;  // Controlled_Buffer controlled_buffer_22
  Register #(.width(32), .trigger("falling")) \u_分支目标地址_7  (
    .D(PC_target), .en(R6), .Q(\分支目标地址_7_q ), .clk(CLK), .clr(1'b0));
  assign PC_target_out = and_7_out ? \分支目标地址_7_q  : 32'bz;  // Controlled_Buffer controlled_buffer_23
  Register #(.width(32), .trigger("falling")) \u_分支目标地址_8  (
    .D(PC_target), .en(R7), .Q(\分支目标地址_8_q ), .clk(CLK), .clr(1'b0));
  assign PC_target_out = and_8_out ? \分支目标地址_8_q  : 32'bz;  // Controlled_Buffer controlled_buffer_24
  Comparator #(.width(32)) comparator_1 (.a(Tag), .b(Tag0), .eq(comparator_1_eq));  // open: gt, lt
  Comparator #(.width(32)) comparator_2 (.a(Tag), .b(Tag1), .eq(comparator_2_eq));  // open: gt, lt
  Comparator #(.width(32)) comparator_3 (.a(Tag), .b(Tag2), .eq(comparator_3_eq));  // open: gt, lt
  Comparator #(.width(32)) comparator_4 (.a(Tag), .b(Tag3), .eq(comparator_4_eq));  // open: gt, lt
  Comparator #(.width(32)) comparator_5 (.a(Tag), .b(Tag4), .eq(comparator_5_eq));  // open: gt, lt
  Comparator #(.width(32)) comparator_6 (.a(Tag), .b(Tag5), .eq(comparator_6_eq));  // open: gt, lt
  Comparator #(.width(32)) comparator_7 (.a(Tag), .b(Tag6), .eq(comparator_7_eq));  // open: gt, lt
  Comparator #(.width(32)) comparator_8 (.a(Tag), .b(Tag7), .eq(comparator_8_eq));  // open: gt, lt
  Comparator #(.width(32)) comparator_9 (.a(TagW), .b(Tag0), .eq(comparator_9_eq));  // open: gt, lt
  Comparator #(.width(32)) comparator_10 (.a(TagW), .b(Tag1), .eq(comparator_10_eq));  // open: gt, lt
  Comparator #(.width(32)) comparator_11 (.a(TagW), .b(Tag2), .eq(comparator_11_eq));  // open: gt, lt
  Comparator #(.width(32)) comparator_12 (.a(TagW), .b(Tag3), .eq(comparator_12_eq));  // open: gt, lt
  Comparator #(.width(32)) comparator_13 (.a(TagW), .b(Tag4), .eq(comparator_13_eq));  // open: gt, lt
  Comparator #(.width(32)) comparator_14 (.a(TagW), .b(Tag5), .eq(comparator_14_eq));  // open: gt, lt
  Comparator #(.width(32)) comparator_15 (.a(TagW), .b(Tag6), .eq(comparator_15_eq));  // open: gt, lt
  Comparator #(.width(32)) comparator_16 (.a(TagW), .b(Tag7), .eq(comparator_16_eq));  // open: gt, lt
  and and_19 (L0, V0, comparator_1_eq);
  and and_20 (L1, V1, comparator_2_eq);
  and and_21 (L2, V2, comparator_3_eq);
  and and_22 (L3, V3, comparator_4_eq);
  and and_23 (L4, V4, comparator_5_eq);
  and and_24 (L5, V5, comparator_6_eq);
  and and_25 (L6, V6, comparator_7_eq);
  and and_26 (L7, V7, comparator_8_eq);
  and and_27 (WL0, V0, comparator_9_eq);
  and and_28 (WL1, V1, comparator_10_eq);
  and and_29 (WL2, V2, comparator_11_eq);
  and and_30 (WL3, V3, comparator_12_eq);
  and and_31 (WL4, V4, comparator_13_eq);
  and and_32 (WL5, V5, comparator_14_eq);
  and and_33 (WL6, V6, comparator_15_eq);
  and and_34 (WL7, V7, comparator_16_eq);
  or or_17 (Hit, L0, L1, L2, L3, L4, L5, L6, L7);
  not not_1 (MissW, HitW);
  or or_18 (HitW, WL0, WL1, WL2, WL3, WL4, WL5, WL6, WL7);
  not not_2 (Miss, Hit);

  // Other names for the same wires on the sheet: ISt[1:0] = Init_state; PCin[31:0] = PC_target;
  //   PCout[31:0] = PC_target_out; Write = WE

  // Notes on the sheet:
  //   输入引脚区
  //   输出引脚区
endmodule
module \动态分支预测流水线  (
);

  wire and_1_out, and_2_out, and_3_out, and_4_out, and_5_out, and_6_out, and_7_out, and_8_out, and_9_out,
       and_10_out, and_11_out, and_12_out, CLK, comparator_1_eq, comparator_2_eq, comparator_3_gt, Equ,
       ex_mem_1_halt_2, fail, Go, halt, id_ex_redirect_1_halt_2, id_ex_redirect_1_pjout, if_id_1_pjout, IR1,
       IR2, IR3, JAL, Jump, loaduse, nohalt, not_1_out, not_2_out, or_3_out, or_4_out, or_5_out, or_8_out,
       Pjump, regDst, RST, syscall, W1, W2, W3, \硬布线控制器_1_signedext , \硬布线控制器_1_syscall ;
  wire [1:0] multiplexer_1_out;
  wire [1:1] \硬布线控制器_1_regwrite ;
  wire [2:0] ex_mem_1_memout, id_ex_redirect_1_memout, InJS, or_2_out, \硬布线控制器_1_memwrite ;
  wire [3:0] id_ex_redirect_1_sel_out, multiplexer_15_out, multiplexer_16_out, \数据相关检测_重定向_1_r1_sel ,
       \硬布线控制器_1_alu_op ;
  wire [4:0] multiplexer_6_out, multiplexer_10_out, R1id, R2id, rW, \硬布线控制器_1_jmp ;
  wire [5:0] func, id_ex_redirect_1_exout, JIns, op;
  wire [5:4] \硬布线控制器_1_alu_src ;
  wire [7:0] ex_mem_1_wbout, id_ex_redirect_1_wbout, mem_wb_1_wbout;
  wire [15:0] \LoadUse次数 , \总周期数 , \无条件分支数 , \条件分支成功数 , \预测失败次数 , \预测成功次数 ;
  wire [25:6] if_id_1_insout;
  wire [27:2] jtarget;
  wire [31:0] bht_1_pc_target_out, btarg, ex_mem_1_r1out, ex_mem_1_r2out, ex_mem_1_resout, EX_PC,
       id_ex_redirect_1_immout, id_ex_redirect_1_r1out, id_ex_redirect_1_r2out, ID_PC, IF_PC, LedData,
       MEM_PC, mem_wb_1_memout, mem_wb_1_resout, mips_alu_1_result, mips_ram_1_p8, multiplexer_2_out,
       multiplexer_3_out, multiplexer_4_out, multiplexer_7_out, multiplexer_12_out, multiplexer_13_out,
       multiplexer_14_out, multiplexer_17_out, multiplexer_18_out, PC_q, R1, R1ex, R2, registerfile_1_p2,
       registerfile_1_p8, registerfile_1_p9, rom_1_data, shifter_1_out, shifter_2_out, shifter_3_out, WB_PC;

  Button \u_总复位  (.out(RST));
  Button _1 (.out(IR1));
  Button _2 (.out(IR2));
  Button _3 (.out(IR3));
  Button \u_继续运行  (.out(Go));
  LED led_1 (.in(W1));
  LED led_2 (.in(W2));
  LED led_3 (.in(W3));
  and and_1 (and_1_out, nohalt, ~loaduse);  // AND_Gate
  Multiplexer #(.select(3), .width(2), .enable("false")) multiplexer_1 (
    .in0(2'b01), .in1(2'b10), .in2(2'b10), .in3(2'b01), .in4(2'b11), .in5(2'b01), .in6(2'b01), .in7(2'b01),
    .out(multiplexer_1_out), .sel(InJS));
  Comparator #(.width(6)) comparator_1 (
    .a({JIns[5:2], InJS[1], JIns[0]}), .b({6{1'b0}}), .eq(comparator_1_eq));  // open: gt, lt
  not not_1 (not_1_out, comparator_1_eq);
  or or_1 (or_2_out[2], JIns[2], JIns[3], JIns[4]);
  Hex_Digit_Display hex_digit_display_1 (.value(LedData[31:28]));  // open: dp
  Register #(.width(32)) PC (.D(multiplexer_4_out), .en(and_1_out), .Q(PC_q), .clk(CLK), .clr(RST));
  BHT bht_1 (
    .CLK(CLK), .WE(not_1_out), .Tag(IF_PC), .PC_target(multiplexer_2_out), .Init_state(multiplexer_1_out),
    .Branch(Jump), .PC_target_out(bht_1_pc_target_out), .Jump(Pjump), .TagW(EX_PC));
  Multiplexer #(.select(3), .width(32), .enable("false")) multiplexer_2 (
    .in0({32{1'b0}}), .in1({EX_PC[31:28], jtarget, 2'b00}), .in2(R1ex), .in3({32{1'b0}}), .in4(btarg),
    .in5({32{1'b0}}), .in6({32{1'b0}}), .in7({32{1'b0}}), .out(multiplexer_2_out),
    .sel({or_2_out[2], InJS[1], or_2_out[0]}));
  or or_2 (or_2_out[0], JIns[0], JIns[5]);
  Hex_Digit_Display hex_digit_display_2 (.value(LedData[27:24]));  // open: dp
  Hex_Digit_Display hex_digit_display_3 (.value(LedData[23:20]));  // open: dp
  Adder #(.width(32)) adder_1 (.a(PC_q), .b(32'h4), .out(IF_PC));  // open: cin, cout
  Hex_Digit_Display hex_digit_display_4 (.value(LedData[15:12]));  // open: dp
  Hex_Digit_Display hex_digit_display_5 (.value(LedData[19:16]));  // open: dp
  ROM #(.addrWidth(10), .dataWidth(32)) rom_1 (.addr(PC_q[11:2]), .data(rom_1_data), .sel(1'b1));
  Multiplexer #(.width(32), .enable("false")) multiplexer_3 (
    .in0(IF_PC), .in1(bht_1_pc_target_out), .out(multiplexer_3_out), .sel(Pjump));
  Multiplexer #(.width(32), .enable("false")) multiplexer_4 (
    .in0(multiplexer_3_out), .in1(multiplexer_14_out), .out(multiplexer_4_out), .sel(fail));
  Hex_Digit_Display hex_digit_display_6 (.value(LedData[11:8]));  // open: dp
  Hex_Digit_Display hex_digit_display_7 (.value(LedData[7:4]));  // open: dp
  Clock clock_1 (.out(CLK));
  IF_ID if_id_1 (
    .Insin(rom_1_data), .PCin(IF_PC), .CLK(CLK), .Insout({op, if_id_1_insout, func}), .PCout(ID_PC),
    .\同步清零_气泡_高电平有效 (fail), .\使能端_低电平有效_stall_高电平有效 (or_3_out), .\异步清零 (RST), .PJIn(Pjump),
    .PJOut(if_id_1_pjout));
  or or_3 (or_3_out, loaduse, halt);
  Hex_Digit_Display hex_digit_display_8 (.value(LedData[3:0]));  // open: dp
  \硬布线控制器  \u_硬布线控制器_1  (
    .Func(func), .OP(op), .ALU_OP(\硬布线控制器_1_alu_op ), .MemToReg(\硬布线控制器_1_memwrite [0]),
    .MemWrite(\硬布线控制器_1_memwrite [1]), .ALU_SRC(\硬布线控制器_1_alu_src [4]), .RegWrite(\硬布线控制器_1_regwrite [1]),
    .SysCALL(\硬布线控制器_1_syscall ), .SignedExt(\硬布线控制器_1_signedext ), .RegDst(regDst), .JR(\硬布线控制器_1_jmp [1]),
    .JMP(\硬布线控制器_1_jmp [0]), .Beq(\硬布线控制器_1_jmp [3]), .JAL(JAL), .Bne(\硬布线控制器_1_jmp [4]),
    .SH(\硬布线控制器_1_memwrite [2]), .BGTZ(\硬布线控制器_1_jmp [2]), .SRLV(\硬布线控制器_1_alu_src [5]));  // open: ERET, RS, MFC0, MTC0
  Comparator #(.width(32)) comparator_2 (.a(R1), .b(32'h22), .eq(comparator_2_eq));  // open: gt, lt
  Shifter #(.width(32), .shift("ar")) shifter_1 (
    .in({if_id_1_insout[15:6], func, {16{1'b0}}}), .\dist (5'b10000), .out(shifter_1_out));
  Multiplexer #(.width(5), .enable("false")) multiplexer_5 (
    .in0(if_id_1_insout[25:21]), .in1(5'b00010), .out(R1id), .sel(\硬布线控制器_1_syscall ));
  Multiplexer #(.width(5), .enable("false")) multiplexer_6 (
    .in0(if_id_1_insout[20:16]), .in1(if_id_1_insout[15:11]), .out(multiplexer_6_out), .sel(regDst));
  and and_2 (and_2_out, comparator_2_eq, syscall);
  and and_3 (and_3_out, ~comparator_2_eq, syscall);  // AND_Gate
  // Probe on \总周期数 
  // Probe on \无条件分支数 
  // Probe on \条件分支成功数 
  // Probe on {16{1'b0}}
  // Probe on \LoadUse次数 
  // Probe on \预测成功次数 
  Multiplexer #(.width(32), .enable("false")) multiplexer_7 (
    .in0({{16{1'b0}}, if_id_1_insout[15:6], func}), .in1(shifter_1_out), .out(multiplexer_7_out),
    .sel(\硬布线控制器_1_signedext ));
  // RegisterFile registerfile_1: pin names not known; wires that end beside it: {if_id_1_insout, func}, registerfile_1_p2, CLK, mem_wb_1_wbout[1], mem_wb_1_wbout[7:3], R1id, R2id, registerfile_1_p8, registerfile_1_p9
  Multiplexer #(.width(5), .enable("false")) multiplexer_8 (
    .in0(if_id_1_insout[20:16]), .in1(5'b00100), .out(R2id), .sel(\硬布线控制器_1_syscall ));
  Multiplexer #(.width(5), .enable("false")) multiplexer_9 (
    .in0(multiplexer_6_out), .in1({5{1'b1}}), .out(rW), .sel(JAL));
  or or_4 (or_4_out, Go, RST);
  // Probe on IF_PC[11:0]
  \数据相关检测_重定向  \u_数据相关检测_重定向_1  (
    .OP(op), .EX_WriteReg_num(id_ex_redirect_1_wbout[7:3]), .EX_RegWrite(id_ex_redirect_1_wbout[1]),
    .MEM_WriteReg_num(ex_mem_1_wbout[7:3]), .MEM_RegWrite(ex_mem_1_wbout[1]), .Func(func), .ID_R1_num(R1id),
    .ID_R2_num(R2id), .EX_MemToReg(id_ex_redirect_1_memout[0]), .R1_sel(\数据相关检测_重定向_1_r1_sel [1:0]),
    .R2_sel(\数据相关检测_重定向_1_r1_sel [3:2]), .loadUse(loaduse));
  ID_EX_redirect id_ex_redirect_1 (
    .Sel_in(\数据相关检测_重定向_1_r1_sel ), .WBin({rW, JAL, \硬布线控制器_1_regwrite [1], \硬布线控制器_1_memwrite [0]}),
    .Memin(\硬布线控制器_1_memwrite ), .Exin({\硬布线控制器_1_alu_src , \硬布线控制器_1_alu_op }),
    .IFin({JAL, \硬布线控制器_1_jmp }), .Jofin({if_id_1_insout, func}), .Immin(multiplexer_7_out),
    .R1in(registerfile_1_p8), .R2in(registerfile_1_p9), .PCin(ID_PC), .Halt(\硬布线控制器_1_syscall ), .CLK(CLK),
    .Sel_out(id_ex_redirect_1_sel_out), .WBout(id_ex_redirect_1_wbout), .Memout(id_ex_redirect_1_memout),
    .Exout(id_ex_redirect_1_exout), .IFout({JIns[5:2], InJS[1], JIns[0]}), .Jofout(jtarget),
    .Immout(id_ex_redirect_1_immout), .R1out(id_ex_redirect_1_r1out), .R2out(id_ex_redirect_1_r2out),
    .PCout(EX_PC), .Halt_2(id_ex_redirect_1_halt_2), .\同步清零_气泡_高电平有效 (or_5_out), .\异步清零 (RST),
    .\使能端_低电平有效_stall_高电平有效 (halt), .PJin(if_id_1_pjout), .PJOut(id_ex_redirect_1_pjout));  // open: Intin, Intout
  or or_5 (or_5_out, fail, loaduse);
  Register #(.width(32)) register_1 (.D(R2), .en(and_2_out), .Q(LedData), .clk(and_2_out), .clr(RST));
  D_Flip_Flop d_ff_1 (.clk(CLK), .D(and_3_out), .Q(halt), .Qn(nohalt), .preset(1'b0), .en(nohalt), .reset(or_4_out));
  // Probe on ID_PC[11:0]
  Comparator #(.width(32)) comparator_3 (.a(R1ex), .b({32{1'b0}}), .gt(comparator_3_gt));  // open: eq, lt
  // Probe on MEM_PC[11:0]
  // Probe on EX_PC[11:0]
  // Probe on \预测失败次数 
  Multiplexer #(.width(5), .enable("false")) multiplexer_10 (
    .in0(id_ex_redirect_1_immout[10:6]), .in1(R1ex[4:0]), .out(multiplexer_10_out),
    .sel(id_ex_redirect_1_exout[5]));
  Adder #(.width(32)) adder_2 (.a(EX_PC), .b(shifter_2_out), .out(btarg));  // open: cin, cout
  Shifter #(.width(32)) shifter_2 (.in(id_ex_redirect_1_immout), .\dist (5'b00010), .out(shifter_2_out));
  or or_6 (InJS[0], JIns[0], JIns[5]);
  and and_4 (and_4_out, JIns[3], Equ);
  and and_5 (and_5_out, JIns[4], ~Equ);  // AND_Gate
  and and_6 (and_6_out, JIns[2], comparator_3_gt);
  // Probe on WB_PC[11:0]
  Multiplexer #(.select(2), .width(32), .enable("false")) multiplexer_11 (
    .in0(id_ex_redirect_1_r1out), .in1(registerfile_1_p2), .in3(ex_mem_1_resout), .out(R1ex),
    .sel(id_ex_redirect_1_sel_out[1:0]));  // open: in2
  Multiplexer #(.select(2), .width(32), .enable("false")) multiplexer_12 (
    .in0(id_ex_redirect_1_r2out), .in1(registerfile_1_p2), .in3(ex_mem_1_resout), .out(multiplexer_12_out),
    .sel(id_ex_redirect_1_sel_out[3:2]));  // open: in2
  Multiplexer #(.width(32), .enable("false")) multiplexer_13 (
    .in0(multiplexer_12_out), .in1(id_ex_redirect_1_immout), .out(multiplexer_13_out),
    .sel(id_ex_redirect_1_exout[4]));
  or or_7 (InJS[2], and_4_out, and_5_out, and_6_out);
  or or_8 (or_8_out, InJS[0], InJS[1]);
  not not_2 (not_2_out, Jump);
  and and_7 (and_7_out, not_2_out, nohalt, loaduse);
  MIPS_ALU mips_alu_1 (
    .X(R1ex), .Y(multiplexer_13_out), .AluOP(id_ex_redirect_1_exout[3:0]), .Equal(Equ),
    .Result(mips_alu_1_result), .shamt(multiplexer_10_out));  // open: Result_2
  Multiplexer #(.select(3), .width(32), .enable("false")) multiplexer_14 (
    .in0(EX_PC), .in1({EX_PC[31:28], jtarget, 2'b00}), .in2(R1ex), .in3({32{1'b0}}), .in4(btarg),
    .in5({32{1'b0}}), .in6({32{1'b0}}), .in7({32{1'b0}}), .out(multiplexer_14_out), .sel(InJS));
  or or_9 (Jump, InJS[2], InJS[0], InJS[1]);
  and and_8 (and_8_out, nohalt, or_8_out);
  and and_9 (and_9_out, nohalt, InJS[2]);
  and and_10 (and_10_out, nohalt, ~fail, Jump);  // AND_Gate
  Counter #(.width(16), .max('hffff)) counter_1 (
    .count(and_11_out), .Q(\预测失败次数 ), .clk(CLK), .clr(RST));  // open: load, D, carry
  and and_11 (and_11_out, nohalt, fail, ~Jump);  // AND_Gate
  EX_MEM ex_mem_1 (
    .WBin(id_ex_redirect_1_wbout), .WBout(ex_mem_1_wbout), .Memin(id_ex_redirect_1_memout),
    .Memout(ex_mem_1_memout), .Resin(mips_alu_1_result), .Resout(ex_mem_1_resout), .R2in(multiplexer_12_out),
    .R2out(ex_mem_1_r2out), .CLK(CLK), .\使能端_低电平有效_stall_高电平有效 (halt), .PCin(EX_PC), .PCout(MEM_PC),
    .\异步清零 (RST), .Halt(id_ex_redirect_1_halt_2), .Halt_2(ex_mem_1_halt_2), .R1in(R1ex),
    .R1out(ex_mem_1_r1out));  // open: 同步清零_气泡_高电平有效, Intin, Intout
  xor xor_1 (fail, id_ex_redirect_1_pjout, Jump);
  Counter #(.width(16), .max('hffff)) counter_2 (
    .count(nohalt), .Q(\总周期数 ), .clk(CLK), .clr(RST));  // open: load, D, carry
  Counter #(.width(16), .max('hffff)) counter_3 (
    .count(and_8_out), .Q(\无条件分支数 ), .clk(CLK), .clr(RST));  // open: load, D, carry
  Counter #(.width(16), .max('hffff)) counter_4 (
    .count(and_9_out), .Q(\条件分支成功数 ), .clk(CLK), .clr(RST));  // open: load, D, carry
  Counter #(.width(16), .max('hffff)) counter_5 (
    .count(and_7_out), .Q(\LoadUse次数 ), .clk(CLK), .clr(RST));  // open: load, D, carry
  Counter #(.width(16), .max('hffff)) counter_6 (
    .count(and_10_out), .Q(\预测成功次数 ), .clk(CLK), .clr(RST));  // open: load, D, carry
  Multiplexer #(.width(4), .enable("false")) multiplexer_15 (
    .in0(4'b1111), .in1(multiplexer_16_out), .out(multiplexer_15_out), .sel(ex_mem_1_memout[2]));
  Multiplexer #(.width(4), .enable("false")) multiplexer_16 (
    .in0(4'b0011), .in1(4'b1100), .out(multiplexer_16_out), .sel(ex_mem_1_resout[1]));
  Multiplexer #(.width(32), .enable("false")) multiplexer_17 (
    .in0(ex_mem_1_r2out), .in1(shifter_3_out), .out(multiplexer_17_out), .sel(and_12_out));
  and and_12 (and_12_out, ex_mem_1_memout[2], ex_mem_1_resout[1]);
  Shifter #(.width(32)) shifter_3 (.in(ex_mem_1_r2out), .\dist (5'b10000), .out(shifter_3_out));
  MEM_WB mem_wb_1 (
    .WBin(ex_mem_1_wbout), .WBout(mem_wb_1_wbout), .memin(mips_ram_1_p8), .memout(mem_wb_1_memout),
    .Resin(ex_mem_1_resout), .Resout(mem_wb_1_resout), .CLK(CLK), .\使能端_低电平有效_stall_高电平有效 (halt),
    .PCin(MEM_PC), .PCout(WB_PC), .\异步清零 (RST), .Halt(ex_mem_1_halt_2), .Halt_2(syscall),
    .R1in(ex_mem_1_r1out), .R1out(R1), .R2in(ex_mem_1_r2out), .R2out(R2));  // open: 同步清零_气泡_高电平有效, Intin, Intout
  // MIPS_RAM mips_ram_1: pin names not known; wires that end beside it: ex_mem_1_resout[21:2], multiplexer_17_out, ex_mem_1_memout[1], multiplexer_15_out, CLK, ex_mem_1_memout[0], RST, mips_ram_1_p8
  Multiplexer #(.width(32), .enable("false")) multiplexer_18 (
    .in0(mem_wb_1_resout), .in1(mem_wb_1_memout), .out(multiplexer_18_out), .sel(mem_wb_1_wbout[0]));
  Multiplexer #(.width(32), .enable("false")) multiplexer_19 (
    .in0(multiplexer_18_out), .in1(WB_PC), .out(registerfile_1_p2), .sel(mem_wb_1_wbout[2]));

  // Other names for the same wires on the sheet: JIns[1] = InJS[1]; jtarget[31:28] = EX_PC[31:28]

  // Notes on the sheet:
  //   中断源
  //   中断等待指示
  //   指令存储器
  //   数码管输出
  //   contents of rom_1 (hex, n*v repeats v):
  //   20110005 8000c06 20110001 20120002 20130003 20140004 8000c0b 20110001 20120002 20130003 20140004
  //   8000c10 20110001 20120002 20130003 20140004 8000c15 20110001 20120002 20130003 20140004 8000c1a
  //   20110001 20120002 20130003 20140004 8000c1f 20110001 20120002 20130003 20140004 8000c24 20110001
  //   20120002 20130003 20140004 8000c29 20110001 20120002 20130003 20140004 2231ffff 1620ffe0 20100001
  //   201200ff 20110001 20130003 12120005 12100004 20110001 20120002 20130003 20140004 16310004 16320003
  //   20110001 20120002 20130003 c000c3d 2002000a c 20100000 22100001 102020 20020022 c 3e00008
  //   SignedExt
  //   Jmp
  //   Beq
  //   Jr
  //   Bne
  //   Sh
  //   Bgtz
  //   Srlv
  //   JAL
  //   rs
  //   rt
  //   rd
  //   MemToReg
  //   MemWrite
  //   AluOP
  //   AluSrcB
  //   RegWrite
  //   流水调试日志用
  //   Filling redirected pipeline needs 4 cycles
endmodule
